// Logisim project P0_L0_CRC.circ as structural Verilog: 2 circuits, main circuit CRC
module CRC (
  input  [7:0] A,
  input  [3:0] B,
  output [10:0] C
);

  wire [10:0] B_t, bit_extender_2_out, n4bit_mod2_1_out_5, n4bit_mod2_2_out_5, n4bit_mod2_3_out_5,
       n4bit_mod2_4_out_5, n4bit_mod2_5_out_5, n4bit_mod2_6_out_5, n4bit_mod2_7_out_5, n4bit_mod2_8_out_5,
       shifter_1_out;

  assign B_t = {{7{1'b0}}, B};  // Bit_Extender bit_extender_1
  assign bit_extender_2_out = {{3{1'b0}}, A};  // Bit_Extender bit_extender_2
  Shifter #(.width(11)) shifter_1 (.in(bit_extender_2_out), .\dist (4'b0011), .out(shifter_1_out));
  _4bit_mod2 u_4bit_mod2_1 (.in_1(shifter_1_out), .B(B_t), .shift(4'b0111), .out_5(n4bit_mod2_1_out_5), .sel(4'b1010));
  _4bit_mod2 u_4bit_mod2_2 (
    .in_1(n4bit_mod2_1_out_5), .B(B_t), .shift(4'b0110), .out_5(n4bit_mod2_2_out_5), .sel(4'b1001));
  _4bit_mod2 u_4bit_mod2_3 (
    .in_1(n4bit_mod2_2_out_5), .B(B_t), .shift(4'b0101), .out_5(n4bit_mod2_3_out_5), .sel(4'b1000));
  _4bit_mod2 u_4bit_mod2_4 (
    .in_1(n4bit_mod2_3_out_5), .B(B_t), .shift(4'b0100), .out_5(n4bit_mod2_4_out_5), .sel(4'b0111));
  _4bit_mod2 u_4bit_mod2_5 (
    .in_1(n4bit_mod2_4_out_5), .B(B_t), .shift(4'b0011), .out_5(n4bit_mod2_5_out_5), .sel(4'b0110));
  _4bit_mod2 u_4bit_mod2_6 (
    .in_1(n4bit_mod2_5_out_5), .B(B_t), .shift(4'b0010), .out_5(n4bit_mod2_6_out_5), .sel(4'b0101));
  _4bit_mod2 u_4bit_mod2_7 (
    .in_1(n4bit_mod2_6_out_5), .B(B_t), .shift(4'b0001), .out_5(n4bit_mod2_7_out_5), .sel(4'b0100));
  _4bit_mod2 u_4bit_mod2_8 (
    .in_1(n4bit_mod2_7_out_5), .B(B_t), .shift(4'b0000), .out_5(n4bit_mod2_8_out_5), .sel(4'b0011));
  assign C = shifter_1_out | n4bit_mod2_8_out_5;  // OR_Gate or_1, 11 bits wide
endmodule

module _4bit_mod2 (
  input  [10:0] in_1,
  input  [3:0] sel,
  input  [10:0] B,
  input  [3:0] shift,
  output [10:0] out_5
);

  wire bitselector_1_out;
  wire [10:0] B_sft, xor_1_out;

  assign xor_1_out = in_1 ^ B_sft;  // XOR_Gate xor_1, 11 bits wide
  BitSelector #(.width(11)) bitselector_1 (.in(in_1), .out(bitselector_1_out), .sel(sel));
  Shifter #(.width(11)) shifter_1 (.in(B), .\dist (shift), .out(B_sft));
  // Probe on B_sft
  Multiplexer #(.width(11)) multiplexer_1 (
    .in0(in_1), .in1(xor_1_out), .out(out_5), .sel(bitselector_1_out));  // open: en
endmodule
