// Logisim project P0_L0_FSM.circ as structural Verilog: 3 circuits, main circuit fsm
module fsm (
  input  CLR,
  input  [1:0] In,
  output Z
);

  wire clock_1_out;
  wire [1:0] multiplexer_1_out, register_1_q, state_module_1_newstate;

  state_module state_module_1 (.statement(register_1_q), .\input (In), .newState(state_module_1_newstate));
  Multiplexer #(.width(2)) multiplexer_1 (
    .in0(state_module_1_newstate), .in1(2'b00), .out(multiplexer_1_out), .sel(CLR));  // open: en
  Clock clock_1 (.out(clock_1_out));
  Register #(.width(2)) register_1 (.D(multiplexer_1_out), .Q(register_1_q), .clk(clock_1_out));  // open: en, clr
  output_module output_module_1 (.statement(register_1_q), .\input (In), .out_3(Z));
endmodule

// state
module state_module (
  input  [1:0] statement,
  input  [1:0] \input ,
  output [1:0] newState
);

  wire and_1_out, and_2_out, and_3_out, and_4_out, and_5_out, and_6_out, and_7_out, not_1_out, not_2_out,
       not_3_out, not_4_out, not_5_out, not_6_out, not_7_out;

  not not_1 (not_1_out, statement[1]);
  and and_1 (and_1_out, not_1_out, statement[0]);
  not not_2 (not_2_out, \input [0]);
  and and_2 (and_2_out, statement[1], not_3_out);
  not not_3 (not_3_out, statement[0]);
  not not_4 (not_4_out, \input [0]);
  not not_5 (not_5_out, \input [1]);
  and and_3 (and_3_out, statement[1], not_6_out);
  not not_6 (not_6_out, statement[0]);
  not not_7 (not_7_out, \input [0]);
  and and_4 (and_4_out, and_1_out, not_2_out);
  and and_5 (and_5_out, and_2_out, not_4_out);
  and and_6 (and_6_out, not_5_out, \input [0]);
  and and_7 (and_7_out, and_3_out, not_7_out);
  or or_1 (newState[1], and_4_out, and_5_out);
  or or_2 (newState[0], and_6_out, and_7_out);
endmodule

// output
module output_module (
  input  [1:0] statement,
  input  [1:0] \input ,
  output out_3
);

  wire and_1_out, and_2_out, and_3_out, and_4_out, and_5_out, and_6_out, and_7_out, not_1_out, not_2_out,
       not_3_out, not_4_out, not_5_out, not_6_out, not_7_out;
  wire [1:0] or_2_out;

  not not_1 (not_1_out, statement[1]);
  and and_1 (and_1_out, not_1_out, statement[0]);
  not not_2 (not_2_out, \input [0]);
  and and_2 (and_2_out, statement[1], not_3_out);
  not not_3 (not_3_out, statement[0]);
  not not_4 (not_4_out, \input [0]);
  not not_5 (not_5_out, \input [1]);
  and and_3 (and_3_out, statement[1], not_6_out);
  not not_6 (not_6_out, statement[0]);
  not not_7 (not_7_out, \input [0]);
  and and_4 (and_4_out, and_1_out, not_2_out);
  and and_5 (and_5_out, and_2_out, not_4_out);
  and and_6 (and_6_out, not_5_out, \input [0]);
  and and_7 (and_7_out, and_3_out, not_7_out);
  or or_1 (or_2_out[1], and_4_out, and_5_out);
  or or_2 (or_2_out[0], and_6_out, and_7_out);
  Comparator #(.width(2), .mode("unsigned")) comparator_1 (.a(2'b11), .b(or_2_out), .eq(out_3));  // open: gt, lt
endmodule
