// Logisim project P0_L0_GRF_experiece.circ as structural Verilog: 2 circuits, main circuit grf
module grf (
  input  clk,
  input  reset,
  input  WE,
  input  [31:0] WD,
  input  [4:0] A1,
  input  [4:0] A2,
  input  [4:0] A3,
  output [31:0] RD1,
  output [31:0] RD2
);

  wire [31:0] R0, R1, R2, R3, R4, R5, R6, R7, R8, R9, R10, R11, R12, R13, R14, R15, R16, R17, R18, R19, R20,
       R21, R22, R23, R24, R25, R26, R27, R28, R29, R30, R31, W0, W1, W2, W3, W4, W5, W6, W7, W8, W9, W10,
       W11, W12, W13, W14, W15, W16, W17, W18, W19, W20, W21, W22, W23, W24, W25, W26, W27, W28, W29, W30,
       W31;

  Register #(.width(32)) _0 (.D(W0), .en(WE), .Q(R0), .clk(clk), .clr(1'b1));
  Register #(.width(32)) _4 (.D(W4), .en(WE), .Q(R4), .clk(clk), .clr(reset));
  Register #(.width(32)) _8 (.D(W8), .en(WE), .Q(R8), .clk(clk), .clr(reset));
  Register #(.width(32)) _12 (.D(W12), .en(WE), .Q(R12), .clk(clk), .clr(reset));
  Demultiplexer #(.select(5), .width(32), .tristate("true")) demultiplexer_1 (
    .out1(W1), .out2(W2), .out3(W3), .out4(W4), .out5(W5), .out6(W6), .out7(W7), .out8(W8), .out9(W9),
    .out10(W10), .out11(W11), .out12(W12), .out13(W13), .out14(W14), .out15(W15), .out16(W16), .out17(W17),
    .out18(W18), .out19(W19), .out20(W20), .out21(W21), .out22(W22), .out23(W23), .out24(W24), .out25(W25),
    .out26(W26), .out27(W27), .out28(W28), .out29(W29), .out30(W30), .out31(W31), .in(WD), .sel(A3), .en(WE));  // open: out0
  Register #(.width(32)) _1 (.D(W1), .en(WE), .Q(R1), .clk(clk), .clr(reset));
  Register #(.width(32)) _5 (.D(W5), .en(WE), .Q(R5), .clk(clk), .clr(reset));
  Register #(.width(32)) _9 (.D(W9), .en(WE), .Q(R9), .clk(clk), .clr(reset));
  Register #(.width(32)) _13 (.D(W13), .en(WE), .Q(R13), .clk(clk), .clr(reset));
  Register #(.width(32)) _2 (.D(W2), .en(WE), .Q(R2), .clk(clk), .clr(reset));
  Register #(.width(32)) _6 (.D(W6), .en(WE), .Q(R6), .clk(clk), .clr(reset));
  Register #(.width(32)) _10 (.D(W10), .en(WE), .Q(R10), .clk(clk), .clr(reset));
  Register #(.width(32)) _14 (.D(W14), .en(WE), .Q(R14), .clk(clk), .clr(reset));
  Register #(.width(32)) _3 (.D(W3), .en(WE), .Q(R3), .clk(clk), .clr(reset));
  Register #(.width(32)) _7 (.D(W7), .en(WE), .Q(R7), .clk(clk), .clr(reset));
  Register #(.width(32)) _11 (.D(W11), .en(WE), .Q(R11), .clk(clk), .clr(reset));
  Register #(.width(32)) _15 (.D(W15), .en(WE), .Q(R15), .clk(clk), .clr(reset));
  Register #(.width(32)) _16 (.D(W16), .en(WE), .Q(R16), .clk(clk), .clr(reset));
  Register #(.width(32)) _20 (.D(W20), .en(WE), .Q(R20), .clk(clk), .clr(reset));
  Register #(.width(32)) _24 (.D(W24), .en(WE), .Q(R24), .clk(clk), .clr(reset));
  Register #(.width(32)) _28 (.D(W28), .en(WE), .Q(R28), .clk(clk), .clr(reset));
  Register #(.width(32)) _17 (.D(W17), .en(WE), .Q(R17), .clk(clk), .clr(reset));
  Register #(.width(32)) _21 (.D(W21), .en(WE), .Q(R21), .clk(clk), .clr(reset));
  Register #(.width(32)) _25 (.D(W25), .en(WE), .Q(R25), .clk(clk), .clr(reset));
  Register #(.width(32)) _29 (.D(W29), .en(WE), .Q(R29), .clk(clk), .clr(reset));
  Multiplexer #(.select(5), .width(32)) multiplexer_1 (
    .in0(R0), .in1(R1), .in2(R2), .in3(R3), .in4(R4), .in5(R5), .in6(R6), .in7(R7), .in8(R8), .in9(R9),
    .in10(R10), .in11(R11), .in12(R12), .in13(R13), .in14(R14), .in15(R15), .in16(R16), .in17(R17),
    .in18(R18), .in19(R19), .in20(R20), .in21(R21), .in22(R22), .in23(R23), .in24(R24), .in25(R25),
    .in26(R26), .in27(R27), .in28(R28), .in29(R29), .in30(R30), .in31(R31), .out(RD1), .sel(A1));  // open: en
  Register #(.width(32)) _18 (.D(W18), .en(WE), .Q(R18), .clk(clk), .clr(reset));
  Register #(.width(32)) _22 (.D(W22), .en(WE), .Q(R22), .clk(clk), .clr(reset));
  Register #(.width(32)) _26 (.D(W26), .en(WE), .Q(R26), .clk(clk), .clr(reset));
  Register #(.width(32)) _30 (.D(W30), .en(WE), .Q(R30), .clk(clk), .clr(reset));
  Register #(.width(32)) _19 (.D(W19), .en(WE), .Q(R19), .clk(clk), .clr(reset));
  Register #(.width(32)) _23 (.D(W23), .en(WE), .Q(R23), .clk(clk), .clr(reset));
  Register #(.width(32)) _27 (.D(W27), .en(WE), .Q(R27), .clk(clk), .clr(reset));
  Register #(.width(32)) _31 (.D(W31), .en(WE), .Q(R31), .clk(clk), .clr(reset));
  Multiplexer #(.select(5), .width(32)) multiplexer_2 (
    .in0(R0), .in1(R1), .in2(R2), .in3(R3), .in4(R4), .in5(R5), .in6(R6), .in7(R7), .in8(R8), .in9(R9),
    .in10(R10), .in11(R11), .in12(R12), .in13(R13), .in14(R14), .in15(R15), .in16(R16), .in17(R17),
    .in18(R18), .in19(R19), .in20(R20), .in21(R21), .in22(R22), .in23(R23), .in24(R24), .in25(R25),
    .in26(R26), .in27(R27), .in28(R28), .in29(R29), .in30(R30), .in31(R31), .out(RD2), .sel(A2));  // open: en

  // Other names for the same wires on the sheet: RST = reset
endmodule

module T (
);

  grf grf_1 ();  // open: clk, reset, WD, A3, RD1, RD2, A1, A2, WE
endmodule
