// Logisim project P0_L1_ftoi.circ as structural Verilog: 3 circuits, main circuit ftoi
module ftoi (
  input  [15:0] \input ,
  output [31:0] out_2
);

  wire Int_init, negSubRes, \全1 ;
  wire [4:0] negator_1_out, subRes;
  wire [31:0] bit_extender_1_out, bit_extender_2_out, multiplexer_1_out, multiplexer_2_out, negator_2_out,
       shifter_1_out, shifter_2_out, \小数左移_1_out_4 ;

  assign bit_extender_1_out = {{31{1'b0}}, Int_init};  // Bit_Extender bit_extender_1
  Shifter #(.width(32)) shifter_1 (.in(bit_extender_1_out), .\dist (subRes), .out(shifter_1_out));
  Subtractor #(.width(5)) subtractor_1 (.a(\input [14:10]), .b(5'b01111), .out(subRes), .bout(negSubRes));  // open: bin
  \判断全1_0  \u_判断全1_0_1  (.in_1(\input [14:10]), .\全1 (\全1 ), .\全0 (Int_init));
  \小数左移  \u_小数左移_1  (.\小数 (\input [9:0]), .subRes(subRes), .\整数左移部分 (shifter_1_out), .out_4(\小数左移_1_out_4 ));
  assign bit_extender_2_out = {{31{1'b0}}, Int_init};  // Bit_Extender bit_extender_2
  Negator #(.width(5)) negator_1 (.in(subRes), .out(negator_1_out));
  Shifter #(.width(32), .shift("lr")) shifter_2 (.in(bit_extender_2_out), .\dist (negator_1_out), .out(shifter_2_out));
  // Probe on multiplexer_1_out
  Multiplexer #(.width(32)) multiplexer_1 (
    .in0(\小数左移_1_out_4 ), .in1(shifter_2_out), .out(multiplexer_1_out), .sel(negSubRes));  // open: en
  Negator #(.width(32)) negator_2 (.in(multiplexer_1_out), .out(negator_2_out));
  Multiplexer #(.width(32)) multiplexer_2 (
    .in0(multiplexer_1_out), .in1(negator_2_out), .out(multiplexer_2_out), .sel(\input [15]));  // open: en
  Multiplexer #(.width(32)) multiplexer_3 (
    .in0(multiplexer_2_out), .in1({32{1'b0}}), .out(out_2), .sel(\全1 ));  // open: en
endmodule

// 全1/0
module \判断全1_0  (
  input  [4:0] in_1,
  output \全1 ,
  output \全0 
);

  and and_1 (\全1 , in_1[0], in_1[1], in_1[2], in_1[3], in_1[4]);
  or or_1 (\全0 , in_1[4], in_1[3], in_1[2], in_1[1], in_1[0]);
endmodule

module \小数左移  (
  input  [9:0] \小数 ,
  input  [4:0] subRes,
  input  [31:0] \整数左移部分 ,
  output [31:0] out_4
);

  wire [31:0] bit_extender_1_out, shifter_1_out, shifter_2_out;

  assign bit_extender_1_out = {{22{1'b0}}, \小数 };  // Bit_Extender bit_extender_1
  Shifter #(.width(32)) shifter_1 (.in(bit_extender_1_out), .\dist (subRes), .out(shifter_1_out));
  Shifter #(.width(32), .shift("lr")) shifter_2 (.in(shifter_1_out), .\dist (5'b01010), .out(shifter_2_out));
  assign out_4 = shifter_2_out | \整数左移部分 ;  // OR_Gate or_1, 32 bits wide
endmodule
