// Logisim project P0_L1_navigation_2020.circ as structural Verilog: 7 circuits, main circuit navigation
module navigation (
  input  [1:0] dir,
  input  clk,
  input  reset,
  output arrive,
  output hit
);

  wire [3:0] register_1_q, state_module_1_out_3;

  state_module state_module_1 (.\input (dir), .statement(register_1_q), .out_3(state_module_1_out_3));
  Register #(.width(4)) register_1 (.D(state_module_1_out_3), .Q(register_1_q), .clk(clk), .clr(reset));  // open: en
  // Probe on register_1_q
  output_module output_module_1 (.statement(register_1_q), .arrive(arrive), .hit(hit));
endmodule

// state
module state_module (
  input  [1:0] \input ,
  input  [3:0] statement,
  output [3:0] out_3
);

  wire [3:0] s1_1_out_2, s2_1_out_2, s3_1_out_2, sa_1_out_2;

  SA sa_1 (.\input (\input ), .out_2(sa_1_out_2));
  S1 s1_1 (.\input (\input ), .out_2(s1_1_out_2));
  S2 s2_1 (.in_1(\input ), .out_2(s2_1_out_2));
  S3 s3_1 (.INPUT(\input ), .out_2(s3_1_out_2));
  Multiplexer #(.select(4), .width(4)) multiplexer_1 (
    .in0(sa_1_out_2), .in1(s1_1_out_2), .in2(s2_1_out_2), .in3(s3_1_out_2), .in4(4'b0000), .in8(sa_1_out_2),
    .in9(s1_1_out_2), .in10(s2_1_out_2), .in11(s3_1_out_2), .out(out_3), .sel(statement));  // open: in5, in6, in7, in12, in13, in14, in15, en
endmodule

module SA (
  input  [1:0] \input ,
  output [3:0] out_2
);

  wire comparator_1_eq;

  // Probe on 4'b1000
  Comparator #(.width(2), .mode("unsigned")) comparator_1 (
    .a(\input ), .b(2'b00), .eq(comparator_1_eq));  // open: gt, lt
  Multiplexer #(.width(4)) multiplexer_1 (
    .in0(4'b1000), .in1(4'b0001), .out(out_2), .sel(comparator_1_eq));  // open: en

  // Notes on the sheet:
  //   1000
  //   0001
endmodule

module S1 (
  input  [1:0] \input ,
  output [3:0] out_2
);

  wire undriven;

  // Probe on undriven
  Multiplexer #(.select(2), .width(4)) multiplexer_1 (
    .in0(4'b0011), .in1(4'b0010), .in2(4'b0000), .in3(4'b1001), .out(out_2), .sel(\input ));  // open: en

  // Notes on the sheet:
  //   0011
endmodule

module S2 (
  input  [1:0] in_1,
  output [3:0] out_2
);

  Multiplexer #(.select(2), .width(4)) multiplexer_1 (
    .in0(4'b0100), .in1(4'b1010), .in2(4'b1010), .in3(4'b0001), .out(out_2), .sel(in_1));  // open: en
endmodule

module S3 (
  input  [1:0] INPUT,
  output [3:0] out_2
);

  Multiplexer #(.select(2), .width(4)) multiplexer_1 (
    .in0(4'b1011), .in1(4'b0100), .in2(4'b0001), .in3(4'b1011), .out(out_2), .sel(INPUT));  // open: en
endmodule

// output
module output_module (
  input  [3:0] statement,
  output arrive,
  output hit
);

  Comparator #(.width(4), .mode("unsigned")) comparator_1 (.a(4'b0100), .b(statement), .eq(arrive));  // open: gt, lt
  BitSelector #(.width(4)) bitselector_1 (.in(statement), .out(hit), .sel(2'b11));
endmodule
