// Logisim project P0_L2_nonexist.circ as structural Verilog: 2 circuits, main circuit main
module main (
  input  [7:0] in_1,
  input  [7:0] in_2,
  input  [7:0] in_3,
  input  [7:0] in_4,
  input  [7:0] in_5,
  output [7:0] out_6
);

  wire [2:0] bitfinder_1_index;
  wire [7:0] one_hot_1_out_2, one_hot_2_out_2, one_hot_3_out_2, one_hot_4_out_2, one_hot_5_out_2, or_1_out,
       or_2_out;

  one_hot one_hot_1 (.in_1(in_1), .out_2(one_hot_1_out_2));
  one_hot one_hot_2 (.in_1(in_2), .out_2(one_hot_2_out_2));
  one_hot one_hot_3 (.in_1(in_3), .out_2(one_hot_3_out_2));
  one_hot one_hot_4 (.in_1(in_4), .out_2(one_hot_4_out_2));
  one_hot one_hot_5 (.in_1(in_5), .out_2(one_hot_5_out_2));
  assign or_1_out = one_hot_1_out_2 | one_hot_2_out_2 | one_hot_3_out_2 | one_hot_4_out_2 | one_hot_5_out_2;  // OR_Gate or_1, 8 bits wide
  // Probe on or_2_out
  assign or_2_out = or_1_out | 8'h1;  // OR_Gate or_2, 8 bits wide
  BitFinder #(.\type ("low0")) bitfinder_1 (.in(or_2_out), .index(bitfinder_1_index));  // open: found
  assign out_6 = {{5{1'b0}}, bitfinder_1_index};  // Bit_Extender bit_extender_1
endmodule

module one_hot (
  input  [7:0] in_1,
  output [7:0] out_2
);

  wire comparator_1_eq;
  wire [2:0] bitadder_1_out;
  wire [7:0] decoder_1_out0;

  Decoder #(.select(3)) decoder_1 (
    .out0(decoder_1_out0[0]), .out1(decoder_1_out0[1]), .out2(decoder_1_out0[2]), .out3(decoder_1_out0[3]),
    .out4(decoder_1_out0[4]), .out5(decoder_1_out0[5]), .out6(decoder_1_out0[6]), .out7(decoder_1_out0[7]),
    .sel(in_1[2:0]));  // open: en
  BitAdder #(.width(5)) bitadder_1 (.in0(in_1[7:3]), .out(bitadder_1_out));
  Comparator #(.width(3), .mode("unsigned")) comparator_1 (
    .a(bitadder_1_out), .b(3'b000), .eq(comparator_1_eq));  // open: gt, lt
  Multiplexer #(.width(8)) multiplexer_1 (
    .in0(8'h1), .in1(decoder_1_out0), .out(out_2), .sel(comparator_1_eq));  // open: en
endmodule
