// Logisim project P0_L3_walker.circ as structural Verilog: 2 circuits, main circuit main
module main (
  input  [1:0] \input ,
  input  reset,
  input  clk,
  output [3:0] out_4
);

  wire [2:0] register_1_q, state_module_1_out_3, state_module_2_out_3;
  wire [3:0] bit_extender_1_out;

  state_module state_module_1 (.\input (\input ), .statement(register_1_q), .out_3(state_module_1_out_3));
  Register #(.width(3)) register_1 (.D(state_module_1_out_3), .Q(register_1_q), .clk(clk), .clr(reset));  // open: en
  state_module state_module_2 (.\input (\input ), .statement(register_1_q), .out_3(state_module_2_out_3));
  assign bit_extender_1_out = {{1{1'b0}}, state_module_2_out_3};  // Bit_Extender bit_extender_1
  Adder #(.width(4)) adder_1 (.a(bit_extender_1_out), .b(4'b0001), .out(out_4));  // open: cin, cout
endmodule

module state_module (
  input  [1:0] \input ,
  input  [2:0] statement,
  output [2:0] out_3
);

  wire [2:0] multiplexer_1_out, multiplexer_2_out, multiplexer_3_out, multiplexer_4_out, multiplexer_5_out,
       multiplexer_6_out, multiplexer_7_out, multiplexer_8_out;

  Multiplexer #(.select(2), .width(3)) multiplexer_1 (
    .in0(3'b111), .in1(3'b111), .in2(3'b110), .in3(3'b000), .out(multiplexer_1_out), .sel(\input ));  // open: en
  Multiplexer #(.select(2), .width(3)) multiplexer_2 (
    .in0(3'b110), .in1(3'b101), .in2(3'b110), .in3(3'b111), .out(multiplexer_2_out), .sel(\input ));  // open: en
  Multiplexer #(.select(2), .width(3)) multiplexer_3 (
    .in0(3'b101), .in1(3'b100), .in2(3'b100), .in3(3'b011), .out(multiplexer_3_out), .sel(\input ));  // open: en
  Multiplexer #(.select(2), .width(3)) multiplexer_4 (
    .in0(3'b110), .in1(3'b100), .in2(3'b101), .in3(3'b101), .out(multiplexer_4_out), .sel(\input ));  // open: en
  Multiplexer #(.select(2), .width(3)) multiplexer_5 (
    .in0(3'b001), .in1(3'b010), .in2(3'b011), .in3(3'b010), .out(multiplexer_5_out), .sel(\input ));  // open: en
  Multiplexer #(.select(2), .width(3)) multiplexer_6 (
    .in0(3'b011), .in1(3'b011), .in2(3'b100), .in3(3'b010), .out(multiplexer_6_out), .sel(\input ));  // open: en
  Multiplexer #(.select(2), .width(3)) multiplexer_7 (
    .in0(3'b000), .in1(3'b001), .in2(3'b111), .in3(3'b000), .out(multiplexer_7_out), .sel(\input ));  // open: en
  Multiplexer #(.select(2), .width(3)) multiplexer_8 (
    .in0(3'b000), .in1(3'b010), .in2(3'b001), .in3(3'b001), .out(multiplexer_8_out), .sel(\input ));  // open: en
  Multiplexer #(.select(3), .width(3)) multiplexer_9 (
    .in0(multiplexer_7_out), .in1(multiplexer_8_out), .in2(multiplexer_5_out), .in3(multiplexer_6_out),
    .in4(multiplexer_3_out), .in5(multiplexer_4_out), .in6(multiplexer_2_out), .in7(multiplexer_1_out),
    .out(out_3), .sel(statement));  // open: en
endmodule
