// Logisim project P1-L0-gray.circ as structural Verilog: 3 circuits, main circuit main
module main (
  input  Reset,
  input  Clk,
  input  En,
  output [2:0] Output,
  output Overflow
);

  wire comparator_1_eq, not_1_out;
  wire [2:0] multiplexer_1_out, next_state, state;

  output_module output_module_1 (.in_1(state), .out_2(Output));
  Comparator #(.width(3), .mode("unsigned")) comparator_1 (
    .a(state), .b(3'b111), .eq(comparator_1_eq));  // open: gt, lt
  state_module state_module_1 (.state(state), .En(En), .out_3(next_state));
  not not_1 (not_1_out, Reset);
  Multiplexer #(.width(3)) multiplexer_1 (
    .in0(3'b000), .in1(next_state), .out(multiplexer_1_out), .sel(not_1_out));  // open: en
  Register #(.width(1)) register_1 (.D(comparator_1_eq), .en(comparator_1_eq), .Q(Overflow), .clk(Clk), .clr(Reset));
  Register #(.width(3)) register_2 (.D(multiplexer_1_out), .Q(state), .clk(Clk));  // open: en, clr
endmodule

// State
module state_module (
  input  [2:0] state,
  input  En,
  output [2:0] out_3
);

  wire [2:0] adder_1_out;

  Adder #(.width(3)) adder_1 (.a(3'b001), .b(state), .out(adder_1_out));  // open: cin, cout
  Multiplexer #(.width(3)) multiplexer_1 (.in0(state), .in1(adder_1_out), .out(out_3), .sel(En));  // open: en
endmodule

// Output
module output_module (
  input  [2:0] in_1,
  output [2:0] out_2
);

  xor xor_1 (out_2[1], in_1[1], in_1[2]);
  xor xor_2 (out_2[0], in_1[0], in_1[1]);

  assign out_2[2] = in_1[2];
endmodule
