// Logisim project P3-cpu.circ as structural Verilog: 11 circuits, main circuit main
module main (
  input  rst,
  output [31:0] Instr,
  output [31:0] PC,
  output out_4,
  output [4:0] out_5,
  output [31:0] RegData,
  output out_7,
  output [31:0] ALURes,
  output [31:0] DMWD
);

  wire ASel, BSel, clock_1_out, DMExt, EXTOp, Zero;
  wire [1:0] DMType, WDSel, WRSel;
  wire [2:0] ALUOp, NPCOp;
  wire [31:0] ext_1_out_3, multiplexer_3_out, multiplexer_4_out, npc_1_npc, PC4, pc_t, RA, RD, shamt;

  // Probe on Instr[25:0]
  Register #(.width(32)) register_1 (.D(npc_1_npc), .Q(pc_t), .clk(clock_1_out), .clr(rst));  // open: en
  Clock clock_1 (.out(clock_1_out));
  IM im_1 (.PC(pc_t), .out_2(Instr));
  NPC npc_1 (.IMM(Instr[25:0]), .RA(RA), .PC4(PC4), .NPC(npc_1_npc), .NPCOp(NPCOp), .PC(pc_t), .Zero(Zero), .rst(rst));
  Multiplexer #(.select(2), .width(5)) multiplexer_1 (
    .in0(Instr[20:16]), .in1(Instr[15:11]), .in2({5{1'b1}}), .out(out_5), .sel(WRSel));  // open: in3, en
  CU cu_1 (
    .Instr(Instr), .NPCOp(NPCOp), .DMWr(out_7), .shamt(shamt), .ALUOp(ALUOp), .ASel(ASel), .BSel(BSel),
    .EXTOp(EXTOp), .RFWr(out_4), .A3Sel(WRSel), .WDSel(WDSel), .out_9(DMType), .out_10(DMExt));
  Multiplexer #(.select(2), .width(32)) multiplexer_2 (
    .in0(ALURes), .in1(RD), .in2(PC4), .out(RegData), .sel(WDSel));  // open: in3, en
  EXT ext_1 (.IMM(Instr[15:0]), .EXTOp(EXTOp), .out_3(ext_1_out_3));
  RF rf_1 (
    .reset(rst), .A1(Instr[25:21]), .A2(Instr[20:16]), .A3(out_5), .WD(RegData), .RD1(RA), .RD2(DMWD),
    .WE(out_4));
  Multiplexer #(.width(32)) multiplexer_3 (.in0(RA), .in1(shamt), .out(multiplexer_3_out), .sel(ASel));  // open: en
  Multiplexer #(.width(32)) multiplexer_4 (
    .in0(DMWD), .in1(ext_1_out_3), .out(multiplexer_4_out), .sel(BSel));  // open: en
  ALU alu_1 (.A(multiplexer_3_out), .B(multiplexer_4_out), .ALURes(ALURes), .ALUOp(ALUOp), .Zero(Zero));
  DM dm_1 (.A(ALURes), .WD(DMWD), .RD(RD), .DMWr(out_7), .rst(rst), .DMExt(DMExt), .DMType(DMType));
  Adder #(.width(32)) adder_1 (.a(32'h3000), .b(pc_t), .out(PC));  // open: cin, cout

  // Other names for the same wires on the sheet: DMWr = out_7; IMM26[25:0] = Instr[25:0]; RegAddr[4:0] = out_5;
  //   RFWr = out_4; WD[31:0] = DMWD

  // Notes on the sheet:
  //   IMM
  //   M1
  //   rs
  //   rt
endmodule

module NPC (
  input  [25:0] IMM,
  input  Zero,
  input  rst,
  input  [31:0] PC,
  input  [2:0] NPCOp,
  input  [31:0] RA,
  output [31:0] NPC,
  output [31:0] PC4
);

  wire [31:0] adder_2_out, bit_extender_1_out, multiplexer_1_out, shifter_1_out;

  Adder #(.width(32)) adder_1 (.a(32'h4), .b(PC), .out(PC4));  // open: cin, cout
  assign bit_extender_1_out = {{16{IMM[15]}}, IMM[15:0]};  // Bit_Extender bit_extender_1
  Shifter #(.width(32)) shifter_1 (.in(bit_extender_1_out), .\dist (5'b00010), .out(shifter_1_out));
  Adder #(.width(32)) adder_2 (.a(PC4), .b(shifter_1_out), .out(adder_2_out));  // open: cin, cout
  Multiplexer #(.width(32)) multiplexer_1 (
    .in0(PC4), .in1(adder_2_out), .out(multiplexer_1_out), .sel(Zero));  // open: en
  Multiplexer #(.select(3), .width(32)) multiplexer_2 (
    .in0(PC4), .in1(multiplexer_1_out), .in2({PC[31:28], IMM, 2'b00}), .in3(RA), .out(NPC), .sel(NPCOp));  // open: in4, in5, in6, in7, en

  // Notes on the sheet:
  //   PC+4
  //   BEQ
  //   JAL
  //   JR
endmodule

module IM (
  input  [31:0] PC,
  output [31:0] out_2
);

  ROM #(.addrWidth(12), .dataWidth(32)) rom_1 (.addr(PC[13:2]), .data(out_2));  // open: sel

  // Notes on the sheet:
  //   contents of rom_1 (hex, n*v repeats v):
  //   34010020 34020002 411822 a12820 c000003 0 34040013 3402000d
endmodule

module PC (
  input  [31:0] IN,
  input  rst,
  output [31:0] out_3
);

  wire clock_1_out;
  wire [31:0] register_1_q, xor_1_out;

  assign xor_1_out = 32'h3000 ^ IN;  // XOR_Gate xor_1, 32 bits wide
  Clock clock_1 (.out(clock_1_out));
  Register #(.width(32)) register_1 (.D(xor_1_out), .Q(register_1_q), .clk(clock_1_out), .clr(rst));  // open: en
  assign out_3 = 32'h3000 ^ register_1_q;  // XOR_Gate xor_2, 32 bits wide
endmodule

module CU (
  input  [31:0] Instr,
  output [2:0] NPCOp,
  output [31:0] shamt,
  output RFWr,
  output [1:0] A3Sel,
  output [1:0] WDSel,
  output EXTOp,
  output [2:0] ALUOp,
  output [1:0] out_9,
  output out_10,
  output ASel,
  output BSel,
  output DMWr
);

  wire _00_2_out, _00_out, _01_2_out, _1_2_out, _1_3_out, _1_4_out, _1_5_out, _1_6_out, _01_out, _1_out,
       _10_2_out, _10_out, add, ADD_2_out, add_fun_out, B_out, beq, beq_2_out, blez, blez_2_out, H_out, jal,
       jal_2_out, jr_out, lb, lbu, lh, lhu, lui, lui_2_out, lw, lwu, not_1_out, not_2_out, not_3_out,
       not_4_out, not_5_out, not_6_out, not_7_out, not_8_out, not_9_out, not_10_out, not_11_out, not_12_out,
       op0_6, OR_out, ori, sb, sbu, sh, shu, sll, sll_fun_out, slt, slt_2_out, slt_fun_out, slti, sub,
       SUB_2_out, sub_fun_out, sw, swu, W_out, \左移_out ;

  not not_1 (not_1_out, Instr[31]);
  not not_2 (not_2_out, Instr[30]);
  not not_3 (not_3_out, Instr[29]);
  // Probe on Instr[31:26]
  not not_4 (not_4_out, Instr[28]);
  assign shamt = {{27{1'b0}}, Instr[10:6]};  // Bit_Extender bit_extender_1
  not not_5 (not_5_out, Instr[27]);
  not not_6 (not_6_out, Instr[26]);
  not not_7 (not_7_out, Instr[4]);
  not not_8 (not_8_out, Instr[5]);
  not not_9 (not_9_out, Instr[3]);
  // Probe on Instr[5:0]
  not not_10 (not_10_out, Instr[2]);
  not not_11 (not_11_out, Instr[0]);
  not not_12 (not_12_out, Instr[1]);
  and add_op (op0_6, not_1_out, not_2_out, not_3_out, not_4_out, not_5_out, not_6_out);
  and add_fun (add_fun_out, Instr[5], not_7_out, not_9_out, not_10_out, not_12_out, not_11_out);
  and sub_fun (sub_fun_out, Instr[5], not_7_out, not_9_out, not_10_out, Instr[1], not_11_out);
  and u_ori (ori, not_1_out, not_2_out, Instr[29], Instr[28], not_5_out, Instr[26]);
  and u_lw (lw, Instr[31], not_2_out, not_3_out, not_4_out, Instr[26], Instr[26]);
  and u_sw (sw, Instr[31], not_2_out, Instr[29], not_4_out, Instr[27], Instr[26]);
  and u_beq (beq, not_1_out, not_2_out, not_3_out, Instr[28], not_5_out, not_6_out);
  and u_lui (lui, not_1_out, not_2_out, Instr[29], Instr[28], Instr[27], Instr[26]);
  and sll_fun (sll_fun_out, not_8_out, not_7_out, not_9_out, not_10_out, not_12_out, not_11_out);
  and slt_fun (slt_fun_out, Instr[5], not_7_out, Instr[3], not_10_out, Instr[1], not_11_out);
  and u_slti (slti, not_1_out, not_2_out, Instr[29], not_4_out, Instr[27], not_6_out);
  and u_blez (blez, not_1_out, not_2_out, not_3_out, Instr[28], Instr[27], not_6_out);
  and u_jal (jal, not_1_out, not_2_out, not_3_out, not_4_out, Instr[27], Instr[26]);
  and u_add (add, op0_6, add_fun_out);
  and u_sub (sub, op0_6, sub_fun_out);
  and u_sll (sll, op0_6, sll_fun_out);
  and u_slt (slt, op0_6, slt_fun_out);
  or W (W_out, lwu, lw, sw, swu);
  or H (H_out, lhu, lh, sh, shu);
  or B (B_out, lbu, lb, sb, sbu);
  or ADD_2 (ADD_2_out, add, lw, sw);
  or SUB_2 (SUB_2_out, sub, beq);
  buf OR (OR_out, ori);  // OR_Gate
  buf lui_2 (lui_2_out, lui);  // OR_Gate
  buf \u_左移  (\左移_out , sll);  // OR_Gate
  or slt_2 (slt_2_out, slt, slti);
  buf blez_2 (blez_2_out, blez);  // OR_Gate
  or beq_2 (beq_2_out, blez, beq);
  buf jal_2 (jal_2_out, jal);  // OR_Gate
  // OR_Gate jr has open pins: out=jr_out
  or _00 (_00_out, ori, lw, lui, slti);
  or _01 (_01_out, slt, sll, sub, add);
  buf _10 (_10_out, jal);  // OR_Gate
  or _00_2 (_00_2_out, slti, slt, ori, sub, add);
  buf _01_2 (_01_2_out, lw);  // OR_Gate
  buf _10_2 (_10_2_out, jal);  // OR_Gate
  buf _1 (_1_out, sll);  // OR_Gate
  or _1_2 (_1_2_out, ori, lw, sw, lui, slti);
  buf _1_3 (_1_3_out, sw);  // OR_Gate
  or _1_4 (_1_4_out, sw, lw, slti);
  or _1_5 (_1_5_out, lb, lh);
  Pull_Resistor pull_resistor_1 (.node(ALUOp));
  Priority_Encoder priority_encoder_1 (
    .in0(ADD_2_out), .in1(SUB_2_out), .in2(OR_out), .in3(lui_2_out), .in4(\左移_out ), .in5(slt_2_out),
    .in6(blez_2_out), .out(ALUOp));  // open: in7, en_in, gs, en_out
  Priority_Encoder priority_encoder_2 (
    .in1(beq_2_out), .in2(jal_2_out), .in3(jr_out), .out(NPCOp));  // open: in0, in4, in5, in6, in7, en_in, gs, en_out
  Pull_Resistor pull_resistor_2 (.node(NPCOp));
  Priority_Encoder #(.select(2)) priority_encoder_3 (
    .in0(_00_out), .in1(_01_out), .in2(_10_out), .out(A3Sel));  // open: in3, gs, en_out, en_in
  Pull_Resistor pull_resistor_3 (.node(A3Sel));
  Priority_Encoder #(.select(2)) priority_encoder_4 (
    .in0(_00_2_out), .in1(_01_2_out), .in2(_10_2_out), .out(WDSel));  // open: in3, gs, en_out, en_in
  Pull_Resistor pull_resistor_4 (.node(WDSel));
  or _1_6 (_1_6_out, slt, add, sub, ori, lw, lui, sll, slti, jal);
  Comparator #(.width(1), .mode("unsigned")) comparator_1 (.a(_1_6_out), .b(1'b1), .eq(RFWr));  // open: gt, lt
  Priority_Encoder #(.select(1)) priority_encoder_5 (.in1(_1_out), .out(ASel));  // open: in0, gs, en_out, en_in
  Pull_Resistor pull_resistor_5 (.node(ASel));
  Comparator #(.width(1), .mode("unsigned")) comparator_2 (.a(_1_2_out), .b(1'b1), .eq(BSel));  // open: gt, lt
  Comparator #(.width(1), .mode("unsigned")) comparator_3 (.a(_1_3_out), .b(1'b1), .eq(DMWr));  // open: gt, lt
  Comparator #(.width(1), .mode("unsigned")) comparator_4 (.a(_1_4_out), .b(1'b1), .eq(EXTOp));  // open: gt, lt
  Priority_Encoder #(.select(2)) priority_encoder_6 (
    .in0(W_out), .in1(H_out), .in2(B_out), .out(out_9));  // open: in3, gs, en_out, en_in
  Pull_Resistor pull_resistor_6 (.node(out_9));
  Comparator #(.width(1), .mode("unsigned")) comparator_5 (.a(_1_5_out), .b(1'b1), .eq(out_10));  // open: gt, lt

  // Other names for the same wires on the sheet: DMExt = out_10; DMType[1:0] = out_9; funct[5:0] = Instr[5:0];
  //   opcode[5:0] = Instr[31:26]; WRSel[1:0] = A3Sel

  // Notes on the sheet:
  //   01
  //   10
  //   11
  //   sll使用：选择s为A
endmodule

module RF (
  input  WE,
  input  reset,
  input  [4:0] A1,
  input  [4:0] A2,
  input  [4:0] A3,
  input  [31:0] WD,
  output [31:0] RD1,
  output [31:0] RD2
);

  wire CLK;
  wire [31:0] R0, R1, R2, R3, R4, R5, R6, R7, R8, R9, R10, R11, R12, R13, R14, R15, R16, R17, R18, R19, R20,
       R21, R22, R23, R24, R25, R26, R27, R28, R29, R30, R31, W0, W1, W2, W3, W4, W5, W6, W7, W8, W9, W10,
       W11, W12, W13, W14, W15, W16, W17, W18, W19, W20, W21, W22, W23, W24, W25, W26, W27, W28, W29, W30,
       W31;

  Clock clock_1 (.out(CLK));
  Register #(.width(32)) _0 (.D(W0), .en(WE), .Q(R0), .clk(CLK), .clr(1'b1));
  Register #(.width(32)) _4 (.D(W4), .en(WE), .Q(R4), .clk(CLK), .clr(reset));
  Register #(.width(32)) _8 (.D(W8), .en(WE), .Q(R8), .clk(CLK), .clr(reset));
  Register #(.width(32)) _12 (.D(W12), .en(WE), .Q(R12), .clk(CLK), .clr(reset));
  Demultiplexer #(.select(5), .width(32), .tristate("true")) demultiplexer_1 (
    .out1(W1), .out2(W2), .out3(W3), .out4(W4), .out5(W5), .out6(W6), .out7(W7), .out8(W8), .out9(W9),
    .out10(W10), .out11(W11), .out12(W12), .out13(W13), .out14(W14), .out15(W15), .out16(W16), .out17(W17),
    .out18(W18), .out19(W19), .out20(W20), .out21(W21), .out22(W22), .out23(W23), .out24(W24), .out25(W25),
    .out26(W26), .out27(W27), .out28(W28), .out29(W29), .out30(W30), .out31(W31), .in(WD), .sel(A3), .en(WE));  // open: out0
  Register #(.width(32)) _1 (.D(W1), .en(WE), .Q(R1), .clk(CLK), .clr(reset));
  Register #(.width(32)) _5 (.D(W5), .en(WE), .Q(R5), .clk(CLK), .clr(reset));
  Register #(.width(32)) _9 (.D(W9), .en(WE), .Q(R9), .clk(CLK), .clr(reset));
  Register #(.width(32)) _13 (.D(W13), .en(WE), .Q(R13), .clk(CLK), .clr(reset));
  Register #(.width(32)) _2 (.D(W2), .en(WE), .Q(R2), .clk(CLK), .clr(reset));
  Register #(.width(32)) _6 (.D(W6), .en(WE), .Q(R6), .clk(CLK), .clr(reset));
  Register #(.width(32)) _10 (.D(W10), .en(WE), .Q(R10), .clk(CLK), .clr(reset));
  Register #(.width(32)) _14 (.D(W14), .en(WE), .Q(R14), .clk(CLK), .clr(reset));
  Register #(.width(32)) _3 (.D(W3), .en(WE), .Q(R3), .clk(CLK), .clr(reset));
  Register #(.width(32)) _7 (.D(W7), .en(WE), .Q(R7), .clk(CLK), .clr(reset));
  Register #(.width(32)) _11 (.D(W11), .en(WE), .Q(R11), .clk(CLK), .clr(reset));
  Register #(.width(32)) _15 (.D(W15), .en(WE), .Q(R15), .clk(CLK), .clr(reset));
  Register #(.width(32)) _16 (.D(W16), .en(WE), .Q(R16), .clk(CLK), .clr(reset));
  Register #(.width(32)) _20 (.D(W20), .en(WE), .Q(R20), .clk(CLK), .clr(reset));
  Register #(.width(32)) _24 (.D(W24), .en(WE), .Q(R24), .clk(CLK), .clr(reset));
  Register #(.width(32)) _28 (.D(W28), .en(WE), .Q(R28), .clk(CLK), .clr(reset));
  Register #(.width(32)) _17 (.D(W17), .en(WE), .Q(R17), .clk(CLK), .clr(reset));
  Register #(.width(32)) _21 (.D(W21), .en(WE), .Q(R21), .clk(CLK), .clr(reset));
  Register #(.width(32)) _25 (.D(W25), .en(WE), .Q(R25), .clk(CLK), .clr(reset));
  Register #(.width(32)) _29 (.D(W29), .en(WE), .Q(R29), .clk(CLK), .clr(reset));
  Multiplexer #(.select(5), .width(32)) multiplexer_1 (
    .in0(R0), .in1(R1), .in2(R2), .in3(R3), .in4(R4), .in5(R5), .in6(R6), .in7(R7), .in8(R8), .in9(R9),
    .in10(R10), .in11(R11), .in12(R12), .in13(R13), .in14(R14), .in15(R15), .in16(R16), .in17(R17),
    .in18(R18), .in19(R19), .in20(R20), .in21(R21), .in22(R22), .in23(R23), .in24(R24), .in25(R25),
    .in26(R26), .in27(R27), .in28(R28), .in29(R29), .in30(R30), .in31(R31), .out(RD1), .sel(A1));  // open: en
  Register #(.width(32)) _18 (.D(W18), .en(WE), .Q(R18), .clk(CLK), .clr(reset));
  Register #(.width(32)) _22 (.D(W22), .en(WE), .Q(R22), .clk(CLK), .clr(reset));
  Register #(.width(32)) _26 (.D(W26), .en(WE), .Q(R26), .clk(CLK), .clr(reset));
  Register #(.width(32)) _30 (.D(W30), .en(WE), .Q(R30), .clk(CLK), .clr(reset));
  Register #(.width(32)) _19 (.D(W19), .en(WE), .Q(R19), .clk(CLK), .clr(reset));
  Register #(.width(32)) _23 (.D(W23), .en(WE), .Q(R23), .clk(CLK), .clr(reset));
  Register #(.width(32)) _27 (.D(W27), .en(WE), .Q(R27), .clk(CLK), .clr(reset));
  Register #(.width(32)) _31 (.D(W31), .en(WE), .Q(R31), .clk(CLK), .clr(reset));
  Multiplexer #(.select(5), .width(32)) multiplexer_2 (
    .in0(R0), .in1(R1), .in2(R2), .in3(R3), .in4(R4), .in5(R5), .in6(R6), .in7(R7), .in8(R8), .in9(R9),
    .in10(R10), .in11(R11), .in12(R12), .in13(R13), .in14(R14), .in15(R15), .in16(R16), .in17(R17),
    .in18(R18), .in19(R19), .in20(R20), .in21(R21), .in22(R22), .in23(R23), .in24(R24), .in25(R25),
    .in26(R26), .in27(R27), .in28(R28), .in29(R29), .in30(R30), .in31(R31), .out(RD2), .sel(A2));  // open: en

  // Other names for the same wires on the sheet: RST = reset
endmodule

module EXT (
  input  [15:0] IMM,
  input  EXTOp,
  output [31:0] out_3
);

  wire [31:0] bit_extender_1_out, bit_extender_2_out;

  assign bit_extender_1_out = {{16{1'b0}}, IMM};  // Bit_Extender bit_extender_1
  assign bit_extender_2_out = {{16{IMM[15]}}, IMM};  // Bit_Extender bit_extender_2
  Multiplexer #(.width(32)) multiplexer_1 (
    .in0(bit_extender_1_out), .in1(bit_extender_2_out), .out(out_3), .sel(EXTOp));  // open: en
endmodule

module ALU (
  input  [2:0] ALUOp,
  input  [31:0] A,
  input  [31:0] B,
  output [31:0] ALURes,
  output Zero
);

  wire comparator_1_lt, comparator_2_gt, comparator_3_eq, not_1_out;
  wire [4:0] bit_extender_1_out;
  wire [31:0] adder_1_out, multiplexer_1_out, OR_out, shifter_1_out, shifter_2_out, subRes;

  Bit_Extender #(.in_width(32), .out_width(5)) bit_extender_1 (.in(A), .out(bit_extender_1_out));
  // Probe on bit_extender_1_out
  Comparator #(.width(32)) comparator_1 (.a(A), .b(B), .lt(comparator_1_lt));  // open: gt, eq
  Comparator #(.width(32)) comparator_2 (.a(A), .b(B), .gt(comparator_2_gt));  // open: eq, lt
  Comparator #(.width(32), .mode("unsigned")) comparator_3 (.a(A), .b(B), .eq(comparator_3_eq));  // open: gt, lt
  Adder #(.width(32)) adder_1 (.a(A), .b(B), .out(adder_1_out));  // open: cin, cout
  Subtractor #(.width(32)) subtractor_1 (.a(A), .b(B), .out(subRes));  // open: bin, bout
  assign OR_out = A | B;  // OR_Gate OR, 32 bits wide
  Shifter #(.width(32)) shifter_1 (.in(B), .\dist (5'b10000), .out(shifter_1_out));
  Shifter #(.width(32)) shifter_2 (.in(B), .\dist (bit_extender_1_out), .out(shifter_2_out));
  not not_1 (not_1_out, comparator_2_gt);
  or or_2 (Zero, not_1_out, comparator_3_eq);
  Multiplexer #(.width(32)) multiplexer_1 (
    .in0({32{1'b0}}), .in1(32'h1), .out(multiplexer_1_out), .sel(comparator_1_lt));  // open: en
  Multiplexer #(.select(3), .width(32)) multiplexer_2 (
    .in0(adder_1_out), .in1(subRes), .in2(OR_out), .in3(shifter_1_out), .in4(shifter_2_out),
    .in5(multiplexer_1_out), .out(ALURes), .sel(ALUOp));  // open: in6, in7, en

  // Notes on the sheet:
  //   lui
  //   isZero: if equal, 1; else 0;
endmodule

module DM (
  input  [1:0] DMType,
  input  DMWr,
  input  rst,
  input  DMExt,
  input  [31:0] A,
  input  [31:0] WD,
  output [31:0] RD
);

  wire clock_1_out;
  wire [31:0] oridata, undriven;

  Clock clock_1 (.out(clock_1_out));
  RAM #(.addrWidth(12), .dataWidth(32), .bus("separate")) ram_1 (
    .addr(A[13:2]), .din(undriven), .data(oridata), .str(DMWr), .clk(clock_1_out), .clr(rst));  // open: sel, ld
  L_JUDGE l_judge_1 (.low(A[1:0]), .RD(oridata), .DMType(DMType), .DMExt(DMExt), .out_5(RD));

  // Other names for the same wires on the sheet: Addr[31:0] = A; low[1:0] = A[1:0]; Reset = rst
endmodule

module L_JUDGE (
  input  [1:0] low,
  input  [31:0] RD,
  input  [1:0] DMType,
  input  DMExt,
  output [31:0] out_5
);

  wire [31:0] bit_extender_1_out, bit_extender_2_out, bit_extender_3_out, bit_extender_4_out,
       bit_extender_5_out, bit_extender_6_out, bit_extender_7_out, bit_extender_8_out, bit_extender_9_out,
       bit_extender_10_out, bit_extender_11_out, bit_extender_12_out, multiplexer_1_out, multiplexer_2_out,
       multiplexer_3_out, multiplexer_4_out, multiplexer_5_out, multiplexer_6_out, multiplexer_7_out,
       multiplexer_8_out;

  assign bit_extender_1_out = {{16{1'b0}}, RD[15:0]};  // Bit_Extender bit_extender_1
  assign bit_extender_2_out = {{16{RD[15]}}, RD[15:0]};  // Bit_Extender bit_extender_2
  assign bit_extender_3_out = {{16{1'b0}}, RD[31:16]};  // Bit_Extender bit_extender_3
  assign bit_extender_4_out = {{16{RD[31]}}, RD[31:16]};  // Bit_Extender bit_extender_4
  assign bit_extender_5_out = {{24{1'b0}}, RD[7:0]};  // Bit_Extender bit_extender_5
  assign bit_extender_6_out = {{24{RD[7]}}, RD[7:0]};  // Bit_Extender bit_extender_6
  assign bit_extender_7_out = {{24{1'b0}}, RD[15:8]};  // Bit_Extender bit_extender_7
  assign bit_extender_8_out = {{24{RD[15]}}, RD[15:8]};  // Bit_Extender bit_extender_8
  assign bit_extender_9_out = {{24{1'b0}}, RD[23:16]};  // Bit_Extender bit_extender_9
  assign bit_extender_10_out = {{24{RD[23]}}, RD[23:16]};  // Bit_Extender bit_extender_10
  assign bit_extender_11_out = {{24{1'b0}}, RD[31:24]};  // Bit_Extender bit_extender_11
  assign bit_extender_12_out = {{24{RD[31]}}, RD[31:24]};  // Bit_Extender bit_extender_12
  Multiplexer #(.width(32)) multiplexer_1 (
    .in0(bit_extender_1_out), .in1(bit_extender_2_out), .out(multiplexer_1_out), .sel(DMExt));  // open: en
  Multiplexer #(.width(32)) multiplexer_2 (
    .in0(bit_extender_3_out), .in1(bit_extender_4_out), .out(multiplexer_2_out), .sel(DMExt));  // open: en
  Multiplexer #(.width(32)) multiplexer_3 (
    .in0(bit_extender_5_out), .in1(bit_extender_6_out), .out(multiplexer_3_out), .sel(DMExt));  // open: en
  Multiplexer #(.width(32)) multiplexer_4 (
    .in0(bit_extender_7_out), .in1(bit_extender_8_out), .out(multiplexer_4_out), .sel(DMExt));  // open: en
  Multiplexer #(.width(32)) multiplexer_5 (
    .in0(bit_extender_9_out), .in1(bit_extender_10_out), .out(multiplexer_5_out), .sel(DMExt));  // open: en
  Multiplexer #(.width(32)) multiplexer_6 (
    .in0(bit_extender_11_out), .in1(bit_extender_12_out), .out(multiplexer_6_out), .sel(DMExt));  // open: en
  Multiplexer #(.width(32)) multiplexer_7 (
    .in0(multiplexer_1_out), .in1(multiplexer_2_out), .out(multiplexer_7_out), .sel(low[1]));  // open: en
  Multiplexer #(.select(2), .width(32)) multiplexer_8 (
    .in0(multiplexer_3_out), .in1(multiplexer_4_out), .in2(multiplexer_5_out), .in3(multiplexer_6_out),
    .out(multiplexer_8_out), .sel(low));  // open: en
  Multiplexer #(.select(2), .width(32)) multiplexer_9 (
    .in0(RD), .in1(multiplexer_7_out), .in2(multiplexer_8_out), .out(out_5), .sel(DMType));  // open: in3, en
endmodule

module S_JUDGE (
  input  [1:0] low,
  input  [31:0] oridata,
  input  [31:0] WD,
  input  [1:0] DMType,
  output [31:0] out_5
);

  wire [31:0] multiplexer_1_out, multiplexer_2_out;

  Multiplexer #(.select(2), .width(32)) multiplexer_1 (
    .in0({oridata[15:0], WD[15:0]}), .in2({WD[15:0], oridata[31:16]}), .out(multiplexer_1_out), .sel(low));  // open: in1, in3, en
  Multiplexer #(.select(2), .width(32)) multiplexer_2 (
    .in0({oridata[31:8], WD[7:0]}), .in1({oridata[31:16], WD[7:0], oridata[7:0]}),
    .in2({oridata[31:24], WD[7:0], oridata[15:0]}), .in3({WD[7:0], oridata[23:0]}), .out(multiplexer_2_out),
    .sel(low));  // open: en
  Multiplexer #(.select(2), .width(32)) multiplexer_3 (
    .in0(WD), .in1(multiplexer_2_out), .in2(multiplexer_1_out), .out(out_5), .sel(DMType));  // open: in3, en

  // Other names for the same wires on the sheet: DB[7:0] = WD[7:0]; DH[15:0] = WD[15:0]; oribyte1[7:0] = oridata[7:0];
  //   orihalf1[15:0] = oridata[15:0]; oribyte2[7:0] = oridata[15:8]; oribyte3[7:0] = oridata[23:16];
  //   orihalf2[15:0] = oridata[31:16]; oribyte4[7:0] = oridata[31:24]
endmodule
