// Logisim project foreverYoloCpu.circ as structural Verilog: 12 circuits, main circuit CPU
module GRF (
  input  clk,
  input  reset,
  input  WE,
  input  [4:0] A1,
  input  [4:0] A2,
  input  [4:0] A3,
  input  [31:0] WD,
  output [31:0] RD1,
  output [31:0] RD2
);

  wire [31:0] _0O, _1I, _1O, _2I, _2O, _3I, _3O, _4I, _4O, _5I, _5O, _6I, _6O, _7I, _7O, _8I, _8O, _9I, _9O,
       _10I, _10O, _11I, _11O, _12I, _12O, _13I, _13O, _14I, _14O, _15I, _15O, _16I, _16O, _17I, _17O, _18I,
       _18O, _19I, _19O, _20I, _20O, _21I, _21O, _22I, _22O, _23I, _23O, _24I, _24O, _25I, _25O, _26I, _26O,
       _27I, _27O, _28I, _28O, _29I, _29O, _30I, _30O, _31I, _31O;

  Register #(.width(32)) _0 (.D({32{1'b0}}), .en(WE), .Q(_0O), .clk(clk), .clr(reset));
  Register #(.width(32)) _8 (.D(_8I), .en(WE), .Q(_8O), .clk(clk), .clr(reset));
  Register #(.width(32)) _16 (.D(_16I), .en(WE), .Q(_16O), .clk(clk), .clr(reset));
  Register #(.width(32)) _24 (.D(_24I), .en(WE), .Q(_24O), .clk(clk), .clr(reset));
  Register #(.width(32)) _1 (.D(_1I), .en(WE), .Q(_1O), .clk(clk), .clr(reset));
  Register #(.width(32)) _9 (.D(_9I), .en(WE), .Q(_9O), .clk(clk), .clr(reset));
  Register #(.width(32)) _17 (.D(_17I), .en(WE), .Q(_17O), .clk(clk), .clr(reset));
  Register #(.width(32)) _25 (.D(_25I), .en(WE), .Q(_25O), .clk(clk), .clr(reset));
  Register #(.width(32)) _2 (.D(_2I), .en(WE), .Q(_2O), .clk(clk), .clr(reset));
  Register #(.width(32)) _10 (.D(_10I), .en(WE), .Q(_10O), .clk(clk), .clr(reset));
  Register #(.width(32)) _18 (.D(_18I), .en(WE), .Q(_18O), .clk(clk), .clr(reset));
  Register #(.width(32)) _26 (.D(_26I), .en(WE), .Q(_26O), .clk(clk), .clr(reset));
  Multiplexer #(.select(5), .width(32)) multiplexer_1 (
    .in0(_0O), .in1(_1O), .in2(_2O), .in3(_3O), .in4(_4O), .in5(_5O), .in6(_6O), .in7(_7O), .in8(_8O),
    .in9(_9O), .in10(_10O), .in11(_11O), .in12(_12O), .in13(_13O), .in14(_14O), .in15(_15O), .in16(_16O),
    .in17(_17O), .in18(_18O), .in19(_19O), .in20(_20O), .in21(_21O), .in22(_22O), .in23(_23O), .in24(_24O),
    .in25(_25O), .in26(_26O), .in27(_27O), .in28(_28O), .in29(_29O), .in30(_30O), .in31(_31O), .out(RD1),
    .sel(A1));  // open: en
  Register #(.width(32)) _3 (.D(_3I), .en(WE), .Q(_3O), .clk(clk), .clr(reset));
  Register #(.width(32)) _11 (.D(_11I), .en(WE), .Q(_11O), .clk(clk), .clr(reset));
  Register #(.width(32)) _19 (.D(_19I), .en(WE), .Q(_19O), .clk(clk), .clr(reset));
  Register #(.width(32)) _27 (.D(_27I), .en(WE), .Q(_27O), .clk(clk), .clr(reset));
  Register #(.width(32)) _4 (.D(_4I), .en(WE), .Q(_4O), .clk(clk), .clr(reset));
  Register #(.width(32)) _12 (.D(_12I), .en(WE), .Q(_12O), .clk(clk), .clr(reset));
  Register #(.width(32)) _20 (.D(_20I), .en(WE), .Q(_20O), .clk(clk), .clr(reset));
  Register #(.width(32)) _28 (.D(_28I), .en(WE), .Q(_28O), .clk(clk), .clr(reset));
  Register #(.width(32)) _5 (.D(_5I), .en(WE), .Q(_5O), .clk(clk), .clr(reset));
  Register #(.width(32)) _13 (.D(_13I), .en(WE), .Q(_13O), .clk(clk), .clr(reset));
  Register #(.width(32)) _21 (.D(_21I), .en(WE), .Q(_21O), .clk(clk), .clr(reset));
  Register #(.width(32)) _29 (.D(_29I), .en(WE), .Q(_29O), .clk(clk), .clr(reset));
  Multiplexer #(.select(5), .width(32)) multiplexer_2 (
    .in0(_0O), .in1(_1O), .in2(_2O), .in3(_3O), .in4(_4O), .in5(_5O), .in6(_6O), .in7(_7O), .in8(_8O),
    .in9(_9O), .in10(_10O), .in11(_11O), .in12(_12O), .in13(_13O), .in14(_14O), .in15(_15O), .in16(_16O),
    .in17(_17O), .in18(_18O), .in19(_19O), .in20(_20O), .in21(_21O), .in22(_22O), .in23(_23O), .in24(_24O),
    .in25(_25O), .in26(_26O), .in27(_27O), .in28(_28O), .in29(_29O), .in30(_30O), .in31(_31O), .out(RD2),
    .sel(A2));  // open: en
  Register #(.width(32)) _6 (.D(_6I), .en(WE), .Q(_6O), .clk(clk), .clr(reset));
  Register #(.width(32)) _7 (.D(_7I), .en(WE), .Q(_7O), .clk(clk), .clr(reset));
  Register #(.width(32)) _15 (.D(_15I), .en(WE), .Q(_15O), .clk(clk), .clr(reset));
  Register #(.width(32)) _14 (.D(_14I), .en(WE), .Q(_14O), .clk(clk), .clr(reset));
  Register #(.width(32)) _22 (.D(_22I), .en(WE), .Q(_22O), .clk(clk), .clr(reset));
  Register #(.width(32)) _23 (.D(_23I), .en(WE), .Q(_23O), .clk(clk), .clr(reset));
  Register #(.width(32)) _30 (.D(_30I), .en(WE), .Q(_30O), .clk(clk), .clr(reset));
  Register #(.width(32)) _31 (.D(_31I), .en(WE), .Q(_31O), .clk(clk), .clr(reset));
  Demultiplexer #(.select(5), .width(32), .tristate("true")) demultiplexer_1 (
    .out1(_1I), .out2(_2I), .out3(_3I), .out4(_4I), .out5(_5I), .out6(_6I), .out7(_7I), .out8(_8I),
    .out9(_9I), .out10(_10I), .out11(_11I), .out12(_12I), .out13(_13I), .out14(_14I), .out15(_15I),
    .out16(_16I), .out17(_17I), .out18(_18I), .out19(_19I), .out20(_20I), .out21(_21I), .out22(_22I),
    .out23(_23I), .out24(_24I), .out25(_25I), .out26(_26I), .out27(_27I), .out28(_28I), .out29(_29I),
    .out30(_30I), .out31(_31I), .in(WD), .sel(A3));  // open: out0, en

  // Notes on the sheet:
  //   RD1
  //   RD2
endmodule

module IFU (
  input  [31:0] PCN,
  input  CLK,
  input  reset,
  output [31:0] Instr,
  output [31:0] PC
);

  wire comparator_1_eq;
  wire [31:0] PC_q, subtractor_1_out;

  Register #(.width(32)) u_PC (.D(PCN), .Q(PC_q), .clk(CLK), .clr(reset));  // open: en
  Comparator #(.width(32), .mode("unsigned")) comparator_1 (
    .a(PC_q), .b({32{1'b0}}), .eq(comparator_1_eq));  // open: gt, lt
  Multiplexer #(.width(32)) multiplexer_1 (.in0(PC_q), .in1(32'h3000), .out(PC), .sel(comparator_1_eq));  // open: en
  Subtractor #(.width(32)) subtractor_1 (.a(PC), .b(32'h3000), .out(subtractor_1_out));  // open: bin, bout
  ROM #(.addrWidth(5), .dataWidth(32)) rom_1 (.addr(subtractor_1_out[6:2]), .data(Instr));  // open: sel
endmodule

module DM (
  input  [1:0] SelectBit,
  input  [31:0] A,
  input  [31:0] WD,
  input  WE,
  input  CLK,
  input  RESET,
  input  in_7,
  output [31:0] RD
);

  wire [31:0] OriData, sjudge_1_out;

  SJudge sjudge_1 (.Data(WD), .LOW(A[1:0]), .OUT(sjudge_1_out), .SelectBit(SelectBit), .OriData(OriData));
  RAM #(.addrWidth(12), .dataWidth(32), .bus("separate")) ram_1 (
    .addr(A[13:2]), .din(sjudge_1_out), .data(OriData), .str(WE), .clk(CLK), .clr(RESET));  // open: sel, ld
  LJudge ljudge_1 (.Data(OriData), .LOW(A[1:0]), .OUT(RD), .SelectBit(SelectBit), .DMExtendSign(in_7));

  // Other names for the same wires on the sheet: LOW[1:0] = A[1:0]; DMExtendSign = in_7
endmodule

module CPU (
  input  in_1,
  output [31:0] out_2,
  output [31:0] out_3,
  output out_4,
  output [4:0] out_5,
  output [31:0] out_6,
  output out_7,
  output [31:0] out_8,
  output halt,
  output [31:0] out_10
);

  wire alu_1_bigger, CLK, clock_2_out, clock_3_out, comparator_1_eq, control_1_branch, DMExtendSign,
       ExtendSign, FOP1, FOP2, FOP3, Jump, not_1_out, NPCControl, or_1_out, undriven;
  wire [1:0] MemToReg, RegDest, RegSrc, SelectBit;
  wire [3:0] ALUControl;
  wire [8:0] counter_1_q;
  wire [27:0] bit_extender_1_out, EPC;
  wire [31:0] dm_1_rd, ext_1_imm32, grf_1_rd1, multiplexer_2_out, npc_1_npc, PC;

  Clock clock_1 (.out(CLK));
  NPC npc_1 (.PC(PC), .SigImm(ext_1_imm32), .NPCControl(NPCControl), .NPC(npc_1_npc), .Jump(Jump), .EPC(EPC));
  IFU0 ifu0_1 (.PCN(npc_1_npc), .CLK(CLK), .reset(in_1), .Instr(out_2), .PC(PC));
  Multiplexer #(.select(2), .width(5)) multiplexer_1 (
    .in0(out_2[20:16]), .in1(out_2[15:11]), .out(out_5), .sel(RegDest));  // open: in2, in3, en
  EXT ext_1 (._16imm(out_2[15:0]), .imm32(ext_1_imm32), .ExtendSign(ExtendSign));
  GRF grf_1 (
    .clk(CLK), .reset(in_1), .WE(out_4), .WD(out_6), .RD1(grf_1_rd1), .RD2(out_10), .A1(out_2[25:21]),
    .A2(out_2[20:16]), .A3(out_5));
  assign bit_extender_1_out = {{2{1'b0}}, out_2[25:0]};  // Bit_Extender bit_extender_1
  Control control_1 (
    .Op(out_2[31:26]), .FC(out_2[5:0]), .ALUop(ALUControl), .Jump(Jump), .SelectBit(SelectBit),
    .Regwrite(out_4), .MemWrite(out_7), .MemtoReg(MemToReg), .RegDest(RegDest), .RegSrc(RegSrc),
    .Branch(control_1_branch), .ExtendSign(ExtendSign), .FOP1(FOP1), .FOP2(FOP2), .FOP3(FOP3),
    .DMExtendSign(DMExtendSign));
  Shifter #(.width(28)) shifter_1 (.in(bit_extender_1_out), .\dist (5'b00010), .out(EPC));
  // Probe on undriven
  Multiplexer #(.select(2), .width(32)) multiplexer_2 (
    .in0(out_10), .in1(ext_1_imm32), .out(multiplexer_2_out), .sel(RegSrc));  // open: in2, in3, en
  ALU alu_1 (.SrcA(grf_1_rd1), .SrcB(multiplexer_2_out), .ALUControl(ALUControl), .Res(out_8), .Bigger(alu_1_bigger));
  Clock clock_2 (.out(clock_2_out));
  and and_1 (NPCControl, control_1_branch, alu_1_bigger);
  DM dm_1 (
    .A(out_8), .WD(out_10), .RD(dm_1_rd), .CLK(CLK), .WE(out_7), .RESET(in_1), .SelectBit(SelectBit),
    .in_7(DMExtendSign));
  Counter #(.width(9), .max('h1ff), .ongoal("stay")) counter_1 (
    .D(9'h1), .Q(counter_1_q), .clk(clock_2_out), .clr(in_1));  // open: load, count, carry
  Comparator #(.width(9), .mode("unsigned")) comparator_1 (
    .a({9{1'b1}}), .b(counter_1_q), .eq(comparator_1_eq));  // open: gt, lt
  not not_1 (not_1_out, comparator_1_eq);
  Clock clock_3 (.out(clock_3_out));
  or or_1 (or_1_out, not_1_out, in_1);
  Multiplexer #(.select(2), .width(32)) multiplexer_3 (
    .in0(out_8), .in1(dm_1_rd), .out(out_6), .sel(MemToReg));  // open: in2, in3, en
  Counter #(.width(1), .max('h1), .ongoal("stay")) counter_2 (
    .D(1'b1), .Q(halt), .clk(clock_3_out), .clr(or_1_out));  // open: load, count, carry
  Adder #(.width(32)) adder_1 (.a(PC), .b(32'h3000), .out(out_3));  // open: cin, cout

  // Other names for the same wires on the sheet: ALURes[31:0] = out_8; MemAddr[4:0] = out_8[6:2]; Instr[31:0] = out_2;
  //   MemData[31:0] = out_10; MemWrite = out_7; RegAddr[4:0] = out_5; RegData[31:0] = out_6; Regwrite = out_4;
  //   RESET = in_1
endmodule

module ALU (
  input  [31:0] SrcA,
  input  [31:0] SrcB,
  input  [3:0] ALUControl,
  output [31:0] Res,
  output Bigger
);

  wire [31:0] adder_1_out, and_1_out, or_1_out, shifter_1_out, subtractor_1_out;

  Adder #(.width(32)) adder_1 (.a(SrcA), .b(SrcB), .out(adder_1_out));  // open: cin, cout
  Subtractor #(.width(32)) subtractor_1 (.a(SrcA), .b(SrcB), .out(subtractor_1_out));  // open: bin, bout
  assign and_1_out = SrcA & SrcB;  // AND_Gate and_1, 32 bits wide
  assign or_1_out = SrcA | SrcB;  // OR_Gate or_1, 32 bits wide
  Shifter #(.width(32)) shifter_1 (.in(SrcB), .\dist (5'b10000), .out(shifter_1_out));
  Comparator #(.width(32), .mode("unsigned")) comparator_1 (.a(SrcA), .b(SrcB), .eq(Bigger));  // open: gt, lt
  Multiplexer #(.select(4), .width(32)) multiplexer_1 (
    .in0(adder_1_out), .in1(subtractor_1_out), .in2(and_1_out), .in3(or_1_out), .in4(shifter_1_out),
    .out(Res), .sel(ALUControl));  // open: in5, in6, in7, in8, in9, in10, in11, in12, in13, in14, in15, en
endmodule

module NPC (
  input  [31:0] PC,
  input  [31:0] SigImm,
  input  [27:0] EPC,
  input  NPCControl,
  input  Jump,
  output [31:0] NPC
);

  wire [31:0] adder_1_out, adder_2_out, EPC_t, multiplexer_1_out, multiplier_1_out;

  Adder #(.width(32)) adder_1 (.a(PC), .b(32'h4), .out(adder_1_out));  // open: cin, cout
  Multiplier #(.width(32)) multiplier_1 (.a(SigImm), .b(32'h4), .out(multiplier_1_out));  // open: cin, cout
  Adder #(.width(32)) adder_2 (.a(adder_1_out), .b(multiplier_1_out), .out(adder_2_out));  // open: cin, cout
  Multiplexer #(.width(32)) multiplexer_1 (
    .in0(adder_1_out), .in1(adder_2_out), .out(multiplexer_1_out), .sel(NPCControl));  // open: en
  Multiplexer #(.width(32)) multiplexer_2 (.in0(multiplexer_1_out), .in1(EPC_t), .out(NPC), .sel(Jump));  // open: en
  Subtractor #(.width(32)) subtractor_1 (.a({adder_1_out[31:28], EPC}), .b(32'h3000), .out(EPC_t));  // open: bin, bout
endmodule

module Control (
  input  [5:0] Op,
  input  [5:0] FC,
  output [1:0] SelectBit,
  output [3:0] ALUop,
  output Regwrite,
  output [1:0] RegDest,
  output MemWrite,
  output [1:0] MemtoReg,
  output [1:0] RegSrc,
  output Branch,
  output Jump,
  output ExtendSign,
  output FOP1,
  output FOP2,
  output FOP3,
  output DMExtendSign
);

  wire ADD, ADDU, ALU1, BEQ, J, LUI, LW, not_1_out, not_2_out, not_3_out, not_4_out, not_5_out, not_6_out,
       not_7_out, not_8_out, not_9_out, not_10_out, not_11_out, not_12_out, ORI, SUB, SUBU, SW;

  not not_1 (not_1_out, Op[5]);
  not not_2 (not_2_out, Op[4]);
  not not_3 (not_3_out, Op[3]);
  not not_4 (not_4_out, Op[2]);
  not not_5 (not_5_out, Op[1]);
  not not_6 (not_6_out, Op[0]);
  and u_lW (LW, Op[5], not_2_out, not_3_out, not_4_out, Op[1], Op[0]);
  and u_SW (SW, Op[5], not_2_out, Op[3], not_4_out, Op[1], Op[0]);
  and ALU (ALU1, not_1_out, not_2_out, not_3_out, not_4_out, not_5_out, not_6_out);
  and u_ORI (ORI, not_1_out, not_2_out, Op[3], Op[2], not_5_out, Op[0]);
  and u_BEQ (BEQ, not_1_out, not_2_out, not_3_out, Op[2], not_5_out, not_6_out);
  and u_LUI (LUI, not_1_out, not_2_out, Op[3], Op[2], Op[1], Op[0]);
  and u_J (J, not_1_out, not_2_out, not_3_out, not_4_out, Op[1], not_6_out);
  not not_7 (not_7_out, FC[5]);
  not not_8 (not_8_out, FC[4]);
  not not_9 (not_9_out, FC[3]);
  not not_10 (not_10_out, FC[2]);
  not not_11 (not_11_out, FC[1]);
  not not_12 (not_12_out, FC[0]);
  and u_ADDU (ADDU, FC[5], not_8_out, not_9_out, ALU1, not_10_out, not_11_out, FC[0]);
  and u_SUBU (SUBU, FC[5], not_8_out, not_9_out, ALU1, not_10_out, FC[1], FC[0]);
  and u_ADD (ADD, ALU1, FC[5], not_8_out, not_9_out, not_10_out, not_11_out, not_12_out);
  and u_SUB (SUB, ALU1, FC[5], not_8_out, not_9_out, not_10_out, FC[1], not_12_out);
  buf or_1 (MemWrite, SW);  // OR_Gate
  or or_2 (ALUop[0], SUBU, ORI, SUB);
  buf or_3 (ALUop[1], ORI);  // OR_Gate
  buf or_4 (ALUop[2], LUI);  // OR_Gate
  buf or_5 (ALUop[3], 1'b0);  // OR_Gate
  buf or_6 (MemtoReg[0], LW);  // OR_Gate
  buf or_7 (MemtoReg[1], 1'b0);  // OR_Gate
  buf or_8 (Branch, BEQ);  // OR_Gate
  buf or_9 (Jump, J);  // OR_Gate
  buf or_10 (ExtendSign, ORI);  // OR_Gate
  // OR_Gate or_11 has open pins: out=FOP1
  // OR_Gate or_12 has open pins: out=FOP3
  buf or_13 (SelectBit[0], 1'b0);  // OR_Gate
  buf or_14 (SelectBit[1], 1'b0);  // OR_Gate
  // OR_Gate or_15 has open pins: out=FOP2
  buf or_16 (DMExtendSign, 1'b0);  // OR_Gate
  or or_17 (Regwrite, ADDU, SUBU, ADD, SUB, LW, LUI, ORI);
  or or_18 (RegDest[0], ADDU, SUBU, ADD, SUB);
  buf or_19 (RegDest[1], 1'b0);  // OR_Gate
  or or_20 (RegSrc[0], SW, LW, ORI, LUI);
  buf or_21 (RegSrc[1], 1'b0);  // OR_Gate

  // Notes on the sheet:
  //   ALU 功能选择
  //   0000 加
  //   0001 减
  //   0010 与
  //   0011 或
  //   0100 Lui专用
  //   DM写入信号
  //   选择提供给GRF的数据
  //   00为ALU
  //   01为DM
  //   B指令
  //   J指令
  //   扩展方式
  //   0符号扩展
  //   1无符号扩展
  //   00 16-20
  //   01 11-15
  //   00 GRF
  //   01 立即数
  //   字节数选择信号
  //   00 字读写
  //   01 字节读写
  //   10 半字读写
  //   GRF写入信号
  //   GRF A3 地址来源
  //   ALU第二操作数SrcB数据来源
endmodule

module main (
  input  in_1,
  output [31:0] out_2,
  output [31:0] out_3,
  output out_4,
  output [4:0] out_5,
  output [31:0] out_6,
  output out_7,
  output [4:0] out_8,
  output [31:0] out_9,
  output [31:0] out_10
);

  // CPU cpu_1: pin names not known; wires that end beside it: in_1, out_2, out_3, out_4, out_5, out_6, out_7, out_8, out_9, out_10
endmodule

module EXT (
  input  [15:0] _16imm,
  input  ExtendSign,
  output [31:0] imm32
);

  wire [31:0] bit_extender_1_out, bit_extender_2_out;

  assign bit_extender_1_out = {{16{_16imm[15]}}, _16imm};  // Bit_Extender bit_extender_1
  assign bit_extender_2_out = {{16{1'b0}}, _16imm};  // Bit_Extender bit_extender_2
  Multiplexer #(.width(32)) multiplexer_1 (
    .in0(bit_extender_1_out), .in1(bit_extender_2_out), .out(imm32), .sel(ExtendSign));  // open: en
endmodule

module IFU0 (
  input  [31:0] PCN,
  input  CLK,
  input  reset,
  output [31:0] Instr,
  output [31:0] PC
);

  Register #(.width(32)) u_PC (.D(PCN), .Q(PC), .clk(CLK), .clr(reset));  // open: en
  ROM #(.addrWidth(12), .dataWidth(32)) rom_1 (.addr(PC[13:2]), .data(Instr));  // open: sel

  // Notes on the sheet:
  //   contents of rom_1 (hex, n*v repeats v):
  //   34000014 34010048 34020084 34030064 34040084 34050060 34060084 34070068 34080074 34090090 340a0018
  //   340b0080 340c0074 340d0080 340e0094 340f0040 34100080 3411001c 34120008 34130004 3414005c 34150090
  //   34160010 3417004c 34180064 34190028 341a0010 341b004c 341c0090 341d002c 341e006c 341f0068 1ab6022
  //   3409020 631822 ac6e0040 c00007a 0 3c1a0024 0 2529022 ae4e0034 c000096 0 2cb6820 37bd822 af600028 0
  //   c0000b6 0 339c822 af27002c 18c6022 ad98004c 842022 8c890038 c0000df 0 a52822 aca70004 339c822
  //   af2f0000 1833020 c00010b 0 0 0 1ef7822 ade30080 c000130 0 a52822 8ca90054 2c61022 421022 8c570040
  //   c000158 4*0 c000178 0 0 3c1b0068 2165820 c0001a2 0 1084022 ad120018 3c1c0060 339c822 af260010
  //   c0001c4 0 8c3820 3c0c002c 116a822 c0001ed 0 3c0a005c 127c822 375d0054 c00020d 0 1ef7822 8dfe007c
  //   37290058 0 c00022b 0 2493022 0 3611001c c000249 0 3567009c 3c000050 3c130064 c000264 0 c00028e 0
  //   1c92020 34af0020 3c1c0060 33bd820 1d11020 1ce7022 adde004c 508020 a90822 339c822 8f320070 34550054
  //   2318822 ae2f0068 1ef7822 adfc005c 3c090038 39ce022 8f880004 0 3c130010 3c39820 1ad6822 adbc0020 0
  //   3e00008 0 1ad6822 8dae000c 23dd822 18c6022 ad930040 346a0058 3cf2022 308d820 421022 ac520018
  //   36d80040 11b40012
endmodule

module LJudge (
  input  [31:0] Data,
  input  [1:0] LOW,
  input  [1:0] SelectBit,
  input  DMExtendSign,
  output [31:0] OUT
);

  wire [31:0] bit_extender_1_out, bit_extender_2_out, bit_extender_3_out, bit_extender_4_out,
       bit_extender_5_out, bit_extender_6_out, bit_extender_7_out, bit_extender_8_out, bit_extender_9_out,
       bit_extender_10_out, bit_extender_11_out, bit_extender_12_out, multiplexer_1_out, multiplexer_2_out,
       multiplexer_3_out, multiplexer_4_out, multiplexer_5_out, multiplexer_6_out, multiplexer_7_out,
       multiplexer_8_out;

  assign bit_extender_1_out = {{24{Data[7]}}, Data[7:0]};  // Bit_Extender bit_extender_1
  assign bit_extender_2_out = {{24{1'b0}}, Data[7:0]};  // Bit_Extender bit_extender_2
  assign bit_extender_3_out = {{24{Data[15]}}, Data[15:8]};  // Bit_Extender bit_extender_3
  assign bit_extender_4_out = {{24{1'b0}}, Data[15:8]};  // Bit_Extender bit_extender_4
  assign bit_extender_5_out = {{24{Data[23]}}, Data[23:16]};  // Bit_Extender bit_extender_5
  assign bit_extender_6_out = {{24{1'b0}}, Data[23:16]};  // Bit_Extender bit_extender_6
  assign bit_extender_7_out = {{24{Data[31]}}, Data[31:24]};  // Bit_Extender bit_extender_7
  assign bit_extender_8_out = {{24{1'b0}}, Data[31:24]};  // Bit_Extender bit_extender_8
  assign bit_extender_9_out = {{16{Data[15]}}, Data[15:0]};  // Bit_Extender bit_extender_9
  assign bit_extender_10_out = {{16{1'b0}}, Data[15:0]};  // Bit_Extender bit_extender_10
  assign bit_extender_11_out = {{16{Data[31]}}, Data[31:16]};  // Bit_Extender bit_extender_11
  assign bit_extender_12_out = {{16{1'b0}}, Data[31:16]};  // Bit_Extender bit_extender_12
  Multiplexer #(.width(32)) multiplexer_1 (
    .in0(bit_extender_1_out), .in1(bit_extender_2_out), .out(multiplexer_1_out), .sel(DMExtendSign));  // open: en
  Multiplexer #(.width(32)) multiplexer_2 (
    .in0(bit_extender_3_out), .in1(bit_extender_4_out), .out(multiplexer_2_out), .sel(DMExtendSign));  // open: en
  Multiplexer #(.width(32)) multiplexer_3 (
    .in0(bit_extender_5_out), .in1(bit_extender_6_out), .out(multiplexer_3_out), .sel(DMExtendSign));  // open: en
  Multiplexer #(.width(32)) multiplexer_4 (
    .in0(bit_extender_7_out), .in1(bit_extender_8_out), .out(multiplexer_4_out), .sel(DMExtendSign));  // open: en
  Multiplexer #(.width(32)) multiplexer_5 (
    .in0(bit_extender_9_out), .in1(bit_extender_10_out), .out(multiplexer_5_out), .sel(DMExtendSign));  // open: en
  Multiplexer #(.width(32)) multiplexer_6 (
    .in0(bit_extender_11_out), .in1(bit_extender_12_out), .out(multiplexer_6_out), .sel(DMExtendSign));  // open: en
  Multiplexer #(.select(2), .width(32)) multiplexer_7 (
    .in0(multiplexer_1_out), .in1(multiplexer_2_out), .in2(multiplexer_3_out), .in3(multiplexer_4_out),
    .out(multiplexer_7_out), .sel(LOW));  // open: en
  Multiplexer #(.select(2), .width(32)) multiplexer_8 (
    .in0(multiplexer_5_out), .in2(multiplexer_6_out), .out(multiplexer_8_out), .sel(LOW));  // open: in1, in3, en
  Multiplexer #(.select(2), .width(32)) multiplexer_9 (
    .in0(Data), .in1(multiplexer_7_out), .in2(multiplexer_8_out), .out(OUT), .sel(SelectBit));  // open: in3, en

  // Other names for the same wires on the sheet: D[31:0] = Data

  // Notes on the sheet:
  //   0 符号扩展
  //   1 无符号扩展
  //   读取字节
  //   读取半字
endmodule

module SJudge (
  input  [31:0] OriData,
  input  [31:0] Data,
  input  [1:0] LOW,
  input  [1:0] SelectBit,
  output [31:0] OUT
);

  wire [31:0] multiplexer_1_out, multiplexer_2_out;

  Multiplexer #(.select(2), .width(32)) multiplexer_1 (
    .in0({OriData[31:8], Data[7:0]}), .in1({OriData[31:16], Data[15:8], OriData[7:0]}),
    .in2({OriData[31:24], Data[23:16], OriData[15:0]}), .in3({Data[31:24], OriData[23:0]}),
    .out(multiplexer_1_out), .sel(LOW));  // open: en
  Multiplexer #(.select(2), .width(32)) multiplexer_2 (
    .in0({OriData[31:16], Data[15:0]}), .in2({Data[15:0], OriData[15:0]}), .out(multiplexer_2_out), .sel(LOW));  // open: in1, in3, en
  Multiplexer #(.select(2), .width(32)) multiplexer_3 (
    .in0(Data), .in1(multiplexer_1_out), .in2(multiplexer_2_out), .out(OUT), .sel(SelectBit));  // open: in3, en

  // Other names for the same wires on the sheet: D[31:0] = Data; Ori07[7:0] = OriData[7:0];
  //   Ori815[7:0] = OriData[15:8]; Ori1623[7:0] = OriData[23:16]; Ori2431[7:0] = OriData[31:24]

  // Notes on the sheet:
  //   读取字节
  //   读取半字
endmodule
