// Logisim project myCpu.circ as structural Verilog: 9 circuits, main circuit main
module main (
  input  rst,
  output [31:0] Instr,
  output [31:0] out_3,
  output out_4,
  output [4:0] out_5,
  output [31:0] RegData,
  output out_7,
  output [31:0] ALURes,
  output [31:0] DMWD,
  output halt
);

  wire BSel, clock_1_out, clock_2_out, clock_3_out, comparator_1_eq, EXTOp, not_1_out, or_1_out, Zero;
  wire [1:0] WDSel, WRSel;
  wire [2:0] ALUOp, NPCOp;
  wire [8:0] counter_1_q;
  wire [31:0] ext_1_out_3, multiplexer_3_out, npc_1_npc, pc, PC4, RA, RD;

  Clock clock_1 (.out(clock_1_out));
  Register #(.width(32)) register_1 (.D(npc_1_npc), .Q(pc), .clk(clock_1_out), .clr(rst));  // open: en
  NPC npc_1 (.IMM(Instr[25:0]), .RA(RA), .NPC(npc_1_npc), .NPCOp(NPCOp), .PC(pc), .Zero(Zero), .rst(rst), .PC4(PC4));
  IM im_1 (.PC(pc), .out_2(Instr));
  CU cu_1 (
    .NPCOp(NPCOp), .opcode(Instr[31:26]), .funct(Instr[5:0]), .A3Sel(WRSel), .WDSel(WDSel), .DMWr(out_7),
    .ALUOp(ALUOp), .BSel(BSel), .EXTOp(EXTOp), .RFWr(out_4));
  Multiplexer #(.select(2), .width(5)) multiplexer_1 (
    .in0(Instr[20:16]), .in1(Instr[15:11]), .in2({5{1'b1}}), .out(out_5), .sel(WRSel));  // open: in3, en
  // Probe on WDSel
  Multiplexer #(.select(2), .width(32)) multiplexer_2 (
    .in0(ALURes), .in1(RD), .in2(PC4), .out(RegData), .sel(WDSel));  // open: in3, en
  EXT ext_1 (.IMM(Instr[15:0]), .EXTOp(EXTOp), .out_3(ext_1_out_3));
  RF rf_1 (
    .reset(rst), .A1(Instr[25:21]), .A2(Instr[20:16]), .A3(out_5), .WD(RegData), .RD1(RA), .RD2(DMWD),
    .WE(out_4));
  Multiplexer #(.width(32)) multiplexer_3 (
    .in0(DMWD), .in1(ext_1_out_3), .out(multiplexer_3_out), .sel(BSel));  // open: en
  ALU alu_1 (.A(RA), .B(multiplexer_3_out), .ALURes(ALURes), .ALUOp(ALUOp), .Zero(Zero));
  // Probe on ALURes
  Clock clock_2 (.out(clock_2_out));
  DM dm_1 (.A(ALURes), .WD(DMWD), .RD(RD), .DMWr(out_7), .rst(rst));  // open: DMOp
  Counter #(.width(9), .max('h1ff), .ongoal("stay")) counter_1 (
    .D(9'h1), .Q(counter_1_q), .clk(clock_2_out), .clr(rst));  // open: load, count, carry
  not not_1 (not_1_out, comparator_1_eq);
  Comparator #(.width(9), .mode("unsigned")) comparator_1 (
    .a({9{1'b1}}), .b(counter_1_q), .eq(comparator_1_eq));  // open: gt, lt
  Clock clock_3 (.out(clock_3_out));
  or or_1 (or_1_out, not_1_out, rst);
  Counter #(.width(1), .max('h1), .ongoal("stay")) counter_2 (
    .D(1'b1), .Q(halt), .clk(clock_3_out), .clr(or_1_out));  // open: load, count, carry
  Adder #(.width(32)) adder_1 (.a(32'h3000), .b(pc), .out(out_3));  // open: cin, cout

  // Other names for the same wires on the sheet: DMWr = out_7; IMM26[25:0] = Instr[25:0]; RegAddr[4:0] = out_5;
  //   RFWr = out_4; WD[31:0] = DMWD

  // Notes on the sheet:
  //   IMM
  //   opcode
  //   funct
  //   M1
endmodule

module NPC (
  input  [25:0] IMM,
  input  Zero,
  input  rst,
  input  [31:0] PC,
  input  [2:0] NPCOp,
  input  [31:0] RA,
  output [31:0] NPC,
  output [31:0] PC4
);

  wire [31:0] adder_2_out, bit_extender_1_out, multiplexer_1_out, shifter_1_out;

  Adder #(.width(32)) adder_1 (.a(32'h4), .b(PC), .out(PC4));  // open: cin, cout
  assign bit_extender_1_out = {{16{IMM[15]}}, IMM[15:0]};  // Bit_Extender bit_extender_1
  Shifter #(.width(32)) shifter_1 (.in(bit_extender_1_out), .\dist (5'b00010), .out(shifter_1_out));
  Adder #(.width(32)) adder_2 (.a(PC4), .b(shifter_1_out), .out(adder_2_out));  // open: cin, cout
  Multiplexer #(.width(32)) multiplexer_1 (
    .in0(PC4), .in1(adder_2_out), .out(multiplexer_1_out), .sel(Zero));  // open: en
  Multiplexer #(.select(3), .width(32)) multiplexer_2 (
    .in0(PC4), .in1(multiplexer_1_out), .in2({PC[31:28], IMM, 2'b00}), .in3(RA), .out(NPC), .sel(NPCOp));  // open: in4, in5, in6, in7, en

  // Notes on the sheet:
  //   PC+4
  //   BEQ
  //   JAL
  //   JR
endmodule

module IM (
  input  [31:0] PC,
  output [31:0] out_2
);

  ROM #(.addrWidth(12), .dataWidth(32)) rom_1 (.addr(PC[13:2]), .data(out_2));  // open: sel
endmodule

module PC (
  input  [31:0] IN,
  input  rst,
  output [31:0] out_3
);

  wire clock_1_out;
  wire [31:0] register_1_q, xor_1_out;

  assign xor_1_out = 32'h3000 ^ IN;  // XOR_Gate xor_1, 32 bits wide
  Clock clock_1 (.out(clock_1_out));
  Register #(.width(32)) register_1 (.D(xor_1_out), .Q(register_1_q), .clk(clock_1_out), .clr(rst));  // open: en
  assign out_3 = 32'h3000 ^ register_1_q;  // XOR_Gate xor_2, 32 bits wide
endmodule

module CU (
  input  [5:0] opcode,
  input  [5:0] funct,
  output DMWr,
  output [2:0] NPCOp,
  output [2:0] ALUOp,
  output BSel,
  output [1:0] A3Sel,
  output [1:0] WDSel,
  output EXTOp,
  output RFWr
);

  wire _00_2_out, _00_out, _01_2_out, _1_2_out, _1_3_out, _1_4_out, _01_out, _1_out, _10_2_out, _10_out, add,
       add_fun_out, add_op_out, ADD_out, beq, beq_2_out, jal, jal_out, jr_out, lui, lui_2_out, lw, not_1_out,
       not_2_out, not_3_out, not_4_out, not_5_out, not_6_out, not_7_out, not_8_out, not_9_out, not_10_out,
       not_11_out, not_12_out, OR_out, ori, sub, sub_fun_out, sub_op_out, SUB_out, sw;

  not not_1 (not_1_out, opcode[4]);
  not not_2 (not_2_out, opcode[5]);
  not not_3 (not_3_out, opcode[3]);
  or _00 (_00_out, ori, sub, add);
  buf _01 (_01_out, lw);  // OR_Gate
  buf _10 (_10_out, jal);  // OR_Gate
  buf _1 (_1_out, sw);  // OR_Gate
  or _1_2 (_1_2_out, sw, lw);
  not not_4 (not_4_out, opcode[2]);
  Comparator #(.width(1), .mode("unsigned")) comparator_1 (.a(_1_out), .b(1'b1), .eq(DMWr));  // open: gt, lt
  Comparator #(.width(1), .mode("unsigned")) comparator_2 (.a(_1_2_out), .b(1'b1), .eq(EXTOp));  // open: gt, lt
  not not_5 (not_5_out, opcode[0]);
  not not_6 (not_6_out, opcode[1]);
  Pull_Resistor pull_resistor_1 (.node(WDSel));
  Priority_Encoder #(.select(2)) priority_encoder_1 (
    .in0(_00_out), .in1(_01_out), .in2(_10_out), .out(WDSel));  // open: in3, gs, en_out, en_in
  not not_7 (not_7_out, funct[4]);
  not not_8 (not_8_out, funct[5]);
  not not_9 (not_9_out, funct[3]);
  or _00_2 (_00_2_out, ori, lw, lui);
  or _01_2 (_01_2_out, sub, add);
  buf _10_2 (_10_2_out, jal);  // OR_Gate
  or _1_3 (_1_3_out, add, sub, ori, lw, lui);
  or _1_4 (_1_4_out, ori, lw, sw, lui);
  not not_10 (not_10_out, funct[2]);
  Priority_Encoder #(.select(2)) priority_encoder_2 (
    .in0(_00_2_out), .in1(_01_2_out), .in2(_10_2_out), .out(A3Sel));  // open: in3, gs, en_out, en_in
  Pull_Resistor pull_resistor_2 (.node(A3Sel));
  Comparator #(.width(1), .mode("unsigned")) comparator_3 (.a(_1_3_out), .b(1'b1), .eq(RFWr));  // open: gt, lt
  Comparator #(.width(1), .mode("unsigned")) comparator_4 (.a(_1_4_out), .b(1'b1), .eq(BSel));  // open: gt, lt
  not not_11 (not_11_out, funct[1]);
  not not_12 (not_12_out, funct[0]);
  and add_op (add_op_out, not_2_out, not_1_out, not_3_out, not_4_out, not_6_out, not_5_out);
  and add_fun (add_fun_out, funct[5], not_7_out, not_9_out, not_10_out, not_11_out, not_12_out);
  and sub_op (sub_op_out, not_2_out, not_1_out, not_3_out, not_4_out, not_6_out, not_5_out);
  and sub_fun (sub_fun_out, funct[5], not_7_out, not_9_out, not_10_out, funct[1], not_12_out);
  and u_ori (ori, not_2_out, not_1_out, opcode[3], opcode[2], not_6_out, opcode[0]);
  and u_lw (lw, opcode[5], not_1_out, not_3_out, not_4_out, opcode[0], opcode[0]);
  and u_sw (sw, opcode[5], not_1_out, opcode[3], not_4_out, opcode[1], opcode[0]);
  and u_beq (beq, not_2_out, not_1_out, not_3_out, opcode[2], not_6_out, not_5_out);
  and u_lui (lui, not_2_out, not_1_out, opcode[3], opcode[2], opcode[1], opcode[0]);
  or u_ADD (ADD_out, add, lw, sw);
  or u_SUB (SUB_out, sub, beq);
  buf OR (OR_out, ori);  // OR_Gate
  buf lui_2 (lui_2_out, lui);  // OR_Gate
  and add_2 (add, add_op_out, add_fun_out);
  and sub_2 (sub, sub_op_out, sub_fun_out);
  Pull_Resistor pull_resistor_3 (.node(ALUOp));
  Priority_Encoder priority_encoder_3 (
    .in0(ADD_out), .in1(SUB_out), .in2(OR_out), .in3(lui_2_out), .out(ALUOp));  // open: in4, in5, in6, in7, en_in, gs, en_out
  buf beq_2 (beq_2_out, beq);  // OR_Gate
  buf u_jal (jal_out, jal);  // OR_Gate
  // OR_Gate jr has open pins: out=jr_out
  Priority_Encoder priority_encoder_4 (
    .in1(beq_2_out), .in2(jal_out), .in3(jr_out), .out(NPCOp));  // open: in0, in4, in5, in6, in7, en_in, gs, en_out
  Pull_Resistor pull_resistor_4 (.node(NPCOp));
endmodule

module RF (
  input  WE,
  input  reset,
  input  [4:0] A1,
  input  [4:0] A2,
  input  [4:0] A3,
  input  [31:0] WD,
  output [31:0] RD1,
  output [31:0] RD2
);

  wire CLK;
  wire [31:0] R0, R1, R2, R3, R4, R5, R6, R7, R8, R9, R10, R11, R12, R13, R14, R15, R16, R17, R18, R19, R20,
       R21, R22, R23, R24, R25, R26, R27, R28, R29, R30, R31, W0, W1, W2, W3, W4, W5, W6, W7, W8, W9, W10,
       W11, W12, W13, W14, W15, W16, W17, W18, W19, W20, W21, W22, W23, W24, W25, W26, W27, W28, W29, W30,
       W31;

  Clock clock_1 (.out(CLK));
  Register #(.width(32)) _0 (.D(W0), .en(WE), .Q(R0), .clk(CLK), .clr(1'b1));
  Register #(.width(32)) _4 (.D(W4), .en(WE), .Q(R4), .clk(CLK), .clr(reset));
  Register #(.width(32)) _8 (.D(W8), .en(WE), .Q(R8), .clk(CLK), .clr(reset));
  Register #(.width(32)) _12 (.D(W12), .en(WE), .Q(R12), .clk(CLK), .clr(reset));
  Demultiplexer #(.select(5), .width(32), .tristate("true")) demultiplexer_1 (
    .out1(W1), .out2(W2), .out3(W3), .out4(W4), .out5(W5), .out6(W6), .out7(W7), .out8(W8), .out9(W9),
    .out10(W10), .out11(W11), .out12(W12), .out13(W13), .out14(W14), .out15(W15), .out16(W16), .out17(W17),
    .out18(W18), .out19(W19), .out20(W20), .out21(W21), .out22(W22), .out23(W23), .out24(W24), .out25(W25),
    .out26(W26), .out27(W27), .out28(W28), .out29(W29), .out30(W30), .out31(W31), .in(WD), .sel(A3), .en(WE));  // open: out0
  Register #(.width(32)) _1 (.D(W1), .en(WE), .Q(R1), .clk(CLK), .clr(reset));
  Register #(.width(32)) _5 (.D(W5), .en(WE), .Q(R5), .clk(CLK), .clr(reset));
  Register #(.width(32)) _9 (.D(W9), .en(WE), .Q(R9), .clk(CLK), .clr(reset));
  Register #(.width(32)) _13 (.D(W13), .en(WE), .Q(R13), .clk(CLK), .clr(reset));
  Register #(.width(32)) _2 (.D(W2), .en(WE), .Q(R2), .clk(CLK), .clr(reset));
  Register #(.width(32)) _6 (.D(W6), .en(WE), .Q(R6), .clk(CLK), .clr(reset));
  Register #(.width(32)) _10 (.D(W10), .en(WE), .Q(R10), .clk(CLK), .clr(reset));
  Register #(.width(32)) _14 (.D(W14), .en(WE), .Q(R14), .clk(CLK), .clr(reset));
  Register #(.width(32)) _3 (.D(W3), .en(WE), .Q(R3), .clk(CLK), .clr(reset));
  Register #(.width(32)) _7 (.D(W7), .en(WE), .Q(R7), .clk(CLK), .clr(reset));
  Register #(.width(32)) _11 (.D(W11), .en(WE), .Q(R11), .clk(CLK), .clr(reset));
  Register #(.width(32)) _15 (.D(W15), .en(WE), .Q(R15), .clk(CLK), .clr(reset));
  Register #(.width(32)) _16 (.D(W16), .en(WE), .Q(R16), .clk(CLK), .clr(reset));
  Register #(.width(32)) _20 (.D(W20), .en(WE), .Q(R20), .clk(CLK), .clr(reset));
  Register #(.width(32)) _24 (.D(W24), .en(WE), .Q(R24), .clk(CLK), .clr(reset));
  Register #(.width(32)) _28 (.D(W28), .en(WE), .Q(R28), .clk(CLK), .clr(reset));
  Register #(.width(32)) _17 (.D(W17), .en(WE), .Q(R17), .clk(CLK), .clr(reset));
  Register #(.width(32)) _21 (.D(W21), .en(WE), .Q(R21), .clk(CLK), .clr(reset));
  Register #(.width(32)) _25 (.D(W25), .en(WE), .Q(R25), .clk(CLK), .clr(reset));
  Register #(.width(32)) _29 (.D(W29), .en(WE), .Q(R29), .clk(CLK), .clr(reset));
  Multiplexer #(.select(5), .width(32)) multiplexer_1 (
    .in0(R0), .in1(R1), .in2(R2), .in3(R3), .in4(R4), .in5(R5), .in6(R6), .in7(R7), .in8(R8), .in9(R9),
    .in10(R10), .in11(R11), .in12(R12), .in13(R13), .in14(R14), .in15(R15), .in16(R16), .in17(R17),
    .in18(R18), .in19(R19), .in20(R20), .in21(R21), .in22(R22), .in23(R23), .in24(R24), .in25(R25),
    .in26(R26), .in27(R27), .in28(R28), .in29(R29), .in30(R30), .in31(R31), .out(RD1), .sel(A1));  // open: en
  Register #(.width(32)) _18 (.D(W18), .en(WE), .Q(R18), .clk(CLK), .clr(reset));
  Register #(.width(32)) _22 (.D(W22), .en(WE), .Q(R22), .clk(CLK), .clr(reset));
  Register #(.width(32)) _26 (.D(W26), .en(WE), .Q(R26), .clk(CLK), .clr(reset));
  Register #(.width(32)) _30 (.D(W30), .en(WE), .Q(R30), .clk(CLK), .clr(reset));
  Register #(.width(32)) _19 (.D(W19), .en(WE), .Q(R19), .clk(CLK), .clr(reset));
  Register #(.width(32)) _23 (.D(W23), .en(WE), .Q(R23), .clk(CLK), .clr(reset));
  Register #(.width(32)) _27 (.D(W27), .en(WE), .Q(R27), .clk(CLK), .clr(reset));
  Register #(.width(32)) _31 (.D(W31), .en(WE), .Q(R31), .clk(CLK), .clr(reset));
  Multiplexer #(.select(5), .width(32)) multiplexer_2 (
    .in0(R0), .in1(R1), .in2(R2), .in3(R3), .in4(R4), .in5(R5), .in6(R6), .in7(R7), .in8(R8), .in9(R9),
    .in10(R10), .in11(R11), .in12(R12), .in13(R13), .in14(R14), .in15(R15), .in16(R16), .in17(R17),
    .in18(R18), .in19(R19), .in20(R20), .in21(R21), .in22(R22), .in23(R23), .in24(R24), .in25(R25),
    .in26(R26), .in27(R27), .in28(R28), .in29(R29), .in30(R30), .in31(R31), .out(RD2), .sel(A2));  // open: en

  // Other names for the same wires on the sheet: RST = reset
endmodule

module EXT (
  input  [15:0] IMM,
  input  EXTOp,
  output [31:0] out_3
);

  wire [31:0] bit_extender_1_out, bit_extender_2_out;

  assign bit_extender_1_out = {{16{1'b0}}, IMM};  // Bit_Extender bit_extender_1
  assign bit_extender_2_out = {{16{IMM[15]}}, IMM};  // Bit_Extender bit_extender_2
  Multiplexer #(.width(32)) multiplexer_1 (
    .in0(bit_extender_1_out), .in1(bit_extender_2_out), .out(out_3), .sel(EXTOp));  // open: en
endmodule

module ALU (
  input  [2:0] ALUOp,
  input  [31:0] A,
  input  [31:0] B,
  output Zero,
  output [31:0] ALURes
);

  wire [31:0] adder_1_out, OR_out, shifter_1_out, subRes;

  Adder #(.width(32)) adder_1 (.a(A), .b(B), .out(adder_1_out));  // open: cin, cout
  Subtractor #(.width(32)) subtractor_1 (.a(A), .b(B), .out(subRes));  // open: bin, bout
  assign OR_out = A | B;  // OR_Gate OR, 32 bits wide
  Shifter #(.width(32)) shifter_1 (.in(B), .\dist (5'b10000), .out(shifter_1_out));
  Comparator #(.width(32), .mode("unsigned")) comparator_1 (.a(subRes), .b({32{1'b0}}), .eq(Zero));  // open: gt, lt
  Multiplexer #(.select(3), .width(32)) multiplexer_1 (
    .in0(adder_1_out), .in1(subRes), .in2(OR_out), .in3(shifter_1_out), .out(ALURes), .sel(ALUOp));  // open: in4, in5, in6, in7, en

  // Notes on the sheet:
  //   lui
  //   isZero: if equal, 1; else 0;
endmodule

module DM (
  input  DMWr,
  input  rst,
  input  [1:0] DMOp,
  input  [31:0] A,
  input  [31:0] WD,
  output [31:0] RD
);

  wire clock_1_out, not_1_out;
  wire [31:0] write;

  Multiplexer #(.select(2), .width(32)) multiplexer_1 (.in0(WD), .out(write), .sel(2'b00));  // open: in1, in2, in3, en
  not not_1 (not_1_out, DMWr);
  Clock clock_1 (.out(clock_1_out));
  RAM #(.addrWidth(12), .dataWidth(32), .bus("separate")) ram_1 (
    .addr(A[13:2]), .din(write), .data(RD), .str(DMWr), .clk(clock_1_out), .ld(not_1_out), .clr(rst));  // open: sel

  // Other names for the same wires on the sheet: Addr[31:0] = A; Reset = rst
endmodule
