// Logisim project myCpu_m.circ as structural Verilog: 9 circuits, main circuit main
module main (
  input  rst,
  output [31:0] Instr,
  output [31:0] out_3,
  output out_4,
  output [4:0] out_5,
  output [31:0] RegData,
  output out_7,
  output [31:0] ALURes,
  output [31:0] DMWD,
  output halt
);

  wire BSel, clock_1_out, clock_2_out, clock_3_out, comparator_1_eq, EXTOp, not_1_out, or_1_out, Zero;
  wire [1:0] WDSel, WRSel;
  wire [2:0] ALUOp, NPCOp;
  wire [8:0] counter_1_q;
  wire [31:0] ext_1_out_3, multiplexer_3_out, npc_1_npc, pc, PC4, RA, RD;

  Clock clock_1 (.out(clock_1_out));
  Register #(.width(32)) register_1 (.D(npc_1_npc), .Q(pc), .clk(clock_1_out), .clr(rst));  // open: en
  NPC npc_1 (.IMM(Instr[25:0]), .RA(RA), .NPC(npc_1_npc), .NPCOp(NPCOp), .PC(pc), .Zero(Zero), .rst(rst), .PC4(PC4));
  IM im_1 (.PC(pc), .out_2(Instr));
  CU cu_1 (
    .NPCOp(NPCOp), .opcode(Instr[31:26]), .funct(Instr[5:0]), .A3Sel(WRSel), .WDSel(WDSel), .DMWr(out_7),
    .ALUOp(ALUOp), .BSel(BSel), .EXTOp(EXTOp), .RFWr(out_4));
  Multiplexer #(.select(2), .width(5)) multiplexer_1 (
    .in0(Instr[20:16]), .in1(Instr[15:11]), .in2({5{1'b1}}), .out(out_5), .sel(WRSel));  // open: in3, en
  // Probe on WDSel
  Multiplexer #(.select(2), .width(32)) multiplexer_2 (
    .in0(ALURes), .in1(RD), .in2(PC4), .out(RegData), .sel(WDSel));  // open: in3, en
  EXT ext_1 (.IMM(Instr[15:0]), .EXTOp(EXTOp), .out_3(ext_1_out_3));
  RF rf_1 (
    .reset(rst), .A1(Instr[25:21]), .A2(Instr[20:16]), .A3(out_5), .WD(RegData), .RD1(RA), .RD2(DMWD),
    .WE(out_4));
  Multiplexer #(.width(32)) multiplexer_3 (
    .in0(DMWD), .in1(ext_1_out_3), .out(multiplexer_3_out), .sel(BSel));  // open: en
  ALU alu_1 (.A(RA), .B(multiplexer_3_out), .ALURes(ALURes), .ALUOp(ALUOp), .Zero(Zero));
  // Probe on ALURes
  Clock clock_2 (.out(clock_2_out));
  DM dm_1 (.A(ALURes), .WD(DMWD), .RD(RD), .DMWr(out_7), .rst(rst));  // open: DMOp
  Counter #(.width(9), .max('h1ff), .ongoal("stay")) counter_1 (
    .D(9'h1), .Q(counter_1_q), .clk(clock_2_out), .clr(rst));  // open: load, count, carry
  not not_1 (not_1_out, comparator_1_eq);
  Comparator #(.width(9), .mode("unsigned")) comparator_1 (
    .a({9{1'b1}}), .b(counter_1_q), .eq(comparator_1_eq));  // open: gt, lt
  Clock clock_3 (.out(clock_3_out));
  or or_1 (or_1_out, not_1_out, rst);
  Counter #(.width(1), .max('h1), .ongoal("stay")) counter_2 (
    .D(1'b1), .Q(halt), .clk(clock_3_out), .clr(or_1_out));  // open: load, count, carry
  Adder #(.width(32)) adder_1 (.a(32'h3000), .b(pc), .out(out_3));  // open: cin, cout

  // Other names for the same wires on the sheet: DMWr = out_7; IMM26[25:0] = Instr[25:0]; RegAddr[4:0] = out_5;
  //   RFWr = out_4; WD[31:0] = DMWD

  // Notes on the sheet:
  //   IMM
  //   opcode
  //   funct
  //   M1
endmodule

module NPC (
  input  [25:0] IMM,
  input  Zero,
  input  rst,
  input  [31:0] PC,
  input  [2:0] NPCOp,
  input  [31:0] RA,
  output [31:0] NPC,
  output [31:0] PC4
);

  wire [31:0] adder_2_out, bit_extender_1_out, multiplexer_1_out, shifter_1_out;

  Adder #(.width(32)) adder_1 (.a(32'h4), .b(PC), .out(PC4));  // open: cin, cout
  assign bit_extender_1_out = {{16{IMM[15]}}, IMM[15:0]};  // Bit_Extender bit_extender_1
  Shifter #(.width(32)) shifter_1 (.in(bit_extender_1_out), .\dist (5'b00010), .out(shifter_1_out));
  Adder #(.width(32)) adder_2 (.a(PC4), .b(shifter_1_out), .out(adder_2_out));  // open: cin, cout
  Multiplexer #(.width(32)) multiplexer_1 (
    .in0(PC4), .in1(adder_2_out), .out(multiplexer_1_out), .sel(Zero));  // open: en
  Multiplexer #(.select(3), .width(32)) multiplexer_2 (
    .in0(PC4), .in1(multiplexer_1_out), .in2({PC[31:28], IMM, 2'b00}), .in3(RA), .out(NPC), .sel(NPCOp));  // open: in4, in5, in6, in7, en

  // Notes on the sheet:
  //   PC+4
  //   BEQ
  //   JAL
  //   JR
endmodule

module IM (
  input  [31:0] PC,
  output [31:0] out_2
);

  ROM #(.addrWidth(12), .dataWidth(32)) rom_1 (.addr(PC[13:2]), .data(out_2));  // open: sel

  // Notes on the sheet:
  //   contents of rom_1 (hex, n*v repeats v):
  //   34010004 3402000b 34030009 34040009 34050003 34060009 34070003 34080003 34090009 340a0003 340b0006
  //   340c0007 340d0005 340e0004 340f000a 3410000b 34110003 3412000c 3413000c 34140008 34150004 34160009
  //   34170005 3418000a 34190004 341a0004 341b000a 341c0007 341d0006 341e000b 02121822 3c10007c 8f940060
  //   01967822 af0e0014 3c130038 acfa0044 00000000 36890098 0035f820 03390822 35df0139 00154820 afaa0000
  //   03d72820 00000000 af1a0058 8f560050 00000000 03403020 00000000 00000000 00000000 00000000 3c0b0098
  //   00000000 3c0d0038 8f840008 00000000 000a5820 36ec00b8 00000000 3c0d00a0 014f4022 00000000 ac26006c
  //   00000000 00000000 0041b022 35860003 03656822 37d300c7 009ea822 00000000 02bf2822 132afff2 00000000
  //   1176ffe3 00000000 02cb7820 aff2002c 00000000 afdf000c ae8b0024 026bc820 03038820 8cd20084 8dda0074
  //   ae520010 00000000 acc40034 03176022 37d9006f 00000000 ad0b0080 34d2019e 00000000 1382ffcf 00000000
  //   8f250050 1273ffcc 00000000 00fcc022 8cf20010 03ed9020 03bde022 0170f022 ac620058 03f87822 aefd0084
  //   1067ffe3 00000000 025a6822 0326f020 8e06008c 00000000 00000000 0377c022 3c160020 11b9ffda 00000000
  //   0137f022 3c010054 36110014 02acb822 3c180050 ac890060 34b7003c 001e8022 8e180030 01e5a820 347b016f
  //   8e9e0008 8c230020 371100c5 3463017f 37fc00a5 0320f822 8c72002c 01ea4820 00000000 02cfb822 1224ffa7
  //   00000000 ad290070 03cfe020 8c760014 03a18020 1149ffbd 00000000 378400a8 11a8ff99 00000000 106bffb8
  //   00000000 00a4e020 34910193 10c2ffa0 00000000 3c110008 352d01a9 8dcc0080 35dd0052 03917022 ae1d0028
  //   ad140034 ae0b0040 11d6ffaa 00000000 8ff8009c 018ad020 3c0a003c 139cff84 00000000 8fab0008 ad8f0020
  //   00000000 8f880008 00000000 00a38022 36610091 aeb8000c af1b0080 0311d822 8f220040 36e500d7 01563822
  //   8f230000 00a12820 02a3a822 3c180008 00000000 3c0e0058 00e62820 00000000 37b1002a 02641020 3c1d0050
  //   021a1822 37f600f3 349b0020 0080f020 3c1c002c 3c1d0020 ae9d0098 36650198 126bff6f 00000000 372a00cc
  //   00000000 1123ff86 00000000 ad230010 03a0e022 3508012c 13b5ff66 00000000 00000000 adc8007c ac6f0060
  //   123aff61 00000000 13f9ff52 00000000 3c15003c 00000000 01308820 34900016 122fff59 00000000 11e5ff4f
  //   00000000 018e6020 00000000 3c1c0038 02a1c820 1217fff6 00000000 352d003d 3c190008 00000000 afd90004
  //   359a011a ad4d007c 00000000 00f49020 00000000 0026a022 01b49020 01010822 007d6820 8ec20078 37d3013f
  //   00778020 00000000 011fd022 1029ffe7 00000000 1222ffb3 00000000 12edffde 00000000 1334ff4b 00000000
  //   3c02008c 36730132 3c160038 122eff2a 00000000 0219c022 3c0a0080 3c060050 37fd009d 02fd5022 0011d820
  //   8c3a002c 8ca5001c acf70014 8d260030 af60006c 36f80080 353800fd 01df9820 02352820 aff20078 8fb900a0
  //   02ba2022 ad960058 131bffc2 00000000 8f1e009c 03dcd020 1355ff19 00000000 acf70004 afb4008c 1348ff29
  //   00000000 022d1020 00000000 0301d022 8db10078 00e7d020 3c0e0010 01c05822 8d530088 aefe0038 3c12005c
  //   01676820 ad880044 3478003b 02a55022 1395ffaf 00000000 35ff00b3 348101ad 3412018c 007b7022 3c140048
  //   ad580040 35c201ab 8e8b0074 029bd022 3c1a0048 00000000 00000000 00000000 ae650044 3c070034 34b800c3
  //   8fea0044 3c1a002c 1035fef1 00000000 36bd014a 025c5022 8cf30080 8ce80060 8f5c0034 02144820 00d42020
  //   00000000 00000000 3c1a0070 af710084 0336f020 01d2a822 00000000 3c08006c 109cfee0 00000000 00000000
  //   ad21003c 359a007f 35d50181 00b77020 023cf022 ad67004c 12f6fed7 00000000 3c1e0024 007b4022 0056e820
  //   ad07003c 00000000 8d320088 1394ff79 00000000 8ebb0008 125ffec4 00000000 3c050044 00000000 1334febb
  //   00000000 00000000 8e590030 00000000 8eea0034 8f4b0070 00000000 00000000 01c91022 00000000 3c15009c
  //   3c0d0060 8e4b002c 01cb7022 028fd822 374a0097 acad0024 35810119 00000000 0083d022 8ec80068 007f1022
  //   02258820 008b6820 00871020 00000000 023c7022 34390150 3c140004 016ab020 af0f0020 136cff52 00000000
  //   00e2d022 0136d822 8f790028 8c8f0004 379100b3 3c0c0018 13a2ffd3 00000000 ac150044 3c0900a0 00000000
  //   00c84022 00000000 00000000 3c05006c 00000000 00000000 8f55003c 0057a022 34f2009e 00000000 3c060010
  //   00000000 afaa004c 01fed820 3c010090 ae23008c 1249ffac 00000000 36bc0127 8da40048 024a2820 11e5ff77
  //   00000000 35120113 3c1b0098 00000000 0208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
endmodule

module PC (
  input  [31:0] IN,
  input  rst,
  output [31:0] out_3
);

  wire clock_1_out;
  wire [31:0] register_1_q, xor_1_out;

  assign xor_1_out = 32'h3000 ^ IN;  // XOR_Gate xor_1, 32 bits wide
  Clock clock_1 (.out(clock_1_out));
  Register #(.width(32)) register_1 (.D(xor_1_out), .Q(register_1_q), .clk(clock_1_out), .clr(rst));  // open: en
  assign out_3 = 32'h3000 ^ register_1_q;  // XOR_Gate xor_2, 32 bits wide
endmodule

module CU (
  input  [5:0] opcode,
  input  [5:0] funct,
  output DMWr,
  output [2:0] NPCOp,
  output [2:0] ALUOp,
  output BSel,
  output [1:0] A3Sel,
  output [1:0] WDSel,
  output EXTOp,
  output RFWr
);

  wire _00_2_out, _00_out, _01_2_out, _1_2_out, _1_3_out, _1_4_out, _01_out, _1_out, _10_2_out, _10_out, add,
       add_fun_out, add_op_out, ADD_out, beq, beq_2_out, jal, jal_out, jr_out, lui, lui_2_out, lw, not_1_out,
       not_2_out, not_3_out, not_4_out, not_5_out, not_6_out, not_7_out, not_8_out, not_9_out, not_10_out,
       not_11_out, not_12_out, OR_out, ori, sub, sub_fun_out, sub_op_out, SUB_out, sw;

  not not_1 (not_1_out, opcode[4]);
  not not_2 (not_2_out, opcode[5]);
  not not_3 (not_3_out, opcode[3]);
  or _00 (_00_out, ori, sub, add);
  buf _01 (_01_out, lw);  // OR_Gate
  buf _10 (_10_out, jal);  // OR_Gate
  buf _1 (_1_out, sw);  // OR_Gate
  or _1_2 (_1_2_out, sw, lw);
  not not_4 (not_4_out, opcode[2]);
  Comparator #(.width(1), .mode("unsigned")) comparator_1 (.a(_1_out), .b(1'b1), .eq(DMWr));  // open: gt, lt
  Comparator #(.width(1), .mode("unsigned")) comparator_2 (.a(_1_2_out), .b(1'b1), .eq(EXTOp));  // open: gt, lt
  not not_5 (not_5_out, opcode[0]);
  not not_6 (not_6_out, opcode[1]);
  Pull_Resistor pull_resistor_1 (.node(WDSel));
  Priority_Encoder #(.select(2)) priority_encoder_1 (
    .in0(_00_out), .in1(_01_out), .in2(_10_out), .out(WDSel));  // open: in3, gs, en_out, en_in
  not not_7 (not_7_out, funct[4]);
  not not_8 (not_8_out, funct[5]);
  not not_9 (not_9_out, funct[3]);
  or _00_2 (_00_2_out, ori, lw, lui);
  or _01_2 (_01_2_out, sub, add);
  buf _10_2 (_10_2_out, jal);  // OR_Gate
  or _1_3 (_1_3_out, add, sub, ori, lw, lui);
  or _1_4 (_1_4_out, ori, lw, sw, lui);
  not not_10 (not_10_out, funct[2]);
  Priority_Encoder #(.select(2)) priority_encoder_2 (
    .in0(_00_2_out), .in1(_01_2_out), .in2(_10_2_out), .out(A3Sel));  // open: in3, gs, en_out, en_in
  Pull_Resistor pull_resistor_2 (.node(A3Sel));
  Comparator #(.width(1), .mode("unsigned")) comparator_3 (.a(_1_3_out), .b(1'b1), .eq(RFWr));  // open: gt, lt
  Comparator #(.width(1), .mode("unsigned")) comparator_4 (.a(_1_4_out), .b(1'b1), .eq(BSel));  // open: gt, lt
  not not_11 (not_11_out, funct[1]);
  not not_12 (not_12_out, funct[0]);
  and add_op (add_op_out, not_2_out, not_1_out, not_3_out, not_4_out, not_6_out, not_5_out);
  and add_fun (add_fun_out, funct[5], not_7_out, not_9_out, not_10_out, not_11_out, not_12_out);
  and sub_op (sub_op_out, not_2_out, not_1_out, not_3_out, not_4_out, not_6_out, not_5_out);
  and sub_fun (sub_fun_out, funct[5], not_7_out, not_9_out, not_10_out, funct[1], not_12_out);
  and u_ori (ori, not_2_out, not_1_out, opcode[3], opcode[2], not_6_out, opcode[0]);
  and u_lw (lw, opcode[5], not_1_out, not_3_out, not_4_out, opcode[0], opcode[0]);
  and u_sw (sw, opcode[5], not_1_out, opcode[3], not_4_out, opcode[1], opcode[0]);
  and u_beq (beq, not_2_out, not_1_out, not_3_out, opcode[2], not_6_out, not_5_out);
  and u_lui (lui, not_2_out, not_1_out, opcode[3], opcode[2], opcode[1], opcode[0]);
  or u_ADD (ADD_out, add, lw, sw);
  or u_SUB (SUB_out, sub, beq);
  buf OR (OR_out, ori);  // OR_Gate
  buf lui_2 (lui_2_out, lui);  // OR_Gate
  and add_2 (add, add_op_out, add_fun_out);
  and sub_2 (sub, sub_op_out, sub_fun_out);
  Pull_Resistor pull_resistor_3 (.node(ALUOp));
  Priority_Encoder priority_encoder_3 (
    .in0(ADD_out), .in1(SUB_out), .in2(OR_out), .in3(lui_2_out), .out(ALUOp));  // open: in4, in5, in6, in7, en_in, gs, en_out
  buf beq_2 (beq_2_out, beq);  // OR_Gate
  buf u_jal (jal_out, jal);  // OR_Gate
  // OR_Gate jr has open pins: out=jr_out
  Priority_Encoder priority_encoder_4 (
    .in1(beq_2_out), .in2(jal_out), .in3(jr_out), .out(NPCOp));  // open: in0, in4, in5, in6, in7, en_in, gs, en_out
  Pull_Resistor pull_resistor_4 (.node(NPCOp));
endmodule

module RF (
  input  WE,
  input  reset,
  input  [4:0] A1,
  input  [4:0] A2,
  input  [4:0] A3,
  input  [31:0] WD,
  output [31:0] RD1,
  output [31:0] RD2
);

  wire CLK;
  wire [31:0] R0, R1, R2, R3, R4, R5, R6, R7, R8, R9, R10, R11, R12, R13, R14, R15, R16, R17, R18, R19, R20,
       R21, R22, R23, R24, R25, R26, R27, R28, R29, R30, R31, W0, W1, W2, W3, W4, W5, W6, W7, W8, W9, W10,
       W11, W12, W13, W14, W15, W16, W17, W18, W19, W20, W21, W22, W23, W24, W25, W26, W27, W28, W29, W30,
       W31;

  Clock clock_1 (.out(CLK));
  Register #(.width(32)) _0 (.D(W0), .en(WE), .Q(R0), .clk(CLK), .clr(1'b1));
  Register #(.width(32)) _4 (.D(W4), .en(WE), .Q(R4), .clk(CLK), .clr(reset));
  Register #(.width(32)) _8 (.D(W8), .en(WE), .Q(R8), .clk(CLK), .clr(reset));
  Register #(.width(32)) _12 (.D(W12), .en(WE), .Q(R12), .clk(CLK), .clr(reset));
  Demultiplexer #(.select(5), .width(32), .tristate("true")) demultiplexer_1 (
    .out1(W1), .out2(W2), .out3(W3), .out4(W4), .out5(W5), .out6(W6), .out7(W7), .out8(W8), .out9(W9),
    .out10(W10), .out11(W11), .out12(W12), .out13(W13), .out14(W14), .out15(W15), .out16(W16), .out17(W17),
    .out18(W18), .out19(W19), .out20(W20), .out21(W21), .out22(W22), .out23(W23), .out24(W24), .out25(W25),
    .out26(W26), .out27(W27), .out28(W28), .out29(W29), .out30(W30), .out31(W31), .in(WD), .sel(A3), .en(WE));  // open: out0
  Register #(.width(32)) _1 (.D(W1), .en(WE), .Q(R1), .clk(CLK), .clr(reset));
  Register #(.width(32)) _5 (.D(W5), .en(WE), .Q(R5), .clk(CLK), .clr(reset));
  Register #(.width(32)) _9 (.D(W9), .en(WE), .Q(R9), .clk(CLK), .clr(reset));
  Register #(.width(32)) _13 (.D(W13), .en(WE), .Q(R13), .clk(CLK), .clr(reset));
  Register #(.width(32)) _2 (.D(W2), .en(WE), .Q(R2), .clk(CLK), .clr(reset));
  Register #(.width(32)) _6 (.D(W6), .en(WE), .Q(R6), .clk(CLK), .clr(reset));
  Register #(.width(32)) _10 (.D(W10), .en(WE), .Q(R10), .clk(CLK), .clr(reset));
  Register #(.width(32)) _14 (.D(W14), .en(WE), .Q(R14), .clk(CLK), .clr(reset));
  Register #(.width(32)) _3 (.D(W3), .en(WE), .Q(R3), .clk(CLK), .clr(reset));
  Register #(.width(32)) _7 (.D(W7), .en(WE), .Q(R7), .clk(CLK), .clr(reset));
  Register #(.width(32)) _11 (.D(W11), .en(WE), .Q(R11), .clk(CLK), .clr(reset));
  Register #(.width(32)) _15 (.D(W15), .en(WE), .Q(R15), .clk(CLK), .clr(reset));
  Register #(.width(32)) _16 (.D(W16), .en(WE), .Q(R16), .clk(CLK), .clr(reset));
  Register #(.width(32)) _20 (.D(W20), .en(WE), .Q(R20), .clk(CLK), .clr(reset));
  Register #(.width(32)) _24 (.D(W24), .en(WE), .Q(R24), .clk(CLK), .clr(reset));
  Register #(.width(32)) _28 (.D(W28), .en(WE), .Q(R28), .clk(CLK), .clr(reset));
  Register #(.width(32)) _17 (.D(W17), .en(WE), .Q(R17), .clk(CLK), .clr(reset));
  Register #(.width(32)) _21 (.D(W21), .en(WE), .Q(R21), .clk(CLK), .clr(reset));
  Register #(.width(32)) _25 (.D(W25), .en(WE), .Q(R25), .clk(CLK), .clr(reset));
  Register #(.width(32)) _29 (.D(W29), .en(WE), .Q(R29), .clk(CLK), .clr(reset));
  Multiplexer #(.select(5), .width(32)) multiplexer_1 (
    .in0(R0), .in1(R1), .in2(R2), .in3(R3), .in4(R4), .in5(R5), .in6(R6), .in7(R7), .in8(R8), .in9(R9),
    .in10(R10), .in11(R11), .in12(R12), .in13(R13), .in14(R14), .in15(R15), .in16(R16), .in17(R17),
    .in18(R18), .in19(R19), .in20(R20), .in21(R21), .in22(R22), .in23(R23), .in24(R24), .in25(R25),
    .in26(R26), .in27(R27), .in28(R28), .in29(R29), .in30(R30), .in31(R31), .out(RD1), .sel(A1));  // open: en
  Register #(.width(32)) _18 (.D(W18), .en(WE), .Q(R18), .clk(CLK), .clr(reset));
  Register #(.width(32)) _22 (.D(W22), .en(WE), .Q(R22), .clk(CLK), .clr(reset));
  Register #(.width(32)) _26 (.D(W26), .en(WE), .Q(R26), .clk(CLK), .clr(reset));
  Register #(.width(32)) _30 (.D(W30), .en(WE), .Q(R30), .clk(CLK), .clr(reset));
  Register #(.width(32)) _19 (.D(W19), .en(WE), .Q(R19), .clk(CLK), .clr(reset));
  Register #(.width(32)) _23 (.D(W23), .en(WE), .Q(R23), .clk(CLK), .clr(reset));
  Register #(.width(32)) _27 (.D(W27), .en(WE), .Q(R27), .clk(CLK), .clr(reset));
  Register #(.width(32)) _31 (.D(W31), .en(WE), .Q(R31), .clk(CLK), .clr(reset));
  Multiplexer #(.select(5), .width(32)) multiplexer_2 (
    .in0(R0), .in1(R1), .in2(R2), .in3(R3), .in4(R4), .in5(R5), .in6(R6), .in7(R7), .in8(R8), .in9(R9),
    .in10(R10), .in11(R11), .in12(R12), .in13(R13), .in14(R14), .in15(R15), .in16(R16), .in17(R17),
    .in18(R18), .in19(R19), .in20(R20), .in21(R21), .in22(R22), .in23(R23), .in24(R24), .in25(R25),
    .in26(R26), .in27(R27), .in28(R28), .in29(R29), .in30(R30), .in31(R31), .out(RD2), .sel(A2));  // open: en

  // Other names for the same wires on the sheet: RST = reset
endmodule

module EXT (
  input  [15:0] IMM,
  input  EXTOp,
  output [31:0] out_3
);

  wire [31:0] bit_extender_1_out, bit_extender_2_out;

  assign bit_extender_1_out = {{16{1'b0}}, IMM};  // Bit_Extender bit_extender_1
  assign bit_extender_2_out = {{16{IMM[15]}}, IMM};  // Bit_Extender bit_extender_2
  Multiplexer #(.width(32)) multiplexer_1 (
    .in0(bit_extender_1_out), .in1(bit_extender_2_out), .out(out_3), .sel(EXTOp));  // open: en
endmodule

module ALU (
  input  [2:0] ALUOp,
  input  [31:0] A,
  input  [31:0] B,
  output Zero,
  output [31:0] ALURes
);

  wire [31:0] adder_1_out, OR_out, shifter_1_out, subRes;

  Adder #(.width(32)) adder_1 (.a(A), .b(B), .out(adder_1_out));  // open: cin, cout
  Subtractor #(.width(32)) subtractor_1 (.a(A), .b(B), .out(subRes));  // open: bin, bout
  assign OR_out = A | B;  // OR_Gate OR, 32 bits wide
  Shifter #(.width(32)) shifter_1 (.in(B), .\dist (5'b10000), .out(shifter_1_out));
  Comparator #(.width(32), .mode("unsigned")) comparator_1 (.a(subRes), .b({32{1'b0}}), .eq(Zero));  // open: gt, lt
  Multiplexer #(.select(3), .width(32)) multiplexer_1 (
    .in0(adder_1_out), .in1(subRes), .in2(OR_out), .in3(shifter_1_out), .out(ALURes), .sel(ALUOp));  // open: in4, in5, in6, in7, en

  // Notes on the sheet:
  //   lui
  //   isZero: if equal, 1; else 0;
endmodule

module DM (
  input  DMWr,
  input  rst,
  input  [1:0] DMOp,
  input  [31:0] A,
  input  [31:0] WD,
  output [31:0] RD
);

  wire clock_1_out, not_1_out;
  wire [31:0] write;

  Multiplexer #(.select(2), .width(32)) multiplexer_1 (.in0(WD), .out(write), .sel(2'b00));  // open: in1, in2, in3, en
  not not_1 (not_1_out, DMWr);
  Clock clock_1 (.out(clock_1_out));
  RAM #(.addrWidth(12), .dataWidth(32), .bus("separate")) ram_1 (
    .addr(A[13:2]), .din(write), .data(RD), .str(DMWr), .clk(clock_1_out), .ld(not_1_out), .clr(rst));  // open: sel

  // Other names for the same wires on the sheet: Addr[31:0] = A; Reset = rst
endmodule
