// Logisim project newCpu_M.circ as structural Verilog: 9 circuits, main circuit main
module main (
  input  rst,
  output [31:0] Instr,
  output [31:0] PC,
  output out_4,
  output [4:0] out_5,
  output [31:0] RegData,
  output out_7,
  output [31:0] ALURes,
  output [31:0] DMWD,
  output halt
);

  wire ASel, BSel, clock_1_out, clock_2_out, clock_3_out, comparator_1_eq, EXTOp, not_1_out, or_1_out, Zero;
  wire [1:0] WDSel, WRSel;
  wire [2:0] ALUOp, NPCOp;
  wire [11:0] counter_1_q;
  wire [31:0] ext_1_out_3, multiplexer_3_out, multiplexer_4_out, npc_1_npc, PC4, pc_t, RA, RD, shamt;

  Register #(.width(32)) register_1 (.D(npc_1_npc), .Q(pc_t), .clk(clock_1_out), .clr(rst));  // open: en
  Clock clock_1 (.out(clock_1_out));
  IM im_1 (.PC(pc_t), .out_2(Instr));
  NPC npc_1 (.IMM(Instr[25:0]), .RA(RA), .PC4(PC4), .NPC(npc_1_npc), .NPCOp(NPCOp), .PC(pc_t), .Zero(Zero), .rst(rst));
  Multiplexer #(.select(2), .width(5)) multiplexer_1 (
    .in0(Instr[20:16]), .in1(Instr[15:11]), .in2({5{1'b1}}), .out(out_5), .sel(WRSel));  // open: in3, en
  CU cu_1 (
    .Instr(Instr), .NPCOp(NPCOp), .DMWr(out_7), .shamt(shamt), .ALUOp(ALUOp), .ASel(ASel), .BSel(BSel),
    .EXTOp(EXTOp), .RFWr(out_4), .A3Sel(WRSel), .WDSel(WDSel));
  Multiplexer #(.select(2), .width(32)) multiplexer_2 (
    .in0(ALURes), .in1(RD), .in2(PC4), .out(RegData), .sel(WDSel));  // open: in3, en
  EXT ext_1 (.IMM(Instr[15:0]), .EXTOp(EXTOp), .out_3(ext_1_out_3));
  RF rf_1 (
    .reset(rst), .A1(Instr[25:21]), .A2(Instr[20:16]), .A3(out_5), .WD(RegData), .RD1(RA), .RD2(DMWD),
    .WE(out_4));
  Multiplexer #(.width(32)) multiplexer_3 (.in0(RA), .in1(shamt), .out(multiplexer_3_out), .sel(ASel));  // open: en
  Multiplexer #(.width(32)) multiplexer_4 (
    .in0(DMWD), .in1(ext_1_out_3), .out(multiplexer_4_out), .sel(BSel));  // open: en
  ALU alu_1 (.A(multiplexer_3_out), .B(multiplexer_4_out), .ALURes(ALURes), .ALUOp(ALUOp), .Zero(Zero));
  Clock clock_2 (.out(clock_2_out));
  Counter #(.width(12), .max('hfff), .ongoal("stay")) counter_1 (
    .D(12'h1), .Q(counter_1_q), .clk(clock_2_out), .clr(rst));  // open: load, count, carry
  DM dm_1 (.A(ALURes), .WD(DMWD), .RD(RD), .DMWr(out_7), .rst(rst));  // open: DMOp
  Comparator #(.width(12), .mode("unsigned")) comparator_1 (
    .a({12{1'b1}}), .b(counter_1_q), .eq(comparator_1_eq));  // open: gt, lt
  not not_1 (not_1_out, comparator_1_eq);
  Counter #(.width(1), .max('h1), .ongoal("stay")) counter_2 (
    .Q(halt), .clk(clock_3_out), .clr(or_1_out));  // open: load, D, count, carry
  Clock clock_3 (.out(clock_3_out));
  or or_1 (or_1_out, not_1_out, rst);
  Adder #(.width(32)) adder_1 (.a(32'h3000), .b(pc_t), .out(PC));  // open: cin, cout

  // Other names for the same wires on the sheet: DMWr = out_7; IMM26[25:0] = Instr[25:0]; RegAddr[4:0] = out_5;
  //   RFWr = out_4; WD[31:0] = DMWD

  // Notes on the sheet:
  //   IMM
  //   M1
endmodule

module NPC (
  input  [25:0] IMM,
  input  Zero,
  input  rst,
  input  [31:0] PC,
  input  [2:0] NPCOp,
  input  [31:0] RA,
  output [31:0] NPC,
  output [31:0] PC4
);

  wire [31:0] adder_2_out, bit_extender_1_out, multiplexer_1_out, shifter_1_out;

  Adder #(.width(32)) adder_1 (.a(32'h4), .b(PC), .out(PC4));  // open: cin, cout
  assign bit_extender_1_out = {{16{IMM[15]}}, IMM[15:0]};  // Bit_Extender bit_extender_1
  Shifter #(.width(32)) shifter_1 (.in(bit_extender_1_out), .\dist (5'b00010), .out(shifter_1_out));
  Adder #(.width(32)) adder_2 (.a(PC4), .b(shifter_1_out), .out(adder_2_out));  // open: cin, cout
  Multiplexer #(.width(32)) multiplexer_1 (
    .in0(PC4), .in1(adder_2_out), .out(multiplexer_1_out), .sel(Zero));  // open: en
  Multiplexer #(.select(3), .width(32)) multiplexer_2 (
    .in0(PC4), .in1(multiplexer_1_out), .in2({PC[31:28], IMM, 2'b00}), .in3(RA), .out(NPC), .sel(NPCOp));  // open: in4, in5, in6, in7, en

  // Notes on the sheet:
  //   PC+4
  //   BEQ
  //   JAL
  //   JR
endmodule

module IM (
  input  [31:0] PC,
  output [31:0] out_2
);

  ROM #(.addrWidth(12), .dataWidth(32)) rom_1 (.addr(PC[13:2]), .data(out_2));  // open: sel

  // Notes on the sheet:
  //   contents of rom_1 (hex, n*v repeats v):
  //   34000014 34010048 34020084 34030064 34040084 34050060 34060084 34070068 34080074 34090090 340a0018
  //   340b0080 340c0074 340d0080 340e0094 340f0040 34100080 3411001c 34120008 34130004 3414005c 34150090
  //   34160010 3417004c 34180064 34190028 341a0010 341b004c 341c0090 341d002c 341e006c 341f0068 01ab6022
  //   03409020 00631822 ac6e0040 0c00007a 00000000 3c1a0024 00000000 02529022 ae4e0034 0c000096 00000000
  //   02cb6820 037bd822 af600028 00000000 0c0000b6 00000000 0339c822 af27002c 018c6022 ad98004c 00842022
  //   8c890038 0c0000df 00000000 00a52822 aca70004 0339c822 af2f0000 01833020 0c00010b 00000000 00000000
  //   00000000 01ef7822 ade30080 0c000130 00000000 00a52822 8ca90054 02c61022 00421022 8c570040 0c000158
  //   00000000 00000000 00000000 00000000 0c000178 00000000 00000000 3c1b0068 02165820 0c0001a2 00000000
  //   01084022 ad120018 3c1c0060 0339c822 af260010 0c0001c4 00000000 008c3820 3c0c002c 0116a822 0c0001ed
  //   00000000 3c0a005c 0127c822 375d0054 0c00020d 00000000 01ef7822 8dfe007c 37290058 00000000 0c00022b
  //   00000000 02493022 00000000 3611001c 0c000249 00000000 3567009c 3c000050 3c130064 0c000264 00000000
  //   0c00028e 00000000 01c92020 34af0020 3c1c0060 033bd820 01d11020 01ce7022 adde004c 00508020 00a90822
  //   0339c822 8f320070 34550054 02318822 ae2f0068 01ef7822 adfc005c 3c090038 039ce022 8f880004 00000000
  //   3c130010 03c39820 01ad6822 adbc0020 00000000 03e00008 00000000 01ad6822 8dae000c 023dd822 018c6022
  //   ad930040 346a0058 03cf2022 0308d820 00421022 ac520018 36d80040 11b40012 00000000 00000000 34aa0024
  //   01a81022 02abf020 35ad0074 03b33820 00842022 8c820064 02f7b822 aefe0084 00000000 3c07001c 10e60004
  //   00000000 00000000 02529022 ae470048 03e00008 00000000 00c63022 00e73822 34e7000a 0339c822 37390001
  //   00d93020 10c70020 00000000 37640048 3c1b009c 01ef7822 8deb0044 00000022 ac1d0004 00000000 377c000c
  //   3635001c 00000000 1088fff2 00000000 00000000 105bffef 00000000 00000000 00421022 ac5d0088 039ce022
  //   8f810024 00421022 ac570084 01085820 01750822 37db007c 00000000 00000000 13a1ffe1 00000000 00000000
  //   3c1c0020 03e00008 00000000 02318822 02f7b822 36f7000a 02108022 36100001 02308820 12370023 00000000
  //   36c00048 3c0d0074 00e73822 8cfa0054 365c000c 0100d020 35a80070 016b5822 ad600050 3c010088 00c50822
  //   00000000 1059fff0 00000000 00000000 01ad6822 8db40094 02739822 8e630010 02602822 0318c022 af0a0080
  //   1199ffe6 00000000 00000000 1211ffe3 00000000 00000000 13baffe0 00000000 00000000 038bb022 00421022
  //   8c520090 03e00008 00000000 01294822 016b5822 356b000a 01ad6822 35ad0001 012d4820 112b001c 00000000
  //   0241b022 3c10000c 02318822 ae36000c 3c030094 01164022 007b7020 03bde822 afb70094 3c07000c 00000000
  //   3c030054 3c010084 00000000 00000000 00842022 8c9e0034 01c71020 00000022 8c150010 00202820 02d6b022
  //   aec10088 36be0014 1308ffe4 00000000 00000000 03e00008 00000000 03bde822 02739822 3673000a 0318c022
  //   37180001 03b8e820 13b3001f 00000000 00000000 035ad022 af4b002c 014a5022 8d520080 00000022 8c050020
  //   00000000 3c160088 014a5022 8d5a0050 117cfff1 00000000 00000000 00e73822 ace2009c 10a6ffec 00000000
  //   00000000 37cd0054 03418022 00000000 3c1c0008 029ed822 3c190064 00000000 00000000 00000022 ac1a0098
  //   00000000 03e00008 00000000 00000022 ac15009c 00000000 00712020 3c1e0018 02ddb022 03665022 3c190034
  //   100e0015 00000000 00000000 02d6b022 8ed7002c 13d70010 00000000 00000000 039ce022 8f850048 00000000
  //   00000000 00edc022 03b9d022 11d60007 00000000 00000000 00a7f022 01ad6822 adb00098 01d04822 3c150034
  //   03e00008 00000000 00421022 00a52822 34a5000a 01ce7022 35ce0001 004e1020 10450021 00000000 3c07007c
  //   0034c020 03def022 afcc0060 00000000 03def022 8fcc002c 00631822 ac6c007c 35260064 34660090 0318c022
  //   af0f001c 00c63022 acc3001c 01b25822 03bde822 afbb008c 00210822 ac360080 3c130064 3c0d0048 016c8822
  //   105dffe5 00000000 00000000 02b5a822 aeb20048 3c160040 1176ffdf 00000000 00000000 03e00008 00000000
  //   01084022 00210822 3421000a 00e73822 34e70001 01074020 11010019 00000000 0318c022 8f090074 034fd820
  //   3c030084 00069822 012d3020 341e0000 02108022 ae03009c 3564002c 01ef7822 adfb0010 0137d020 018c6022
  //   8d9b0084 3c000008 00000000 00000000 03ba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
endmodule

module PC (
  input  [31:0] IN,
  input  rst,
  output [31:0] out_3
);

  wire clock_1_out;
  wire [31:0] register_1_q, xor_1_out;

  assign xor_1_out = 32'h3000 ^ IN;  // XOR_Gate xor_1, 32 bits wide
  Clock clock_1 (.out(clock_1_out));
  Register #(.width(32)) register_1 (.D(xor_1_out), .Q(register_1_q), .clk(clock_1_out), .clr(rst));  // open: en
  assign out_3 = 32'h3000 ^ register_1_q;  // XOR_Gate xor_2, 32 bits wide
endmodule

module CU (
  input  [31:0] Instr,
  output [2:0] NPCOp,
  output [31:0] shamt,
  output RFWr,
  output [1:0] A3Sel,
  output [1:0] WDSel,
  output EXTOp,
  output [2:0] ALUOp,
  output ASel,
  output BSel,
  output DMWr
);

  wire _00_2_out, _00_out, _01_2_out, _1_2_out, _1_3_out, _1_4_out, _1_5_out, _01_out, _1_out, _10_2_out,
       _10_out, add, ADD_2_out, add_fun_out, beq, beq_2_out, jal, jal_out, jr_out, lui, lui_2_out, lw,
       not_1_out, not_2_out, not_3_out, not_4_out, not_5_out, not_6_out, not_7_out, not_8_out, not_9_out,
       not_10_out, not_11_out, not_12_out, op0_6, OR_out, ori, sub, SUB_2_out, sub_fun_out, sw;

  not not_1 (not_1_out, Instr[31]);
  not not_2 (not_2_out, Instr[30]);
  not not_3 (not_3_out, Instr[29]);
  not not_4 (not_4_out, Instr[28]);
  assign shamt = {{27{1'b0}}, Instr[10:6]};  // Bit_Extender bit_extender_1
  not not_5 (not_5_out, Instr[27]);
  not not_6 (not_6_out, Instr[26]);
  not not_7 (not_7_out, Instr[4]);
  not not_8 (not_8_out, Instr[5]);
  not not_9 (not_9_out, Instr[3]);
  not not_10 (not_10_out, Instr[2]);
  not not_11 (not_11_out, Instr[0]);
  not not_12 (not_12_out, Instr[1]);
  and add_op (op0_6, not_1_out, not_2_out, not_3_out, not_4_out, not_5_out, not_6_out);
  and add_fun (add_fun_out, Instr[5], not_7_out, not_9_out, not_10_out, not_12_out, not_11_out);
  and sub_fun (sub_fun_out, Instr[5], not_7_out, not_9_out, not_10_out, Instr[1], not_11_out);
  and u_ori (ori, not_1_out, not_2_out, Instr[29], Instr[28], not_5_out, Instr[26]);
  and u_lw (lw, Instr[31], not_2_out, not_3_out, not_4_out, Instr[26], Instr[26]);
  and u_sw (sw, Instr[31], not_2_out, Instr[29], not_4_out, Instr[27], Instr[26]);
  and u_beq (beq, not_1_out, not_2_out, not_3_out, Instr[28], not_5_out, not_6_out);
  and u_lui (lui, not_1_out, not_2_out, Instr[29], Instr[28], Instr[27], Instr[26]);
  and u_add (add, op0_6, add_fun_out);
  and u_sub (sub, op0_6, sub_fun_out);
  or ADD_2 (ADD_2_out, add, lw, sw);
  or SUB_2 (SUB_2_out, sub, beq);
  buf OR (OR_out, ori);  // OR_Gate
  buf lui_2 (lui_2_out, lui);  // OR_Gate
  buf beq_2 (beq_2_out, beq);  // OR_Gate
  buf u_jal (jal_out, jal);  // OR_Gate
  // OR_Gate jr has open pins: out=jr_out
  or _00 (_00_out, ori, lw, lui);
  or _01 (_01_out, sub, add);
  buf _10 (_10_out, jal);  // OR_Gate
  or _00_2 (_00_2_out, ori, sub, add);
  buf _01_2 (_01_2_out, lw);  // OR_Gate
  buf _10_2 (_10_2_out, jal);  // OR_Gate
  // OR_Gate _1 has open pins: out=_1_out
  or _1_2 (_1_2_out, ori, lw, sw, lui);
  buf _1_3 (_1_3_out, sw);  // OR_Gate
  or _1_4 (_1_4_out, sw, lw);
  Pull_Resistor pull_resistor_1 (.node(ALUOp));
  Priority_Encoder priority_encoder_1 (
    .in0(ADD_2_out), .in1(SUB_2_out), .in2(OR_out), .in3(lui_2_out), .out(ALUOp));  // open: in4, in5, in6, in7, en_in, gs, en_out
  Priority_Encoder priority_encoder_2 (
    .in1(beq_2_out), .in2(jal_out), .in3(jr_out), .out(NPCOp));  // open: in0, in4, in5, in6, in7, en_in, gs, en_out
  Pull_Resistor pull_resistor_2 (.node(NPCOp));
  Priority_Encoder #(.select(2)) priority_encoder_3 (
    .in0(_00_out), .in1(_01_out), .in2(_10_out), .out(A3Sel));  // open: in3, gs, en_out, en_in
  Pull_Resistor pull_resistor_3 (.node(A3Sel));
  Priority_Encoder #(.select(2)) priority_encoder_4 (
    .in0(_00_2_out), .in1(_01_2_out), .in2(_10_2_out), .out(WDSel));  // open: in3, gs, en_out, en_in
  Pull_Resistor pull_resistor_4 (.node(WDSel));
  or _1_5 (_1_5_out, add, sub, ori, lw, lui);
  Comparator #(.width(1), .mode("unsigned")) comparator_1 (.a(_1_5_out), .b(1'b1), .eq(RFWr));  // open: gt, lt
  Pull_Resistor pull_resistor_5 (.node(ASel));
  Priority_Encoder #(.select(1)) priority_encoder_5 (.in1(_1_out), .out(ASel));  // open: in0, gs, en_out, en_in
  Comparator #(.width(1), .mode("unsigned")) comparator_2 (.a(_1_2_out), .b(1'b1), .eq(BSel));  // open: gt, lt
  Comparator #(.width(1), .mode("unsigned")) comparator_3 (.a(_1_3_out), .b(1'b1), .eq(DMWr));  // open: gt, lt
  Comparator #(.width(1), .mode("unsigned")) comparator_4 (.a(_1_4_out), .b(1'b1), .eq(EXTOp));  // open: gt, lt

  // Other names for the same wires on the sheet: funct[5:0] = Instr[5:0]; opcode[5:0] = Instr[31:26];
  //   WRSel[1:0] = A3Sel

  // Notes on the sheet:
  //   01
  //   10
  //   11
  //   sll使用：选择s为A
endmodule

module RF (
  input  WE,
  input  reset,
  input  [4:0] A1,
  input  [4:0] A2,
  input  [4:0] A3,
  input  [31:0] WD,
  output [31:0] RD1,
  output [31:0] RD2
);

  wire CLK;
  wire [31:0] R0, R1, R2, R3, R4, R5, R6, R7, R8, R9, R10, R11, R12, R13, R14, R15, R16, R17, R18, R19, R20,
       R21, R22, R23, R24, R25, R26, R27, R28, R29, R30, R31, W0, W1, W2, W3, W4, W5, W6, W7, W8, W9, W10,
       W11, W12, W13, W14, W15, W16, W17, W18, W19, W20, W21, W22, W23, W24, W25, W26, W27, W28, W29, W30,
       W31;

  Clock clock_1 (.out(CLK));
  Register #(.width(32)) _0 (.D(W0), .en(WE), .Q(R0), .clk(CLK), .clr(1'b1));
  Register #(.width(32)) _4 (.D(W4), .en(WE), .Q(R4), .clk(CLK), .clr(reset));
  Register #(.width(32)) _8 (.D(W8), .en(WE), .Q(R8), .clk(CLK), .clr(reset));
  Register #(.width(32)) _12 (.D(W12), .en(WE), .Q(R12), .clk(CLK), .clr(reset));
  Demultiplexer #(.select(5), .width(32), .tristate("true")) demultiplexer_1 (
    .out1(W1), .out2(W2), .out3(W3), .out4(W4), .out5(W5), .out6(W6), .out7(W7), .out8(W8), .out9(W9),
    .out10(W10), .out11(W11), .out12(W12), .out13(W13), .out14(W14), .out15(W15), .out16(W16), .out17(W17),
    .out18(W18), .out19(W19), .out20(W20), .out21(W21), .out22(W22), .out23(W23), .out24(W24), .out25(W25),
    .out26(W26), .out27(W27), .out28(W28), .out29(W29), .out30(W30), .out31(W31), .in(WD), .sel(A3), .en(WE));  // open: out0
  Register #(.width(32)) _1 (.D(W1), .en(WE), .Q(R1), .clk(CLK), .clr(reset));
  Register #(.width(32)) _5 (.D(W5), .en(WE), .Q(R5), .clk(CLK), .clr(reset));
  Register #(.width(32)) _9 (.D(W9), .en(WE), .Q(R9), .clk(CLK), .clr(reset));
  Register #(.width(32)) _13 (.D(W13), .en(WE), .Q(R13), .clk(CLK), .clr(reset));
  Register #(.width(32)) _2 (.D(W2), .en(WE), .Q(R2), .clk(CLK), .clr(reset));
  Register #(.width(32)) _6 (.D(W6), .en(WE), .Q(R6), .clk(CLK), .clr(reset));
  Register #(.width(32)) _10 (.D(W10), .en(WE), .Q(R10), .clk(CLK), .clr(reset));
  Register #(.width(32)) _14 (.D(W14), .en(WE), .Q(R14), .clk(CLK), .clr(reset));
  Register #(.width(32)) _3 (.D(W3), .en(WE), .Q(R3), .clk(CLK), .clr(reset));
  Register #(.width(32)) _7 (.D(W7), .en(WE), .Q(R7), .clk(CLK), .clr(reset));
  Register #(.width(32)) _11 (.D(W11), .en(WE), .Q(R11), .clk(CLK), .clr(reset));
  Register #(.width(32)) _15 (.D(W15), .en(WE), .Q(R15), .clk(CLK), .clr(reset));
  Register #(.width(32)) _16 (.D(W16), .en(WE), .Q(R16), .clk(CLK), .clr(reset));
  Register #(.width(32)) _20 (.D(W20), .en(WE), .Q(R20), .clk(CLK), .clr(reset));
  Register #(.width(32)) _24 (.D(W24), .en(WE), .Q(R24), .clk(CLK), .clr(reset));
  Register #(.width(32)) _28 (.D(W28), .en(WE), .Q(R28), .clk(CLK), .clr(reset));
  Register #(.width(32)) _17 (.D(W17), .en(WE), .Q(R17), .clk(CLK), .clr(reset));
  Register #(.width(32)) _21 (.D(W21), .en(WE), .Q(R21), .clk(CLK), .clr(reset));
  Register #(.width(32)) _25 (.D(W25), .en(WE), .Q(R25), .clk(CLK), .clr(reset));
  Register #(.width(32)) _29 (.D(W29), .en(WE), .Q(R29), .clk(CLK), .clr(reset));
  Multiplexer #(.select(5), .width(32)) multiplexer_1 (
    .in0(R0), .in1(R1), .in2(R2), .in3(R3), .in4(R4), .in5(R5), .in6(R6), .in7(R7), .in8(R8), .in9(R9),
    .in10(R10), .in11(R11), .in12(R12), .in13(R13), .in14(R14), .in15(R15), .in16(R16), .in17(R17),
    .in18(R18), .in19(R19), .in20(R20), .in21(R21), .in22(R22), .in23(R23), .in24(R24), .in25(R25),
    .in26(R26), .in27(R27), .in28(R28), .in29(R29), .in30(R30), .in31(R31), .out(RD1), .sel(A1));  // open: en
  Register #(.width(32)) _18 (.D(W18), .en(WE), .Q(R18), .clk(CLK), .clr(reset));
  Register #(.width(32)) _22 (.D(W22), .en(WE), .Q(R22), .clk(CLK), .clr(reset));
  Register #(.width(32)) _26 (.D(W26), .en(WE), .Q(R26), .clk(CLK), .clr(reset));
  Register #(.width(32)) _30 (.D(W30), .en(WE), .Q(R30), .clk(CLK), .clr(reset));
  Register #(.width(32)) _19 (.D(W19), .en(WE), .Q(R19), .clk(CLK), .clr(reset));
  Register #(.width(32)) _23 (.D(W23), .en(WE), .Q(R23), .clk(CLK), .clr(reset));
  Register #(.width(32)) _27 (.D(W27), .en(WE), .Q(R27), .clk(CLK), .clr(reset));
  Register #(.width(32)) _31 (.D(W31), .en(WE), .Q(R31), .clk(CLK), .clr(reset));
  Multiplexer #(.select(5), .width(32)) multiplexer_2 (
    .in0(R0), .in1(R1), .in2(R2), .in3(R3), .in4(R4), .in5(R5), .in6(R6), .in7(R7), .in8(R8), .in9(R9),
    .in10(R10), .in11(R11), .in12(R12), .in13(R13), .in14(R14), .in15(R15), .in16(R16), .in17(R17),
    .in18(R18), .in19(R19), .in20(R20), .in21(R21), .in22(R22), .in23(R23), .in24(R24), .in25(R25),
    .in26(R26), .in27(R27), .in28(R28), .in29(R29), .in30(R30), .in31(R31), .out(RD2), .sel(A2));  // open: en

  // Other names for the same wires on the sheet: RST = reset
endmodule

module EXT (
  input  [15:0] IMM,
  input  EXTOp,
  output [31:0] out_3
);

  wire [31:0] bit_extender_1_out, bit_extender_2_out;

  assign bit_extender_1_out = {{16{1'b0}}, IMM};  // Bit_Extender bit_extender_1
  assign bit_extender_2_out = {{16{IMM[15]}}, IMM};  // Bit_Extender bit_extender_2
  Multiplexer #(.width(32)) multiplexer_1 (
    .in0(bit_extender_1_out), .in1(bit_extender_2_out), .out(out_3), .sel(EXTOp));  // open: en
endmodule

module ALU (
  input  [2:0] ALUOp,
  input  [31:0] A,
  input  [31:0] B,
  output Zero,
  output [31:0] ALURes
);

  wire [31:0] adder_1_out, OR_out, shifter_1_out, subRes;

  Adder #(.width(32)) adder_1 (.a(A), .b(B), .out(adder_1_out));  // open: cin, cout
  Subtractor #(.width(32)) subtractor_1 (.a(A), .b(B), .out(subRes));  // open: bin, bout
  assign OR_out = A | B;  // OR_Gate OR, 32 bits wide
  Shifter #(.width(32)) shifter_1 (.in(B), .\dist (5'b10000), .out(shifter_1_out));
  Comparator #(.width(32), .mode("unsigned")) comparator_1 (.a(subRes), .b({32{1'b0}}), .eq(Zero));  // open: gt, lt
  Multiplexer #(.select(3), .width(32)) multiplexer_1 (
    .in0(adder_1_out), .in1(subRes), .in2(OR_out), .in3(shifter_1_out), .out(ALURes), .sel(ALUOp));  // open: in4, in5, in6, in7, en

  // Notes on the sheet:
  //   lui
  //   isZero: if equal, 1; else 0;
endmodule

module DM (
  input  DMWr,
  input  rst,
  input  [1:0] DMOp,
  input  [31:0] A,
  input  [31:0] WD,
  output [31:0] RD
);

  wire clock_1_out, not_1_out;
  wire [31:0] write;

  Multiplexer #(.select(2), .width(32)) multiplexer_1 (.in0(WD), .out(write), .sel(2'b00));  // open: in1, in2, in3, en
  not not_1 (not_1_out, DMWr);
  Clock clock_1 (.out(clock_1_out));
  RAM #(.addrWidth(12), .dataWidth(32), .bus("separate")) ram_1 (
    .addr(A[13:2]), .din(write), .data(RD), .str(DMWr), .clk(clock_1_out), .ld(not_1_out), .clr(rst));  // open: sel

  // Other names for the same wires on the sheet: Addr[31:0] = A; Reset = rst
endmodule
