// Logisim project Logisim_4BitSort.circ as structural Verilog
module _1bit_swap (
  input  I1,
  input  I2,
  input  I3,
  output O1,
  output O2
);

  wire and_1_out, and_2_out, and_3_out, and_4_out, not_1_out, not_2_out;

  not not_1 (not_1_out, I3);
  not not_2 (not_2_out, I3);
  and and_1 (and_1_out, I1, not_1_out);
  and and_2 (and_2_out, I2, I3);
  and and_3 (and_3_out, I1, I3);
  and and_4 (and_4_out, I2, not_2_out);
  or or_1 (O1, and_1_out, and_2_out);
  or or_2 (O2, and_3_out, and_4_out);
endmodule

module _4bit_swap (
  input  [3:0] _4I1,
  input  [3:0] _4I2,
  input  _4I3,
  output [3:0] out_4,
  output [3:0] out_5
);

  _1bit_swap u_1bit_swap_1 (.I1(_4I1[0]), .I2(_4I2[0]), .I3(_4I3), .O1(out_4[0]), .O2(out_5[0]));
  _1bit_swap u_1bit_swap_2 (.I1(_4I1[1]), .I2(_4I2[1]), .I3(_4I3), .O1(out_4[1]), .O2(out_5[1]));
  _1bit_swap u_1bit_swap_3 (.I1(_4I1[2]), .I2(_4I2[2]), .I3(_4I3), .O1(out_4[2]), .O2(out_5[2]));
  _1bit_swap u_1bit_swap_4 (.I1(_4I1[3]), .I2(_4I2[3]), .I3(_4I3), .O1(out_4[3]), .O2(out_5[3]));
endmodule

module _4bit_sort (
  input  [3:0] A,
  input  [3:0] B,
  input  [3:0] C,
  input  [3:0] D,
  output [3:0] _1,
  output [3:0] _2,
  output [3:0] _3,
  output [3:0] _4
);

  wire [3:0] n1v1_sort_1_out_3, n1v1_sort_1_out_4, n1v1_sort_2_out_3, n1v1_sort_2_out_4, n1v1_sort_3_out_3,
       n1v1_sort_3_out_4, n1v1_sort_4_out_4, n1v1_sort_5_out_4;

  _1V1_SORT u_1v1_sort_1 (.in_1(A), .in_2(B), .out_3(n1v1_sort_1_out_3), .out_4(n1v1_sort_1_out_4));
  _1V1_SORT u_1v1_sort_2 (.in_1(n1v1_sort_1_out_3), .in_2(C), .out_3(n1v1_sort_2_out_3), .out_4(n1v1_sort_2_out_4));
  _1V1_SORT u_1v1_sort_3 (
    .in_1(n1v1_sort_1_out_4), .in_2(n1v1_sort_2_out_4), .out_3(n1v1_sort_3_out_3), .out_4(n1v1_sort_3_out_4));
  _1V1_SORT u_1v1_sort_4 (.in_1(n1v1_sort_2_out_3), .in_2(D), .out_3(_1), .out_4(n1v1_sort_4_out_4));
  _1V1_SORT u_1v1_sort_5 (.in_1(n1v1_sort_3_out_3), .in_2(n1v1_sort_4_out_4), .out_3(_2), .out_4(n1v1_sort_5_out_4));
  _1V1_SORT u_1v1_sort_6 (.in_1(n1v1_sort_3_out_4), .in_2(n1v1_sort_5_out_4), .out_3(_3), .out_4(_4));
endmodule

module _1V1_SORT (
  input  [3:0] in_1,
  input  [3:0] in_2,
  output [3:0] out_3,
  output [3:0] out_4
);

  wire comparator_1_gt;

  Comparator #(.width(4), .mode("unsigned")) comparator_1 (.a(in_1), .b(in_2), .gt(comparator_1_gt));  // open: eq, lt
  _4bit_swap u_4bit_swap_1 (._4I1(in_1), ._4I2(in_2), ._4I3(comparator_1_gt), .out_4(out_3), .out_5(out_4));
endmodule
