// Logisim project Logisim_fibonacci_1.circ as structural Verilog: 2 circuits, main circuit main
module main (
  input  [2:0] N,
  output [3:0] Nth
);

  wire clock_1_out, clock_2_out, comparator_1_gt, not_1_out;
  wire [2:0] adder_1_out, register_1_q;
  wire [3:0] register_2_q, register_2_q_2, \状态转移_1_out_3 , \状态转移_1_out_4 ;
  wire [7:0] multiplexer_1_out;

  Clock clock_1 (.out(clock_1_out));
  Register #(.width(3)) register_1 (
    .D(adder_1_out), .en(comparator_1_gt), .Q(register_1_q), .clk(clock_1_out));  // open: clr
  Comparator #(.width(3), .mode("unsigned")) comparator_1 (
    .a(N), .b(register_1_q), .gt(comparator_1_gt));  // open: eq, lt
  \状态转移  \u_状态转移_1  (.in_1(register_2_q_2), .in_2(register_2_q), .out_3(\状态转移_1_out_3 ), .out_4(\状态转移_1_out_4 ));
  Adder #(.width(3)) adder_1 (.a(3'b001), .b(register_1_q), .out(adder_1_out));  // open: cin, cout
  Register register_2 (
    .D({\状态转移_1_out_3 , \状态转移_1_out_4 }), .en(comparator_1_gt), .Q({register_2_q_2, register_2_q}),
    .clk(clock_2_out));  // open: clr
  Clock clock_2 (.out(clock_2_out));
  not not_1 (not_1_out, comparator_1_gt);
  Multiplexer #(.width(8)) multiplexer_1 (
    .in0({8{1'b0}}), .in1({register_2_q_2, register_2_q}), .out(multiplexer_1_out), .sel(not_1_out));  // open: en
  BitSelector #(.group(4)) bitselector_1 (.in(multiplexer_1_out), .out(Nth), .sel(1'b0));
endmodule

module \状态转移  (
  input  [3:0] in_1,
  input  [3:0] in_2,
  output [3:0] out_3,
  output [3:0] out_4
);

  wire comparator_1_eq;
  wire [3:0] bit_extender_1_out;

  // Probe on comparator_1_eq
  Comparator #(.width(4), .mode("unsigned")) comparator_1 (
    .a(in_1), .b(4'b0000), .eq(comparator_1_eq));  // open: gt, lt
  assign bit_extender_1_out = {{3{1'b0}}, comparator_1_eq};  // Bit_Extender bit_extender_1
  // Probe on out_4
  Adder #(.width(4)) adder_1 (.a(bit_extender_1_out), .b(in_1), .out(out_4));  // open: cin, cout
  Adder #(.width(4)) adder_2 (.a(out_4), .b(in_2), .out(out_3));  // open: cin, cout
endmodule
