// Logisim project Logisim_mod5.circ as structural Verilog: 1 circuit, main circuit mod5
module mod5 (
  input  In,
  output S0,
  output S1,
  output S2,
  output S3,
  output S4
);

  wire clock_1_out;
  wire [1:0] bitselector_1_out;
  wire [2:1] register_1_q;

  // Probe on bitselector_1_out
  BitSelector #(.width(3), .group(2)) bitselector_1 (.in({register_1_q, In}), .out(bitselector_1_out), .sel(1'b0));
  Clock clock_1 (.out(clock_1_out));
  Demultiplexer #(.select(2)) demultiplexer_1 (
    .out0(S1), .out1(S2), .out2(S4), .out3(S3), .in(1'b1), .sel(bitselector_1_out));  // open: en
  Register #(.width(2)) register_1 (.D(bitselector_1_out), .Q(register_1_q), .clk(clock_1_out));  // open: en, clr

  assign S0 = 1'b0;
endmodule
