// Logisim project Logisim_swap.circ as structural Verilog: 1 circuit, main circuit swap
module swap (
  input  I1,
  input  I2,
  input  S,
  output O1,
  output O2
);

  wire comparator_1_gt, xnor_1_out;

  xnor xnor_1 (xnor_1_out, I1, I2);
  Comparator #(.width(1)) comparator_1 (.a(xnor_1_out), .b(S), .gt(comparator_1_gt));  // open: eq, lt
  xor xor_1 (O1, I1, comparator_1_gt);
  xor xor_2 (O2, comparator_1_gt, I2);
endmodule
