// Logisim project special.circ as structural Verilog: 5 circuits, main circuit CRC
module CRC (
  input  [7:0] A,
  input  [3:0] B,
  output [10:0] out_3
);

  wire clock_1_out, state_module_1_crl;
  wire [10:0] B_t, bit_extender_1_out, initial_1_out_3, register_1_q, shifter_1_out, state_module_1_out_3;

  assign bit_extender_1_out = {{3{1'b0}}, A};  // Bit_Extender bit_extender_1
  assign B_t = {{7{1'b0}}, B};  // Bit_Extender bit_extender_2
  Shifter #(.width(11)) shifter_1 (.in(bit_extender_1_out), .\dist (4'b0011), .out(shifter_1_out));
  \initial  initial_1 (.\input (shifter_1_out), .statement(register_1_q), .out_3(initial_1_out_3));
  state_module state_module_1 (.B(B_t), .A(initial_1_out_3), .out_3(state_module_1_out_3), .crl(state_module_1_crl));
  Register #(.width(11)) register_1 (.D(state_module_1_out_3), .Q(register_1_q), .clk(clock_1_out));  // open: en, clr
  Clock clock_1 (.out(clock_1_out));
  output_module output_module_1 (.A(shifter_1_out), .in_2(register_1_q), .crl(state_module_1_crl), .out_4(out_3));
endmodule

module \initial  (
  input  [10:0] \input ,
  input  [10:0] statement,
  output [10:0] out_3
);

  wire clock_1_out, counter_1_q;

  Counter #(.width(1), .max('h1), .ongoal("stay")) counter_1 (
    .D(1'b1), .Q(counter_1_q), .clk(clock_1_out));  // open: load, count, carry, clr
  Clock clock_1 (.out(clock_1_out));
  Multiplexer #(.width(11)) multiplexer_1 (.in0(\input ), .in1(statement), .out(out_3), .sel(counter_1_q));  // open: en
endmodule

// state
module state_module (
  input  [10:0] B,
  input  [10:0] A,
  output [10:0] out_3,
  output crl
);

  wire undriven;
  wire [3:0] bitfinder_1_index, subtractor_1_out;
  wire [10:0] shifter_1_out, xor_1_out;

  // Probe on undriven
  BitFinder #(.width(11), .\type ("high1")) bitfinder_1 (.in(A), .index(bitfinder_1_index));  // open: found
  Subtractor #(.width(4)) subtractor_1 (.a(bitfinder_1_index), .b(4'b0011), .out(subtractor_1_out));  // open: bin, bout
  Shifter #(.width(11)) shifter_1 (.in(B), .\dist (subtractor_1_out), .out(shifter_1_out));
  assign xor_1_out = A ^ shifter_1_out;  // XOR_Gate xor_1, 11 bits wide
  Comparator #(.width(4), .mode("unsigned")) comparator_1 (
    .a(bitfinder_1_index), .b(4'b0010), .gt(crl));  // open: eq, lt
  Multiplexer #(.width(11)) multiplexer_1 (.in0(A), .in1(xor_1_out), .out(out_3), .sel(crl));  // open: en
endmodule

// output
module output_module (
  input  [10:0] A,
  input  [10:0] in_2,
  input  crl,
  output [10:0] out_4
);

  wire clock_1_out, comparator_1_gt, counter_1_q, or_2_out;
  wire [3:0] bitfinder_1_index;
  wire [10:0] and_1_out, multiplexer_1_out, or_1_out;

  assign and_1_out = 11'h7 & in_2;  // AND_Gate and_1, 11 bits wide
  assign or_1_out = A | and_1_out;  // OR_Gate or_1, 11 bits wide
  Clock clock_1 (.out(clock_1_out));
  BitFinder #(.width(11), .\type ("high1")) bitfinder_1 (.in(in_2), .index(bitfinder_1_index));  // open: found
  Multiplexer #(.width(11)) multiplexer_1 (
    .in0({11{1'b0}}), .in1(or_1_out), .out(multiplexer_1_out), .sel(counter_1_q));  // open: en
  Counter #(.width(1), .max('h1), .ongoal("stay")) counter_1 (
    .D(1'b1), .Q(counter_1_q), .clk(clock_1_out));  // open: load, count, carry, clr
  Comparator #(.width(4), .mode("unsigned")) comparator_1 (
    .a(bitfinder_1_index), .b(4'b0010), .gt(comparator_1_gt));  // open: eq, lt
  Multiplexer #(.width(11)) multiplexer_2 (
    .in0(multiplexer_1_out), .in1({11{1'b0}}), .out(out_4), .sel(or_2_out));  // open: en
  or or_2 (or_2_out, comparator_1_gt, crl);
endmodule

module Slt (
  input  fh,
  input  cmp,
  output slt
);

  wire not_1_out;

  not not_1 (not_1_out, fh);
  or or_1 (slt, not_1_out, cmp);
endmodule
