// Logisim project temp.circ as structural Verilog: 5 circuits, main circuit main
module main (
  input  [31:0] N,
  output [31:0] out_2
);

  wire clock_1_out, clock_2_out, clock_3_out, clock_4_out, clock_5_out, clock_6_out, clock_7_out,
       clock_8_out, clock_9_out, E, judge1, not_1_out;
  wire [31:0] \n电路寄存器初始化_1_out_3 , Q1, Q2, Q3, Q4, R, R1, R3, R4, register_1_q, register_2_q, register_3_q,
       register_4_q, register_5_q, register_6_q, register_7_q, register_8_q, register_9_q, \res初始化_1_out_5 ,
       \res初始化_1_out_6 , \res初始化_1_out_7 , \res初始化_1_out_8 , shifter_1_out, W1, W2, W3, W4, \矩阵乘法_2_ci1 ,
       \矩阵乘法_2_ci2 , \矩阵乘法_2_ci3 , \矩阵乘法_2_ci4 ;

  Register #(.width(32)) register_1 (.D(shifter_1_out), .en(E), .Q(register_1_q), .clk(clock_1_out));  // open: clr
  Clock clock_1 (.out(clock_1_out));
  Clock clock_2 (.out(clock_2_out));
  Clock clock_3 (.out(clock_3_out));
  Clock clock_4 (.out(clock_4_out));
  Clock clock_5 (.out(clock_5_out));
  Register #(.width(32)) register_2 (.D(W1), .en(E), .Q(register_2_q), .clk(clock_2_out));  // open: clr
  Register #(.width(32)) register_3 (.D(W2), .en(E), .Q(register_3_q), .clk(clock_3_out));  // open: clr
  Register #(.width(32)) register_4 (.D(W3), .en(E), .Q(register_4_q), .clk(clock_4_out));  // open: clr
  Register #(.width(32)) register_5 (.D(W4), .en(E), .Q(register_5_q), .clk(clock_5_out));  // open: clr
  \N电路寄存器初始化  \n电路寄存器初始化_1  (.N(N), .in_2(register_1_q), .out_3(\n电路寄存器初始化_1_out_3 ));
  BitSelector #(.width(32)) bitselector_1 (.in(\n电路寄存器初始化_1_out_3 ), .out(judge1), .sel({5{1'b0}}));
  // Probe on Q1
  \矩阵初始化  \u_矩阵初始化_1  (
    .in_1(register_2_q), .in_2(register_3_q), .in_3(register_4_q), .in_4(register_5_q), .out_5(Q1),
    .out_6(Q2), .out_7(Q3), .out_8(Q4));
  // Probe on judge1
  Shifter #(.width(32), .shift("lr")) shifter_1 (.in(\n电路寄存器初始化_1_out_3 ), .\dist (5'b00001), .out(shifter_1_out));
  Comparator #(.width(32), .mode("unsigned")) comparator_1 (.a(shifter_1_out), .b({32{1'b0}}), .gt(E));  // open: eq, lt
  // Probe on shifter_1_out
  // Probe on E
  \矩阵乘法  \u_矩阵乘法_1  (
    .AI1(Q1), .AI2(Q2), .AI3(Q3), .AI4(Q4), .BI1(Q1), .BI2(Q2), .BI3(Q3), .BI4(Q4), .CI1(W1), .CI2(W2),
    .CI3(W3), .CI4(W4));
  // Probe on W2
  Register #(.width(32)) register_6 (.D(R1), .en(E), .Q(register_6_q), .clk(clock_6_out));  // open: clr
  Clock clock_6 (.out(clock_6_out));
  Register #(.width(32)) register_7 (.D(R), .en(E), .Q(register_7_q), .clk(clock_7_out));  // open: clr
  Clock clock_7 (.out(clock_7_out));
  Register #(.width(32)) register_8 (.D(R3), .en(E), .Q(register_8_q), .clk(clock_8_out));  // open: clr
  Clock clock_8 (.out(clock_8_out));
  Register #(.width(32)) register_9 (.D(R4), .en(E), .Q(register_9_q), .clk(clock_9_out));  // open: clr
  Clock clock_9 (.out(clock_9_out));
  // Probe on \res初始化_1_out_5 
  \RES初始化  \res初始化_1  (
    .in_1(register_6_q), .in_2(register_7_q), .in_3(register_8_q), .in_4(register_9_q),
    .out_5(\res初始化_1_out_5 ), .out_6(\res初始化_1_out_6 ), .out_7(\res初始化_1_out_7 ), .out_8(\res初始化_1_out_8 ));
  \矩阵乘法  \u_矩阵乘法_2  (
    .AI1(\res初始化_1_out_5 ), .AI2(\res初始化_1_out_6 ), .AI3(\res初始化_1_out_7 ), .AI4(\res初始化_1_out_8 ), .BI1(Q1),
    .BI2(Q2), .BI3(Q3), .BI4(Q4), .CI1(\矩阵乘法_2_ci1 ), .CI2(\矩阵乘法_2_ci2 ), .CI3(\矩阵乘法_2_ci3 ),
    .CI4(\矩阵乘法_2_ci4 ));
  not not_1 (not_1_out, E);
  Multiplexer #(.width(32)) multiplexer_1 (.in0(R1), .in1(\矩阵乘法_2_ci1 ), .out(R1), .sel(judge1));  // open: en
  Multiplexer #(.width(32)) multiplexer_2 (.in0(R), .in1(\矩阵乘法_2_ci2 ), .out(R), .sel(judge1));  // open: en
  Multiplexer #(.width(32)) multiplexer_3 (.in0({32{1'b0}}), .in1(R), .out(out_2), .sel(not_1_out));  // open: en
  Multiplexer #(.width(32)) multiplexer_4 (.in0(R3), .in1(\矩阵乘法_2_ci3 ), .out(R3), .sel(judge1));  // open: en
  Multiplexer #(.width(32)) multiplexer_5 (.in0(R4), .in1(\矩阵乘法_2_ci4 ), .out(R4), .sel(judge1));  // open: en

  // Other names for the same wires on the sheet: R2[31:0] = R

  // Notes on the sheet:
  //   右移拆分快速幂
  //   计算各幂（状态转移）
  //   输出
  //   计算乘积（状态转移）
endmodule

module \矩阵乘法  (
  input  [31:0] AI1,
  input  [31:0] AI2,
  input  [31:0] AI3,
  input  [31:0] AI4,
  input  [31:0] BI1,
  input  [31:0] BI2,
  input  [31:0] BI3,
  input  [31:0] BI4,
  output [31:0] CI1,
  output [31:0] CI2,
  output [31:0] CI3,
  output [31:0] CI4
);

  wire [31:0] multiplier_1_out, multiplier_2_out, multiplier_3_out, multiplier_4_out, multiplier_5_out,
       multiplier_6_out, multiplier_7_out, multiplier_8_out;

  Multiplier #(.width(32)) multiplier_1 (.a(AI1), .b(BI1), .out(multiplier_1_out));  // open: cin, cout
  Multiplier #(.width(32)) multiplier_2 (.a(AI2), .b(BI3), .out(multiplier_2_out));  // open: cin, cout
  Multiplier #(.width(32)) multiplier_3 (.a(AI1), .b(BI2), .out(multiplier_3_out));  // open: cin, cout
  Multiplier #(.width(32)) multiplier_4 (.a(AI2), .b(BI4), .out(multiplier_4_out));  // open: cin, cout
  Multiplier #(.width(32)) multiplier_5 (.a(AI3), .b(BI1), .out(multiplier_5_out));  // open: cin, cout
  Multiplier #(.width(32)) multiplier_6 (.a(AI4), .b(BI3), .out(multiplier_6_out));  // open: cin, cout
  Multiplier #(.width(32)) multiplier_7 (.a(AI3), .b(BI2), .out(multiplier_7_out));  // open: cin, cout
  Multiplier #(.width(32)) multiplier_8 (.a(AI4), .b(BI4), .out(multiplier_8_out));  // open: cin, cout
  Adder #(.width(32)) adder_1 (.a(multiplier_1_out), .b(multiplier_2_out), .out(CI1));  // open: cin, cout
  Adder #(.width(32)) adder_2 (.a(multiplier_3_out), .b(multiplier_4_out), .out(CI2));  // open: cin, cout
  Adder #(.width(32)) adder_3 (.a(multiplier_5_out), .b(multiplier_6_out), .out(CI3));  // open: cin, cout
  Adder #(.width(32)) adder_4 (.a(multiplier_7_out), .b(multiplier_8_out), .out(CI4));  // open: cin, cout
endmodule

module \矩阵初始化  (
  input  [31:0] in_1,
  input  [31:0] in_2,
  input  [31:0] in_3,
  input  [31:0] in_4,
  output [31:0] out_5,
  output [31:0] out_6,
  output [31:0] out_7,
  output [31:0] out_8
);

  wire and_1_out, initial1, initial2, initial3, initial4;
  wire [31:0] bit_extender_1_out;

  Comparator #(.width(32), .mode("unsigned")) comparator_1 (.a({32{1'b0}}), .b(in_1), .eq(initial1));  // open: gt, lt
  Comparator #(.width(32), .mode("unsigned")) comparator_2 (.a({32{1'b0}}), .b(in_2), .eq(initial2));  // open: gt, lt
  Comparator #(.width(32), .mode("unsigned")) comparator_3 (.a({32{1'b0}}), .b(in_3), .eq(initial3));  // open: gt, lt
  Comparator #(.width(32), .mode("unsigned")) comparator_4 (.a({32{1'b0}}), .b(in_4), .eq(initial4));  // open: gt, lt
  and and_1 (and_1_out, initial1, initial2, initial3, initial4);
  assign bit_extender_1_out = {{31{1'b0}}, and_1_out};  // Bit_Extender bit_extender_1
  Adder #(.width(32)) adder_1 (.a(in_1), .b(bit_extender_1_out), .out(out_5));  // open: cin, cout
  Adder #(.width(32)) adder_2 (.a(in_2), .b(bit_extender_1_out), .out(out_6));  // open: cin, cout
  Adder #(.width(32)) adder_3 (.a(in_3), .b(bit_extender_1_out), .out(out_7));  // open: cin, cout

  assign out_8 = in_4;

  // Other names for the same wires on the sheet: _1[31:0] = in_1; _2[31:0] = in_2; _3[31:0] = in_3; _4[31:0] = in_4
endmodule

module \N电路寄存器初始化  (
  input  [31:0] N,
  input  [31:0] in_2,
  output [31:0] out_3
);

  wire comparator_1_eq;

  Comparator #(.width(32), .mode("unsigned")) comparator_1 (
    .a({32{1'b0}}), .b(in_2), .eq(comparator_1_eq));  // open: gt, lt
  Multiplexer #(.width(32)) multiplexer_1 (.in0(in_2), .in1(N), .out(out_3), .sel(comparator_1_eq));  // open: en
endmodule

module \RES初始化  (
  input  [31:0] in_1,
  input  [31:0] in_2,
  input  [31:0] in_3,
  input  [31:0] in_4,
  output [31:0] out_5,
  output [31:0] out_6,
  output [31:0] out_7,
  output [31:0] out_8
);

  wire and_1_out, initial1, initial2, initial3, initial4;
  wire [31:0] bit_extender_1_out;

  Comparator #(.width(32), .mode("unsigned")) comparator_1 (.a({32{1'b0}}), .b(in_1), .eq(initial1));  // open: gt, lt
  Comparator #(.width(32), .mode("unsigned")) comparator_2 (.a({32{1'b0}}), .b(in_2), .eq(initial2));  // open: gt, lt
  Comparator #(.width(32), .mode("unsigned")) comparator_3 (.a({32{1'b0}}), .b(in_3), .eq(initial3));  // open: gt, lt
  Comparator #(.width(32), .mode("unsigned")) comparator_4 (.a({32{1'b0}}), .b(in_4), .eq(initial4));  // open: gt, lt
  and and_1 (and_1_out, initial1, initial2, initial3, initial4);
  assign bit_extender_1_out = {{31{1'b0}}, and_1_out};  // Bit_Extender bit_extender_1
  Adder #(.width(32)) adder_1 (.a(in_1), .b(bit_extender_1_out), .out(out_5));  // open: cin, cout
  Adder #(.width(32)) adder_2 (.a(bit_extender_1_out), .b(in_4), .out(out_8));  // open: cin, cout

  assign out_6 = in_2;
  assign out_7 = in_3;

  // Other names for the same wires on the sheet: _1[31:0] = in_1; _2[31:0] = in_2; _3[31:0] = in_3; _4[31:0] = in_4
endmodule
