// Logisim project test.circ as structural Verilog: 2 circuits, main circuit grf
module grf (
  input  [4:0] A3,
  input  clk,
  input  reset,
  input  WE,
  input  [31:0] WD,
  input  [4:0] A1,
  input  [4:0] A2,
  output [31:0] RD1,
  output [31:0] RD2
);

  wire [31:0] R0, R1, R2, R3, R4, R5, R6, R7, R8, R9, R10, R11, R12, R13, R14, R15, R16, R17, R18, R19, R20,
       R21, R22, R23, R24, R25, R26, R27, R28, R29, R30, R31, W0, W1, W2, W3, W4, W5, W6, W7, W8, W9, W10,
       W11, W12, W13, W14, W15, W16, W17, W18, W19, W20, W21, W22, W23, W24, W25, W26, W27, W28, W29, W30,
       W31;

  write _1 (.OldData(R1), .NewData(WD), .A3(A3), .No(5'b00001), .WE(WE), .out_6(W1));
  write _5 (.OldData(R5), .NewData(WD), .A3(A3), .No(5'b00101), .WE(WE), .out_6(W5));
  write _9 (.OldData(R9), .NewData(WD), .A3(A3), .No(5'b01001), .WE(WE), .out_6(W9));
  write _13 (.OldData(R13), .NewData(WD), .A3(A3), .No(5'b01101), .WE(WE), .out_6(W13));
  write _17 (.OldData(R17), .NewData(WD), .A3(A3), .No(5'b10001), .WE(WE), .out_6(W17));
  write _21 (.OldData(R21), .NewData(WD), .A3(A3), .No(5'b10101), .WE(WE), .out_6(W21));
  write _25 (.OldData(R25), .NewData(WD), .A3(A3), .No(5'b11001), .WE(WE), .out_6(W25));
  write _29 (.OldData(R29), .NewData(WD), .A3(A3), .No(5'b11101), .WE(WE), .out_6(W29));
  Register #(.width(32)) _0 (.D(W0), .Q(R0), .clk(clk), .clr(1'b1));  // open: en
  Register #(.width(32)) _4 (.D(W4), .Q(R4), .clk(clk), .clr(reset));  // open: en
  Register #(.width(32)) _8 (.D(W8), .Q(R8), .clk(clk), .clr(reset));  // open: en
  Register #(.width(32)) _12 (.D(W12), .Q(R12), .clk(clk), .clr(reset));  // open: en
  write _2 (.OldData(R2), .NewData(WD), .A3(A3), .No(5'b00010), .WE(WE), .out_6(W2));
  write _6 (.OldData(R6), .NewData(WD), .A3(A3), .No(5'b00110), .WE(WE), .out_6(W6));
  write _10 (.OldData(R10), .NewData(WD), .A3(A3), .No(5'b01010), .WE(WE), .out_6(W10));
  write _14 (.OldData(R14), .NewData(WD), .A3(A3), .No(5'b01110), .WE(WE), .out_6(W14));
  write _18 (.OldData(R18), .NewData(WD), .A3(A3), .No(5'b10010), .WE(WE), .out_6(W18));
  write _22 (.OldData(R22), .NewData(WD), .A3(A3), .No(5'b10110), .WE(WE), .out_6(W22));
  write _26 (.OldData(R26), .NewData(WD), .A3(A3), .No(5'b11010), .WE(WE), .out_6(W26));
  write _30 (.OldData(R30), .NewData(WD), .A3(A3), .No(5'b11110), .WE(WE), .out_6(W30));
  Register #(.width(32)) _1_2 (.D(W1), .Q(R1), .clk(clk), .clr(reset));  // open: en
  Register #(.width(32)) _5_2 (.D(W5), .Q(R5), .clk(clk), .clr(reset));  // open: en
  Register #(.width(32)) _9_2 (.D(W9), .Q(R9), .clk(clk), .clr(reset));  // open: en
  Register #(.width(32)) _13_2 (.D(W13), .Q(R13), .clk(clk), .clr(reset));  // open: en
  write _3 (.OldData(R3), .NewData(WD), .A3(A3), .No(5'b00011), .WE(WE), .out_6(W3));
  write _7 (.OldData(R7), .NewData(WD), .A3(A3), .No(5'b00111), .WE(WE), .out_6(W7));
  write _11 (.OldData(R11), .NewData(WD), .A3(A3), .No(5'b01011), .WE(WE), .out_6(W11));
  write _15 (.OldData(R15), .NewData(WD), .A3(A3), .No(5'b01111), .WE(WE), .out_6(W15));
  write _19 (.OldData(R19), .NewData(WD), .A3(A3), .No(5'b10011), .WE(WE), .out_6(W19));
  write _23 (.OldData(R2), .NewData(WD), .A3(A3), .No(5'b10111), .WE(WE), .out_6(W23));
  write _27 (.OldData(R27), .NewData(WD), .A3(A3), .No(5'b11011), .WE(WE), .out_6(W27));
  write _31 (.OldData(R31), .NewData(WD), .A3(A3), .No({5{1'b1}}), .WE(WE), .out_6(W31));
  Register #(.width(32)) _2_2 (.D(W2), .Q(R2), .clk(clk), .clr(reset));  // open: en
  Register #(.width(32)) _6_2 (.D(W6), .Q(R6), .clk(clk), .clr(reset));  // open: en
  Register #(.width(32)) _10_2 (.D(W10), .Q(R10), .clk(clk), .clr(reset));  // open: en
  Register #(.width(32)) _14_2 (.D(W14), .Q(R14), .clk(clk), .clr(reset));  // open: en
  write _4_2 (.OldData(R4), .NewData(WD), .A3(A3), .No(5'b00100), .WE(WE), .out_6(W4));
  write _8_2 (.OldData(R8), .NewData(WD), .A3(A3), .No(5'b01000), .WE(WE), .out_6(W8));
  write _12_2 (.OldData(R12), .NewData(WD), .A3(A3), .No(5'b01100), .WE(WE), .out_6(W12));
  write _16 (.OldData(R16), .NewData(WD), .A3(A3), .No(5'b10000), .WE(WE), .out_6(W16));
  write _20 (.OldData(R20), .NewData(WD), .A3(A3), .No(5'b10100), .WE(WE), .out_6(W20));
  write _24 (.OldData(R24), .NewData(WD), .A3(A3), .No(5'b11000), .WE(WE), .out_6(W24));
  write _28 (.OldData(R28), .NewData(WD), .A3(A3), .No(5'b11100), .WE(WE), .out_6(W28));
  Register #(.width(32)) _3_2 (.D(W3), .Q(R3), .clk(clk), .clr(reset));  // open: en
  Register #(.width(32)) _7_2 (.D(W7), .Q(R7), .clk(clk), .clr(reset));  // open: en
  Register #(.width(32)) _11_2 (.D(W11), .Q(R11), .clk(clk), .clr(reset));  // open: en
  Register #(.width(32)) _15_2 (.D(W15), .Q(R15), .clk(clk), .clr(reset));  // open: en
  Register #(.width(32)) _16_2 (.D(W16), .Q(R16), .clk(clk), .clr(reset));  // open: en
  Register #(.width(32)) _20_2 (.D(W20), .Q(R20), .clk(clk), .clr(reset));  // open: en
  Register #(.width(32)) _24_2 (.D(W24), .Q(R24), .clk(clk), .clr(reset));  // open: en
  Register #(.width(32)) _28_2 (.D(W28), .Q(R28), .clk(clk), .clr(reset));  // open: en
  Register #(.width(32)) _17_2 (.D(W17), .Q(R17), .clk(clk), .clr(reset));  // open: en
  Register #(.width(32)) _21_2 (.D(W21), .Q(R21), .clk(clk), .clr(reset));  // open: en
  Register #(.width(32)) _25_2 (.D(W25), .Q(R25), .clk(clk), .clr(reset));  // open: en
  Register #(.width(32)) _29_2 (.D(W29), .Q(R29), .clk(clk), .clr(reset));  // open: en
  Multiplexer #(.select(5), .width(32)) multiplexer_1 (
    .in0(R0), .in1(R1), .in2(R2), .in3(R3), .in4(R4), .in5(R5), .in6(R6), .in7(R7), .in8(R8), .in9(R9),
    .in10(R10), .in11(R11), .in12(R12), .in13(R13), .in14(R14), .in15(R15), .in16(R16), .in17(R17),
    .in18(R18), .in19(R19), .in20(R20), .in21(R21), .in22(R22), .in23(R23), .in24(R24), .in25(R25),
    .in26(R26), .in27(R27), .in28(R28), .in29(R29), .in30(R30), .in31(R31), .out(RD1), .sel(A1));  // open: en
  Pull_Resistor pull_resistor_1 (.node(A1));
  Register #(.width(32)) _18_2 (.D(W18), .Q(R18), .clk(clk), .clr(reset));  // open: en
  Register #(.width(32)) _22_2 (.D(W22), .Q(R22), .clk(clk), .clr(reset));  // open: en
  Register #(.width(32)) _26_2 (.D(W26), .Q(R26), .clk(clk), .clr(reset));  // open: en
  Register #(.width(32)) _30_2 (.D(W30), .Q(R30), .clk(clk), .clr(reset));  // open: en
  Register #(.width(32)) _19_2 (.D(W19), .Q(R19), .clk(clk), .clr(reset));  // open: en
  Register #(.width(32)) _23_2 (.D(W23), .Q(R23), .clk(clk), .clr(reset));  // open: en
  Register #(.width(32)) _27_2 (.D(W27), .Q(R27), .clk(clk), .clr(reset));  // open: en
  Register #(.width(32)) _31_2 (.D(W31), .Q(R31), .clk(clk), .clr(reset));  // open: en
  Multiplexer #(.select(5), .width(32)) multiplexer_2 (
    .in0(R0), .in1(R1), .in2(R2), .in3(R3), .in4(R4), .in5(R5), .in6(R6), .in7(R7), .in8(R8), .in9(R9),
    .in10(R10), .in11(R11), .in12(R12), .in13(R13), .in14(R14), .in15(R15), .in16(R16), .in17(R17),
    .in18(R18), .in19(R19), .in20(R20), .in21(R21), .in22(R22), .in23(R23), .in24(R24), .in25(R25),
    .in26(R26), .in27(R27), .in28(R28), .in29(R29), .in30(R30), .in31(R31), .out(RD2), .sel(A2));  // open: en
  Pull_Resistor pull_resistor_2 (.node(A2));

  // Other names for the same wires on the sheet: RST = reset
endmodule

module write (
  input  [31:0] OldData,
  input  [31:0] NewData,
  input  [4:0] A3,
  input  [4:0] No,
  input  WE,
  output [31:0] out_6
);

  wire and_1_out, comparator_1_eq;

  Comparator #(.width(5), .mode("unsigned")) comparator_1 (.a(A3), .b(No), .eq(comparator_1_eq));  // open: gt, lt
  and and_1 (and_1_out, comparator_1_eq, WE);
  Multiplexer #(.width(32)) multiplexer_1 (.in0(OldData), .in1(NewData), .out(out_6), .sel(and_1_out));  // open: en
endmodule
