// Logisim project 递推.circ as structural Verilog: 4 circuits, main circuit main
module main (
  input  [7:0] in_1,
  output [7:0] out_2
);

  wire state_module_1_we;
  wire [7:0] multiplexer_1_out, state_module_1_1_out_2, state_module_1_2_out_2, state_module_1_newstate,
       \递推1 , \递推2 , \递推3 ;

  state_module_1 state_module_1_1 (.in_1(\递推2 ), .out_2(state_module_1_1_out_2));
  state_module_1 state_module_1_2 (.in_1(\递推1 ), .out_2(state_module_1_2_out_2));
  Register register_1 (.D(state_module_1_1_out_2), .Q(\递推3 ));  // open: en, clk, clr
  Register register_2 (.D(state_module_1_2_out_2), .Q(\递推2 ));  // open: en, clk, clr
  state_module state_module_1 (
    .\input (in_1), .statement(\递推1 ), .minus_1(\递推2 ), .minus_2(\递推3 ), .we(state_module_1_we),
    .newState(state_module_1_newstate));
  Register register_3 (.D(state_module_1_newstate), .en(state_module_1_we), .Q(\递推1 ));  // open: clk, clr
  output_module output_module_1 (.in_1(multiplexer_1_out), .\input (in_1), .out_3(out_2));
  Multiplexer #(.width(8)) multiplexer_1 (
    .in0(\递推1 ), .in1({8{1'b0}}), .out(multiplexer_1_out), .sel(state_module_1_we));  // open: en
endmodule

module output_module (
  input  [7:0] in_1,
  input  [7:0] \input ,
  output [7:0] out_3
);

  wire [2:0] comparator_2_lt;

  Comparator comparator_1 (.a(\input ), .b({8{1'b0}}), .eq(comparator_2_lt[2]));  // open: gt, lt
  Comparator comparator_2 (.a(\input ), .b(8'h4), .gt(comparator_2_lt[1]), .lt(comparator_2_lt[0]));  // open: eq
  Multiplexer #(.select(3), .width(8)) multiplexer_1 (
    .in1(8'h1), .in2(in_1), .in5(8'h5), .out(out_3), .sel(comparator_2_lt));  // open: in0, in3, in4, in6, in7, en
endmodule

module state_module (
  input  [7:0] \input ,
  input  [7:0] statement,
  input  [7:0] minus_1,
  input  [7:0] minus_2,
  output we,
  output [7:0] newState
);

  wire clock_1_out, clock_2_out, comparator_1_eq, counter_2_q;
  wire [7:0] adder_1_out, adder_2_out, counter_1_q, subtractor_1_out;

  Clock clock_1 (.out(clock_1_out));
  Subtractor subtractor_1 (.a(\input ), .b(8'h2), .out(subtractor_1_out));  // open: bin, bout
  Adder adder_1 (.a(statement), .b(minus_1), .out(adder_1_out));  // open: cin, cout
  Counter counter_1 (.D(8'h1), .Q(counter_1_q), .clk(clock_1_out));  // open: load, count, carry, clr
  Adder adder_2 (.a(adder_1_out), .b(minus_2), .out(adder_2_out));  // open: cin, cout
  Clock clock_2 (.out(clock_2_out));
  Comparator comparator_1 (.a(counter_1_q), .b(subtractor_1_out), .eq(comparator_1_eq));  // open: gt, lt
  Multiplexer #(.width(8)) multiplexer_1 (
    .in0(8'h1), .in1(adder_2_out), .out(newState), .sel(counter_2_q));  // open: en
  Counter #(.width(1), .max('h1)) counter_2 (
    .D(1'b1), .Q(counter_2_q), .clk(clock_2_out));  // open: load, count, carry, clr
  not not_1 (we, comparator_1_eq);
endmodule

module state_module_1 (
  input  [7:0] in_1,
  output [7:0] out_2
);

  wire clock_1_out, counter_1_q;

  Clock clock_1 (.out(clock_1_out));
  Counter #(.width(1), .max('h1), .ongoal("stay")) counter_1 (
    .D(1'b1), .Q(counter_1_q), .clk(clock_1_out));  // open: load, count, carry, clr
  Multiplexer #(.width(8)) multiplexer_1 (.in0(8'h1), .in1(in_1), .out(out_2), .sel(counter_1_q));  // open: en
endmodule
